// Logisim project EhBASIC Logisim 6502 Computer.circ as structural Verilog: 41 circuits, main circuit 6502 architecture with BASIC
module _6502_architecture_with_BASIC (
);

  wire and_1_out, and_4_out, button_1_out, CLK, KBD, MNR, n6502_cpu_ls6502_1_phi1, n6502_cpu_ls6502_1_r_w_,
       not_1_out, not_2_out, not_3_out, RAM, ROM, RST;
  wire [6:0] keyboard_1_data;
  wire [7:0] controlled_buffer_2_out, n6502_cpu_ls6502_1_data_output;
  wire [7:7] keyboard_1_avail;
  wire [14:0] n6502_cpu_ls6502_1_address_bus_0;

  Clock clock_1 (.out(CLK));
  Button button_1 (.out(button_1_out));
  assign RST = button_1_out ? 1'b0 : 1'bz;  // Controlled_Buffer controlled_buffer_1
  Pull_Resistor #(.pull(1)) pull_resistor_1 (.node(RST));
  not not_1 (not_1_out, n6502_cpu_ls6502_1_r_w_);
  assign controlled_buffer_2_out = not_1_out ? n6502_cpu_ls6502_1_data_output : 8'bz;  // Controlled_Buffer controlled_buffer_2
  _6502_CPU__LS6502 u_6502_cpu_ls6502_1 (
    .RST_(RST), .R_W_(n6502_cpu_ls6502_1_r_w_), .PHI0(CLK), .PHI1(n6502_cpu_ls6502_1_phi1),
    .Address_Bus_0(n6502_cpu_ls6502_1_address_bus_0[0]), .Address_Bus_1(n6502_cpu_ls6502_1_address_bus_0[1]),
    .Address_Bus_2(n6502_cpu_ls6502_1_address_bus_0[2]), .Address_Bus_3(n6502_cpu_ls6502_1_address_bus_0[3]),
    .Address_Bus_4(n6502_cpu_ls6502_1_address_bus_0[4]), .Address_Bus_5(n6502_cpu_ls6502_1_address_bus_0[5]),
    .Address_Bus_6(n6502_cpu_ls6502_1_address_bus_0[6]), .Address_Bus_7(n6502_cpu_ls6502_1_address_bus_0[7]),
    .Address_Bus_8(n6502_cpu_ls6502_1_address_bus_0[8]), .Address_Bus_9(n6502_cpu_ls6502_1_address_bus_0[9]),
    .Address_Bus_10(n6502_cpu_ls6502_1_address_bus_0[10]),
    .Address_Bus_11(n6502_cpu_ls6502_1_address_bus_0[11]),
    .Address_Bus_12(n6502_cpu_ls6502_1_address_bus_0[12]),
    .Address_Bus_13(n6502_cpu_ls6502_1_address_bus_0[13]),
    .Address_Bus_14(n6502_cpu_ls6502_1_address_bus_0[14]), .Address_Bus_15(ROM),
    .Data_input(controlled_buffer_2_out), .Data_output(n6502_cpu_ls6502_1_data_output));  // open: RDY_, NMI_, IRQ_, BE, SO_, SYNC, PHI2, VSS, N_C, VSS_2, VCC, N_C_2
  and and_1 (and_1_out, n6502_cpu_ls6502_1_address_bus_0[14], n6502_cpu_ls6502_1_address_bus_0[13], n6502_cpu_ls6502_1_address_bus_0[12]);
  nor nor_1 (RAM, ROM, and_1_out);
  and and_2 (KBD, ~ROM, and_1_out, n6502_cpu_ls6502_1_address_bus_0[0]);  // AND_Gate
  and and_3 (MNR, ~ROM, and_1_out, ~n6502_cpu_ls6502_1_address_bus_0[0]);  // AND_Gate
  TTY #(.rows(10), .cols(40)) tty_1 (
    .data(controlled_buffer_2_out[6:0]), .clk(n6502_cpu_ls6502_1_phi1), .we(and_4_out));  // open: clr
  and and_4 (and_4_out, not_2_out, MNR);
  not not_2 (not_2_out, n6502_cpu_ls6502_1_r_w_);
  Keyboard keyboard_1 (.clk(not_3_out), .avail(keyboard_1_avail[7]), .data(keyboard_1_data));  // open: re, clr
  not not_3 (not_3_out, KBD);
  assign controlled_buffer_2_out = KBD ? {keyboard_1_avail[7], keyboard_1_data} : 8'bz;  // Controlled_Buffer controlled_buffer_3
  // Probe on {keyboard_1_avail[7], keyboard_1_data}
  RAM #(.addrWidth(15), .bus("asynch")) ram_1 (
    .addr(n6502_cpu_ls6502_1_address_bus_0), .data(controlled_buffer_2_out), .sel(RAM),
    .ld(n6502_cpu_ls6502_1_r_w_));  // open: clr
  ROM #(.addrWidth(15)) rom_1 (.addr(n6502_cpu_ls6502_1_address_bus_0), .data(controlled_buffer_2_out), .sel(ROM));

  // Notes on the sheet:
  //   Clock
  //   Reset
  //   Vss
  //   RDY
  //   PHI1
  //   IRQ\
  //   N.C.
  //   NMI\
  //   SYNC
  //   Vcc
  //   AB0
  //   AB1
  //   AB2
  //   AB3
  //   AB4
  //   AB5
  //   AB6
  //   AB7
  //   AB8
  //   AB9
  //   AB10
  //   AB11
  //   RST\
  //   PHI2
  //   SO
  //   PHI0
  //   BE
  //   N.C.
  //   R/W_
  //   DB0
  //   DB1
  //   DB2
  //   DB3
  //   DB4
  //   DB5
  //   DB6
  //   DB7
  //   AB15
  //   AB14
  //   AB13
  //   AB12
  //   Vss
  //   for memory size
  //   In the startup you should first
  //   run the clock, push reset button,
  //   then type c for [C]old and 1024
  //   Bus
  //   Arbiter
  //   Monitor
  //   Address : $7000 (Mirrored)
  //   Keyboard
  //   Address : $7001 (Mirrored)
  //   RAM
  //   28 Ko ($0000-$6FFF)
  //   ROM
  //   32 Ko ($8000-$FFFF)
  //   contents of rom_1 (hex, n*v repeats v):
  //   a0 4 b9 fa a0 99 0 2 88 10 f7 a2 ff 86 88 9a a9 4c 85 a1 a2 1c bd fe a0 95 bb ca d0 f8 a2 12 bd 1b
  //   a1 95 0 ca 10 f8 a9 0 85 dc 85 df 85 b2 85 67 a9 e 85 64 a9 3 85 a0 a2 68 86 65 20 96 88 a9 2e a0 a1
  //   20 d7 88 20 40 82 86 c3 84 c4 20 c2 0 d0 1f a0 0 e6 11 d0 8 e6 12 a5 12 c9 80 f0 1d a9 55 91 11 d1
  //   11 d0 15 a 91 11 d1 11 f0 e5 d0 c 20 aa 99 a5 ac c9 98 b0 a2 20 fb 94 a5 11 a4 12 c0 1 90 97 85 85
  //   84 86 85 81 84 82 a0 0 a2 3 84 79 86 7a 98 91 79 e6 79 20 96 88 20 54 83 a5 85 38 e5 79 aa a5 86 e5
  //   7a 20 86 9a a9 3d a0 a1 20 d7 88 a9 5a a0 81 85 1 84 2 6c 1 0 20 b 81 85 7f 84 80 38 a5 a6 e5 aa a8
  //   a5 a7 e5 ab aa e8 98 f0 24 38 49 ff 65 a6 85 a6 b0 3 c6 a7 38 98 49 ff 65 a4 85 a4 b0 8 c6 a5 90 4
  //   b1 a6 91 a4 88 d0 f9 b1 a6 91 a4 c6 a7 c6 a5 ca d0 f2 60 85 78 ba e4 78 90 30 60 c4 82 90 2a d0 4 c5
  //   81 90 24 48 a2 8 98 48 b5 a3 ca 10 fa 20 e3 91 a2 0 68 95 a4 e8 e0 8 30 f8 68 a8 68 c4 82 90 6 d0 5
  //   c5 81 b0 1 60 a2 c 20 96 88 bd c7 a6 bc c8 a6 20 d7 88 20 8d 83 a9 4 a0 a8 20 d7 88 a4 88 c8 f0 3 20
  //   7b 9a a9 0 85 df 85 dc a9 15 a0 a8 20 d7 88 20 4d 82 86 c3 84 c4 20 c2 0 f0 f4 a2 ff 86 88 90 6 20
  //   82 82 4c f7 84 20 59 87 20 82 82 84 5d 20 28 83 90 44 a0 1 b1 aa 85 72 a5 7b 85 71 a5 ab 85 74 a5 aa
  //   88 f1 aa 18 65 7b 85 7b 85 73 a5 7c 69 ff 85 7c e5 ab aa 38 a5 aa e5 7b a8 b0 3 e8 c6 74 18 65 71 90
  //   3 c6 72 18 b1 71 91 73 c8 d0 f9 e6 72 e6 74 ca d0 f2 ad 21 2 f0 3f a5 85 a4 86 85 81 84 82 a5 7b 85
  //   a6 a4 7c 84 a7 65 5d 90 1 c8 85 a4 84 a5 20 c1 80 a5 7f a4 80 85 7b 84 7c a4 5d 88 b9 1d 2 91 aa 88
  //   c0 3 d0 f6 a5 12 91 aa 88 a5 11 91 aa 88 a9 ff 91 aa 20 69 83 a6 79 a5 7a a0 1 86 71 85 72 b1 71 f0
  //   18 a0 4 c8 b1 71 d0 fb 38 98 65 71 aa a0 0 91 71 98 65 72 c8 91 71 90 e0 4c 67 81 20 ef 88 20 ec 88
  //   d0 5 20 f1 88 ca 2c a2 0 20 ee a0 90 fb f0 f9 c9 7 f0 14 c9 a f0 1d c9 d f0 19 e0 0 d0 4 c9 21 90 e5
  //   c9 8 f0 da e0 47 b0 c 9d 21 2 e8 20 f1 88 d0 d4 4c 8d 88 a9 7 d0 f4 a0 ff 38 a5 c3 e9 21 aa 86 60 bd
  //   21 2 f0 51 c9 5f b0 4d c9 3c b0 e c9 30 b0 45 85 5c c9 22 f0 61 c9 2a 90 3b 24 60 70 37 86 78 84 ba
  //   a0 2e 84 73 a0 a3 84 74 a0 0 d1 73 f0 5 90 21 c8 d0 f7 98 a aa bd 4c a3 85 73 bd 4d a3 85 74 a0 ff
  //   a6 78 c8 b1 73 30 8 e8 dd 21 2 f0 f5 d0 2b a4 ba e8 c8 99 21 2 c9 0 f0 32 e9 3a f0 4 c9 49 d0 2 85
  //   60 49 57 d0 93 85 5c bd 21 2 f0 e2 c5 5c f0 de c8 99 21 2 e8 d0 f0 a6 78 b1 73 8 c8 28 10 f9 b1 73
  //   d0 be bd 21 2 10 c3 c8 c8 99 21 2 c8 c8 c8 c6 c3 60 a5 79 a6 7a a0 1 85 aa 86 ab b1 aa f0 1a a0 3 b1
  //   aa 88 c5 12 d0 4 b1 aa c5 11 b0 9 88 b1 aa aa 88 b1 aa 90 de f0 1 18 60 d0 fd a9 0 a8 91 79 c8 91 79
  //   18 a5 79 69 2 85 7b a5 7a 69 0 85 7c 18 a5 79 69 ff 85 c3 a5 7a 69 ff 85 c4 a5 85 a4 86 85 81 84 82
  //   a5 7b a4 7c 85 7d 84 7e 85 7f 84 80 20 48 85 a2 68 86 65 68 aa 68 8e fe 1 8d ff 1 a2 fd 9a a9 0 85
  //   8c 85 61 60 f0 d0 60 90 6 f0 4 c9 b7 d0 f4 20 59 87 20 28 83 20 c2 0 f0 c c9 b7 d0 93 20 bc 0 20 59
  //   87 d0 8b a5 11 5 12 d0 6 a9 ff 85 11 85 12 a0 1 84 60 20 96 88 b1 aa f0 3e 20 18 85 c8 b1 aa aa c8
  //   b1 aa c5 12 d0 4 e4 11 f0 2 b0 2a 84 97 20 86 9a a9 20 a4 97 29 7f 20 f1 88 c9 22 d0 6 a5 60 49 ff
  //   85 60 c8 b1 aa d0 e a8 b1 aa aa c8 b1 aa 86 aa 85 ab d0 b7 60 10 de 24 60 30 da a2 a5 a a 90 2 e8 18
  //   69 2f 90 1 e8 85 73 86 74 84 97 a0 0 b1 73 aa c8 b1 73 ca f0 b8 20 f1 88 c8 b1 73 48 c8 b1 73 a0 0
  //   85 74 68 85 73 b1 73 ca f0 a2 20 f1 88 c8 d0 f5 a9 80 85 61 20 b8 87 68 68 a9 10 20 3 81 20 a1 86 18
  //   98 65 c3 48 a5 c4 69 0 48 a5 88 48 a5 87 48 a9 ad 20 f5 8b 20 d4 8a 20 d1 8a a5 b0 9 7f 25 ad 85 ad
  //   a9 9b a0 84 85 71 84 72 4c 88 8b a9 fe a0 a1 20 81 98 20 c2 0 c9 b2 d0 6 20 bc 0 20 d1 8a 20 ed 98
  //   85 b0 20 7d 8b a5 98 48 a5 97 48 a9 81 48 20 18 85 a5 c3 a4 c4 a6 88 e8 f0 4 85 8b 84 8c a0 0 b1 c3
  //   f0 7 c9 3a f0 1d 4c 6 8c a0 2 b1 c3 18 f0 56 c8 b1 c3 85 87 c8 b1 c3 85 88 98 65 c3 85 c3 90 2 e6 c4
  //   20 bc 0 20 0 85 4c c0 84 f0 54 a b0 3 4c b8 87 c9 56 b0 ce a8 b9 26 a2 48 b9 25 a2 48 4c bc 0 6c 3 2
  //   c9 3 b0 1 18 d0 67 a5 c4 49 2 f0 10 49 2 a4 c3 84 8b 85 8c a5 87 a4 88 85 89 84 8a 68 68 90 7 a9 fc
  //   a0 a7 4c 4f 81 4c 5a 81 d0 f 38 a5 79 e9 1 a4 7a b0 1 88 85 8f 84 90 60 20 59 87 20 a4 86 a5 88 c5 1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
  //   then type.
  //   Note : to use the keyboard, press
  //   the rectangle with the hand cursor
  //   less than 1 minute.
  //   Note: The simulation is very slow,
  //   you should choose the max frequency
  //   (4.1KHz) in menu >Simulate>Tick
  //   Frequency. Even though, the startup
  //   in cold mode and 1024 of memory will
  //   take 5 to 6 minutes. The second
  //   reset with warm mode should take 
endmodule

// 6502
module _6502_CPU__LS6502 (
  input  PHI0,
  input  RDY_,
  input  RST_,
  input  NMI_,
  input  IRQ_,
  input  BE,
  input  SO_,
  input  [7:0] Data_input,
  input  VCC,
  input  VSS,
  input  VSS_2,
  input  N_C,
  input  N_C_2,
  output PHI1,
  output PHI2,
  output Address_Bus_0,
  output Address_Bus_1,
  output Address_Bus_2,
  output Address_Bus_3,
  output Address_Bus_4,
  output Address_Bus_5,
  output Address_Bus_6,
  output Address_Bus_7,
  output Address_Bus_8,
  output Address_Bus_9,
  output Address_Bus_10,
  output Address_Bus_11,
  output Address_Bus_12,
  output Address_Bus_13,
  output Address_Bus_14,
  output Address_Bus_15,
  output [7:0] Data_output,
  output R_W_,
  output SYNC
);

  wire ABw, Accw, ALU0, ALU1, ALU2, ALU3, and_1_out, and_3_out, and_4_out, B, B7, brch, brk, C, CF0, CF1,
       CF2, clk, D, d_ff_1_qn, F0, F1, F2, flags_status_processor_register_1_out, I, Int,
       interrupt_controller_1_mux1, interrupt_controller_1_mux2_0, interrupt_controller_1_mux2_1,
       interrupt_controller_1_mux2_2, IRw, MU0, MU1, MU2, mu_memory_unit_1_ab_lo_plus_plus, Mux0, Mux1, Mux2,
       N, not_1_out, or_1_out, or_2_out, or_3_out, OUTw, pc_lo_program_counter_low_1_cout, PC_plus_plus,
       PChw, PClw, R_W__t, rst, SO, SPw, SYNC_t, TMPw, to_B, to_C, to_N, to_V, to_Z, V, xor_1_out, Xw, Yw, Z;
  wire [2:0] mux_8_1_8_bits_2_output_2;
  wire [3:0] cu_control_unit_1_car_value, cu_control_unit_1_car_value_2,
       flags_status_processor_register_1_processor_status_register_output,
       flags_status_processor_register_1_processor_status_register_output_2, mux_8_1_8_bits_1_output,
       mux_8_1_8_bits_1_output_2, mux_8_1_8_bits_2_output;
  wire [7:0] a_accumulator_1_output, address_bus_high_1_output, address_bus_low_register_1_outputs,
       alu_arithmetic_and_logic_unit_1_sum, ir_istruction_register_1_output, mux_2_1_8_bits_1_output,
       out_data_output_register_1_output, pc_hi_program_counter_high_1_outputs,
       pc_lo_program_counter_low_1_outputs, s_stack_pointer_1_output, tmp_temporary_register_1_output,
       x_index_x_1_output, y_index_y_1_output;
  wire [15:0] mu_memory_unit_1_output;

  Pull_Resistor #(.pull(1)) pull_resistor_1 (.node(RDY_));
  Pull_Resistor #(.pull(1)) pull_resistor_2 (.node(RST_));
  Pull_Resistor #(.pull(1)) pull_resistor_3 (.node(NMI_));
  Pull_Resistor #(.pull(1)) pull_resistor_4 (.node(IRQ_));
  Pull_Resistor #(.pull(1)) pull_resistor_5 (.node(BE));
  Pull_Resistor #(.pull(1)) pull_resistor_6 (.node(SO_));
  not not_1 (not_1_out, SO_);
  Interrupt_Controller interrupt_controller_1 (
    .clk(clk), .i_flag(I), .\break (brk), .mux1(interrupt_controller_1_mux1),
    .mux2_0(interrupt_controller_1_mux2_0), .mux2_1(interrupt_controller_1_mux2_1),
    .mux2_2(interrupt_controller_1_mux2_2), .set_B_flag(to_B), .Interrupt(Int), .rst(rst), .NMI_(NMI_),
    .RST_(RST_), .IRQ_(IRQ_));
  Mux_8_1__8_bits mux_8_1_8_bits_1 (
    .Input_0({8{1'b1}}), .Input_1(8'hfa), .Input_2(8'hfb), .Input_3(8'hfc), .Input_4(8'hfd), .Input_5(8'hfe),
    .Input_6({8{1'b0}}), .Input_7({8{1'b0}}), .Output({mux_8_1_8_bits_1_output_2, mux_8_1_8_bits_1_output}),
    .Select_0(interrupt_controller_1_mux2_0), .Select_1(interrupt_controller_1_mux2_1),
    .Select_2(interrupt_controller_1_mux2_2));
  Rising_Eadge_Detector R_E_D (.\input (not_1_out), .\output (SO), .clk(clk));
  Hex_Digit_Display hex_digit_display_1 (.value(mux_8_1_8_bits_1_output_2));  // open: dp
  and and_1 (and_1_out, ~RDY_, R_W__t);  // AND_Gate
  Hex_Digit_Display hex_digit_display_2 (.value(mux_8_1_8_bits_1_output));  // open: dp
  not not_2 (PHI1, PHI0);
  D_Flip_Flop d_ff_1 (.clk(PHI0), .D(and_1_out), .Qn(d_ff_1_qn));  // open: Q, preset, en, reset
  and and_2 (clk, d_ff_1_qn, PHI1);
  Mux_2_1__8_bits mux_2_1_8_bits_1 (
    .Input_0(alu_arithmetic_and_logic_unit_1_sum),
    .Input_1({mux_8_1_8_bits_1_output_2, mux_8_1_8_bits_1_output}), .Output(mux_2_1_8_bits_1_output),
    .Select(interrupt_controller_1_mux1));
  not not_3 (PHI2, PHI1);
  IR__Istruction_Register ir_istruction_register_1 (
    .\input (alu_arithmetic_and_logic_unit_1_sum), .\output (ir_istruction_register_1_output), .clk(clk),
    .write_enable(IRw));
  xor xor_1 (xor_1_out, to_C, B7);
  and and_3 (and_3_out, xor_1_out, brch);
  or or_1 (or_1_out, and_3_out, pc_lo_program_counter_low_1_cout);
  PC_hi__Program_Counter_high pc_hi_program_counter_high_1 (
    .enable(or_1_out), .load(PChw), .CLK(clk), .reset(1'b0), .Outputs(pc_hi_program_counter_high_1_outputs),
    .Inputs(alu_arithmetic_and_logic_unit_1_sum), .dec_inc_(and_4_out));  // open: Cout
  or or_2 (or_2_out, brch, PClw);
  PC_lo__Program_Counter_Low pc_lo_program_counter_low_1 (
    .Outputs(pc_lo_program_counter_low_1_outputs), .Inputs(alu_arithmetic_and_logic_unit_1_sum),
    .Cout(pc_lo_program_counter_low_1_cout), .CLK(clk), .reset(1'b0), .inc(PC_plus_plus), .load(or_2_out));
  S__Stack_Pointer s_stack_pointer_1 (
    .\input (alu_arithmetic_and_logic_unit_1_sum), .\output (s_stack_pointer_1_output), .clk(clk),
    .write_enable(SPw));
  LED led_1 (.in(N));
  LED led_2 (.in(V));
  X__Index_X x_index_x_1 (
    .\input (alu_arithmetic_and_logic_unit_1_sum), .\output (x_index_x_1_output), .clk(clk), .write_enable(Xw));
  Y__Index_Y y_index_y_1 (
    .\input (alu_arithmetic_and_logic_unit_1_sum), .\output (y_index_y_1_output), .clk(clk), .write_enable(Yw));
  TMP__Temporary_register tmp_temporary_register_1 (
    .\input (alu_arithmetic_and_logic_unit_1_sum), .\output (tmp_temporary_register_1_output), .clk(clk),
    .write_enable(TMPw));
  A__Accumulator a_accumulator_1 (
    .\input (alu_arithmetic_and_logic_unit_1_sum), .\output (a_accumulator_1_output), .clk(clk),
    .write_enable(Accw));
  and and_4 (and_4_out, brch, B7, ~to_C);  // AND_Gate
  Flags__Status_Processor_Register flags_status_processor_register_1 (
    .processor_status_register_output({flags_status_processor_register_1_processor_status_register_output_2, flags_status_processor_register_1_processor_status_register_output}),
    .clk(clk), .N_in(to_N), .V_in(to_V), .B_in(to_B), .Z_in(to_Z), .C_in(to_C), .N_out(N), .V_out(V),
    .out(flags_status_processor_register_1_out), .B_out(B), .Z_out(Z), .C_out(C), .SO(SO),
    .Memory_input(alu_arithmetic_and_logic_unit_1_sum), .D_out(D), .I_out(I), .F2(F2), .F1(F1), .F0(F0),
    .cfg2(CF2), .cfg1(CF1), .cfg0(CF0));
  LED led_3 (.in(flags_status_processor_register_1_out));
  LED led_4 (.in(B));
  Hex_Digit_Display hex_digit_display_3 (.value(ir_istruction_register_1_output[7:4]));  // open: dp
  Hex_Digit_Display hex_digit_display_4 (.value(mux_2_1_8_bits_1_output[7:4]));  // open: dp
  Hex_Digit_Display hex_digit_display_5 (.value(pc_hi_program_counter_high_1_outputs[7:4]));  // open: dp
  Hex_Digit_Display hex_digit_display_6 (.value(pc_lo_program_counter_low_1_outputs[7:4]));  // open: dp
  Hex_Digit_Display hex_digit_display_7 (.value(s_stack_pointer_1_output[7:4]));  // open: dp
  LED led_5 (.in(D));
  LED led_6 (.in(I));
  Hex_Digit_Display hex_digit_display_8 (.value(x_index_x_1_output[7:4]));  // open: dp
  Hex_Digit_Display hex_digit_display_9 (.value(y_index_y_1_output[7:4]));  // open: dp
  Hex_Digit_Display hex_digit_display_10 (.value(tmp_temporary_register_1_output[7:4]));  // open: dp
  Hex_Digit_Display hex_digit_display_11 (.value(a_accumulator_1_output[7:4]));  // open: dp
  Hex_Digit_Display hex_digit_display_12 (.value(ir_istruction_register_1_output[3:0]));  // open: dp
  // Probe on ir_istruction_register_1_output
  Hex_Digit_Display hex_digit_display_13 (.value(mux_2_1_8_bits_1_output[3:0]));  // open: dp
  Hex_Digit_Display hex_digit_display_14 (.value(pc_hi_program_counter_high_1_outputs[3:0]));  // open: dp
  Hex_Digit_Display hex_digit_display_15 (.value(pc_lo_program_counter_low_1_outputs[3:0]));  // open: dp
  Hex_Digit_Display hex_digit_display_16 (.value(s_stack_pointer_1_output[3:0]));  // open: dp
  LED led_7 (.in(Z));
  LED led_8 (.in(C));
  Hex_Digit_Display hex_digit_display_17 (.value(x_index_x_1_output[3:0]));  // open: dp
  Hex_Digit_Display hex_digit_display_18 (.value(y_index_y_1_output[3:0]));  // open: dp
  Hex_Digit_Display hex_digit_display_19 (.value(tmp_temporary_register_1_output[3:0]));  // open: dp
  Hex_Digit_Display hex_digit_display_20 (.value(a_accumulator_1_output[3:0]));  // open: dp
  // Probe on a_accumulator_1_output
  Hex_Digit_Display hex_digit_display_21 (.value(alu_arithmetic_and_logic_unit_1_sum[7:4]));  // open: dp
  Hex_Digit_Display hex_digit_display_22 (.value(alu_arithmetic_and_logic_unit_1_sum[3:0]));  // open: dp
  Hex_Digit_Display hex_digit_display_23 (.value(flags_status_processor_register_1_processor_status_register_output_2));  // open: dp
  // Probe on x_index_x_1_output
  // Probe on y_index_y_1_output
  or or_3 (or_3_out, rst, R_W__t);
  LED u_SYNC (.in(SYNC_t));
  LED u_R_W_ (.in(or_3_out));
  // Probe on pc_hi_program_counter_high_1_outputs
  // Probe on pc_lo_program_counter_low_1_outputs
  // Probe on s_stack_pointer_1_output
  Hex_Digit_Display hex_digit_display_24 (.value(flags_status_processor_register_1_processor_status_register_output));  // open: dp
  // Probe on {flags_status_processor_register_1_processor_status_register_output_2, flags_status_processor_register_1_processor_status_register_output}
  Hex_Digit_Display hex_digit_display_25 (.value({B7, mux_8_1_8_bits_2_output_2}));  // open: dp
  ALU__Arithmetic_and_Logic_Unit alu_arithmetic_and_logic_unit_1 (
    .A(a_accumulator_1_output), .B({B7, mux_8_1_8_bits_2_output_2, mux_8_1_8_bits_2_output}), .Cin(C),
    .Sum(alu_arithmetic_and_logic_unit_1_sum), .Cout(to_C), .zero(to_Z), .negative(to_N), .overflow(to_V),
    .Functions({ALU3, ALU2, ALU1, ALU0}));
  LED u_OUTw (.in(OUTw));
  LED u_ABw (.in(ABw));
  LED u_PC_plus_plus (.in(PC_plus_plus));
  MU__Memory_Unit mu_memory_unit_1 (
    .MU2(MU2), .MU1(MU1), .MU0(MU0), .from_ALU(mux_2_1_8_bits_1_output), .CLK(clk), .carry(to_C),
    .from_PC_hi(pc_hi_program_counter_high_1_outputs), .\output (mu_memory_unit_1_output),
    .from_PC_lo(pc_lo_program_counter_low_1_outputs), .from_Stack(s_stack_pointer_1_output),
    .AB_lo_plus_plus(mu_memory_unit_1_ab_lo_plus_plus));
  Mux_8_1__8_bits mux_8_1_8_bits_2 (
    .Input_0(Data_input), .Input_1(pc_hi_program_counter_high_1_outputs),
    .Input_2(pc_lo_program_counter_low_1_outputs), .Input_3(s_stack_pointer_1_output),
    .Input_4({flags_status_processor_register_1_processor_status_register_output_2, flags_status_processor_register_1_processor_status_register_output}),
    .Input_5(x_index_x_1_output), .Input_6(y_index_y_1_output), .Input_7(tmp_temporary_register_1_output),
    .Output({B7, mux_8_1_8_bits_2_output_2, mux_8_1_8_bits_2_output}), .Select_0(Mux0), .Select_1(Mux1),
    .Select_2(Mux2));
  Hex_Digit_Display hex_digit_display_26 (.value(mux_8_1_8_bits_2_output));  // open: dp
  LED u_IRw (.in(IRw));
  LED u_PChw (.in(PChw));
  LED u_PClw (.in(PClw));
  LED u_SPw (.in(SPw));
  LED u_TMPw (.in(TMPw));
  LED u_Yw (.in(Yw));
  LED u_Xw (.in(Xw));
  LED u_Accw (.in(Accw));
  CU__Control_Unit cu_control_unit_1 (
    .CLK(clk), .OpCode(ir_istruction_register_1_output), .ALU3(ALU3), .ALU2(ALU2), .ALU1(ALU1), .ALU0(ALU0),
    .Mux2(Mux2), .Mux1(Mux1), .Mux0(Mux0), .MU1(MU1), .MU0(MU0), .brk(brk), .MU2(MU2), .CF2(CF2), .CF1(CF1),
    .CF0(CF0), .F2(F2), .F1(F1), .F0(F0), .TMPw(TMPw), .Yw(Yw), .Xw(Xw), .Accw(Accw), .IRw(IRw), .PChw(PChw),
    .PClw(PClw), .SPw(SPw), .OUTw(OUTw), .ABw(ABw), .R_W_(R_W__t), .SYNC(SYNC_t),
    .PC_plus_plus(PC_plus_plus), .Negative(N), .Ovreflow(V), .Zero(Z), .Carry(C), .brch(brch),
    .Interrupt(Int), .CAR_value({cu_control_unit_1_car_value_2, cu_control_unit_1_car_value}));
  LED u_F1 (.in(F1));
  LED u_F0 (.in(F0));
  LED u_F2 (.in(F2));
  Hex_Digit_Display hex_digit_display_27 (.value(mu_memory_unit_1_output[15:12]));  // open: dp
  Hex_Digit_Display hex_digit_display_28 (.value(mu_memory_unit_1_output[11:8]));  // open: dp
  LED u_CF2 (.in(CF2));
  LED u_CF1 (.in(CF1));
  LED u_brch (.in(brch));
  LED u_CF0 (.in(CF0));
  Hex_Digit_Display hex_digit_display_29 (.value(mu_memory_unit_1_output[7:4]));  // open: dp
  Hex_Digit_Display hex_digit_display_30 (.value(mu_memory_unit_1_output[3:0]));  // open: dp
  OUT__Data_output_register out_data_output_register_1 (
    .\input (alu_arithmetic_and_logic_unit_1_sum), .\output (out_data_output_register_1_output), .clk(clk),
    .write_enable(OUTw));
  LED u_MU2 (.in(MU2));
  LED u_MU1 (.in(MU1));
  LED u_brk (.in(brk));
  Hex_Digit_Display hex_digit_display_31 (.value(out_data_output_register_1_output[3:0]));  // open: dp
  Hex_Digit_Display hex_digit_display_32 (.value(out_data_output_register_1_output[7:4]));  // open: dp
  LED u_Mux2 (.in(Mux2));
  LED u_Mux1 (.in(Mux1));
  LED u_MU0 (.in(MU0));
  Hex_Digit_Display hex_digit_display_33 (.value(cu_control_unit_1_car_value_2));  // open: dp
  LED u_ALU3 (.in(ALU3));
  LED u_ALU2 (.in(ALU2));
  LED u_ALU1 (.in(ALU1));
  LED u_Mux0 (.in(Mux0));
  Address_Bus__high address_bus_high_1 (
    .\input (mu_memory_unit_1_output[15:8]), .\output (address_bus_high_1_output), .clk(clk),
    .write_enable(ABw));
  Address_Bus__low_register address_bus_low_register_1 (
    .Inputs(mu_memory_unit_1_output[7:0]), .Outputs(address_bus_low_register_1_outputs),
    .inc(mu_memory_unit_1_ab_lo_plus_plus), .load(ABw), .CLK(clk), .reset(1'b0));  // open: Cout
  Hex_Digit_Display hex_digit_display_34 (.value(cu_control_unit_1_car_value));  // open: dp
  // Probe on {cu_control_unit_1_car_value_2, cu_control_unit_1_car_value}
  LED u_ALU0 (.in(ALU0));
  Hex_Digit_Display hex_digit_display_35 (.value(address_bus_high_1_output[7:4]));  // open: dp
  Hex_Digit_Display hex_digit_display_36 (.value(Data_input[7:4]));  // open: dp
  Hex_Digit_Display hex_digit_display_37 (.value(address_bus_low_register_1_outputs[7:4]));  // open: dp
  Hex_Digit_Display hex_digit_display_38 (.value(address_bus_high_1_output[3:0]));  // open: dp
  Hex_Digit_Display hex_digit_display_39 (.value(Data_input[3:0]));  // open: dp
  assign Data_output = BE ? out_data_output_register_1_output : 8'bz;  // Controlled_Buffer controlled_buffer_1
  Hex_Digit_Display hex_digit_display_40 (.value(address_bus_low_register_1_outputs[3:0]));  // open: dp
  assign {Address_Bus_15, Address_Bus_14, Address_Bus_13, Address_Bus_12, Address_Bus_11, Address_Bus_10, Address_Bus_9, Address_Bus_8, Address_Bus_7, Address_Bus_6, Address_Bus_5, Address_Bus_4, Address_Bus_3, Address_Bus_2, Address_Bus_1, Address_Bus_0} = BE ? {address_bus_high_1_output, address_bus_low_register_1_outputs} : 16'bz;  // Controlled_Buffer controlled_buffer_2
  Pull_Resistor pull_resistor_7 (.node(Data_input));
  assign R_W_ = BE ? R_W__t : 1'bz;  // Controlled_Buffer controlled_buffer_3
  and and_5 (SYNC, SYNC_t, clk);

  // Notes on the sheet:
  //   001: write NZ
  //   Control Flags [CF] codes :
  //   000: write nothing
  //   010: write NZC
  //   011: write NZCV
  //   110: write NV from M7 and M6
  //   111: write all flags from stack
  //   100: set flag with code [F2,F1,F0]
  //   101: reset flag with code [F2,F1,F0]
  //   Clock
  //   Circuit
  //   ALU commands :
  //   0000: A^B
  //   0001: A&B
  //   0010: A-1
  //   0011: 0>>B>>C
  //   0100: A+B
  //   0101: A+B+C
  //   0110: A
  //   0111: A-B-(C-1)
  //   From ALU
  //   branch across 256 page
  //   boundary manager
  //   1000: B+1
  //   1001: B
  //   1010: B-1
  //   1011: C>>B>>C
  //   1100: C<<B<<0
  //   1101: C<<B<<C
  //   1110: A|B
  //   1111: A-B
  //   MU commands :
  //   001: [01,SP]
  //   010: AB-lo++
  //   011: [@hi,@lo]
  //   000: PC:[PC-hi,PC-lo]
  //   101: write ALU on @hi
  //   110: @hi++ if Carry
  //   Micro-instrucrion
  //   register (CAR) value :
  //   100: write ALU on @lo and @hi <- 0
  //   111: write ALU on @lo and write Carry
  //    @hi and @lo are 2 internal 8bits registers
endmodule

// CU
module CU__Control_Unit (
  input  CLK,
  input  Interrupt,
  input  Negative,
  input  Ovreflow,
  input  Carry,
  input  Zero,
  input  [7:0] OpCode,
  output [7:0] CAR_value,
  output OUTw,
  output ABw,
  output IRw,
  output SYNC,
  output PChw,
  output R_W_,
  output ALU3,
  output PClw,
  output PC_plus_plus,
  output CF2,
  output MU2,
  output Mux2,
  output ALU2,
  output SPw,
  output CF1,
  output MU1,
  output Mux1,
  output ALU1,
  output TMPw,
  output F2,
  output F1,
  output F0,
  output CF0,
  output brk,
  output MU0,
  output Mux0,
  output ALU0,
  output Yw,
  output Xw,
  output Accw,
  output brch
);

  wire csr_control_status_register_1_v2, not_1_out, sc_sequencer_controller_1_load_car_,
       sc_sequencer_controller_1_load_mapper_brench_,
       sc_sequencer_controller_1_operation_mapper_address_mode_mapper_, sc_sequencer_controller_1_reset;
  wire [1:0] csr_control_status_register_1_sc0;
  wire [3:0] address_mode_mapper_1_control_address, address_mode_mapper_1_control_address_2;
  wire [7:0] csr_control_status_register_1_ad0, mux_2_1_8_bits_1_output, mux_2_1_8_bits_2_output,
       operation_mapper_1_operation_address;
  wire [9:0] rom_1_data;
  wire [31:0] rom_2_data;

  BC__Branch_Controller bc_branch_controller_1 (
    .negative(Negative), .overflow(Ovreflow), .carry(Carry), .zero(Zero), .branch_2(brch), .OpCode(OpCode),
    .branch(csr_control_status_register_1_v2));
  SC__Sequencer_Controller sc_sequencer_controller_1 (
    .Interrupt(Interrupt),
    .Operation_Mapper_Address_Mode_Mapper_(sc_sequencer_controller_1_operation_mapper_address_mode_mapper_),
    .Load_Mapper_Brench_(sc_sequencer_controller_1_load_mapper_brench_),
    .Load_CAR_(sc_sequencer_controller_1_load_car_), .Command(csr_control_status_register_1_sc0),
    .reset(sc_sequencer_controller_1_reset), .SYNC(SYNC));
  Address_Mode_Mapper address_mode_mapper_1 (
    .Control_Address({address_mode_mapper_1_control_address_2, address_mode_mapper_1_control_address}),
    .OpCode(OpCode));
  Hex_Digit_Display hex_digit_display_1 (.value(address_mode_mapper_1_control_address_2));  // open: dp
  Hex_Digit_Display hex_digit_display_2 (.value(address_mode_mapper_1_control_address));  // open: dp
  Hex_Digit_Display hex_digit_display_3 (.value(CAR_value[7:4]));  // open: dp
  Hex_Digit_Display hex_digit_display_4 (.value(operation_mapper_1_operation_address[3:0]));  // open: dp
  Hex_Digit_Display hex_digit_display_5 (.value(operation_mapper_1_operation_address[7:4]));  // open: dp
  Operation_Mapper operation_mapper_1 (.OpCode(OpCode), .operation_address(operation_mapper_1_operation_address));
  Mux_2_1__8_bits mux_2_1_8_bits_1 (
    .Input_0({address_mode_mapper_1_control_address_2, address_mode_mapper_1_control_address}),
    .Input_1(operation_mapper_1_operation_address), .Output(mux_2_1_8_bits_1_output),
    .Select(sc_sequencer_controller_1_operation_mapper_address_mode_mapper_));
  Mux_2_1__8_bits mux_2_1_8_bits_2 (
    .Input_0(csr_control_status_register_1_ad0), .Input_1(mux_2_1_8_bits_1_output),
    .Output(mux_2_1_8_bits_2_output), .Select(sc_sequencer_controller_1_load_mapper_brench_));
  CAR__Control_Address_Register car_control_address_register_1 (
    .load_inc_(sc_sequencer_controller_1_load_car_), .CLK(CLK), .reset(sc_sequencer_controller_1_reset),
    .Inputs(mux_2_1_8_bits_2_output), .Outputs(CAR_value));  // open: Cout
  Hex_Digit_Display hex_digit_display_6 (.value(CAR_value[3:0]));  // open: dp
  not not_1 (not_1_out, CLK);
  ROM #(.dataWidth(10)) rom_1 (.addr(CAR_value), .data(rom_1_data));  // open: sel
  ROM #(.dataWidth(32)) rom_2 (.addr(CAR_value), .data(rom_2_data));  // open: sel
  CSR__Control_Status_Register csr_control_status_register_1 (
    .clk(not_1_out), .Write(1'b1), .V0(MU2), .MU1(MU1), .MU0(MU0), .Mux2(Mux2), .Mux1(Mux1), .Mux0(Mux0),
    .ALU3(ALU3), .ALU2(ALU2), .ALU1(ALU1), .ALU0(ALU0), .Xw(Xw), .Accw(Accw), .F2(F2), .F1(F1), .F0(F0),
    .CF2(CF2), .CF1(CF1), .CF0(CF0), .V2(csr_control_status_register_1_v2), .V1(brk), .OUTw(OUTw), .ABw(ABw),
    .IRw(IRw), .PChw(PChw), .PClw(PClw), .SPw(SPw), .TMPw(TMPw), .Yw(Yw), .signals_input(rom_2_data),
    .SC1(csr_control_status_register_1_sc0[1]), .SC0(csr_control_status_register_1_sc0[0]),
    .next_address_input(rom_1_data), .AD7(csr_control_status_register_1_ad0[7]),
    .AD6(csr_control_status_register_1_ad0[6]), .AD5(csr_control_status_register_1_ad0[5]),
    .AD4(csr_control_status_register_1_ad0[4]), .AD3(csr_control_status_register_1_ad0[3]),
    .AD2(csr_control_status_register_1_ad0[2]), .AD1(csr_control_status_register_1_ad0[1]),
    .AD0(csr_control_status_register_1_ad0[0]), .SYNC(SYNC), .R_W_(R_W_), .PC_plus_plus(PC_plus_plus));

  // Notes on the sheet:
  //   SC cmds :
  //   00 : CAR++
  //   01 : CAR <- next address
  //   11 : CAR <- Operation Mapper
  //   Address Mode
  //   10 : CAR <- Operation Address Mode Mapper
  //   Operation
  //   30      29     28
  //   27  26  25  24
  //   MP ROM
  //   (addresses+SC cmds)
  //   MP ROM
  //   (signals)
  //   23  22  21  20
  //   contents of rom_1 (hex, n*v repeats v):
  //   13*0 110 100 0 0 0 200 0 300 300 0 0 300 0 0 0 300 0 0 0 300 0 0 0 110 4*0 300 6*0 300 6*0 300 7*0
  //   300 8*0 300 7*0 4*110 0 4*110 0 110 0 110 0 110 0 110 0 110 0 110 0 110 0 110 0 6*110 0 110 110 0
  //   110 110 0 0 0 110 110 110 0 0 0 6*110 0 110 110 110 0 0 110 0 0 110 4*0 5*110 0 0 110 0 110 0 110 0
  //   110 8*0 110 6*0 110 8*0 110
  //   contents of rom_2 (hex, n*v repeats v):
  //   2c000499 40003a 2c0000a9 40003a 2c0000c9 40003a 20000200 20000280 24000580 20800409 20000200
  //   20000280 24014180 21000009 30000000 0 64000000 32000009 20000000 0 20000000 34000000 34000000
  //   20000209 24000180 34200006 20040009 20000254 240401f9 34200006 20040009 20000264 240401f9 34200006
  //   20040029 20000804 20040079 34000000 20000209 34000000 20000289 24000180 34200006 20040009 200003d4
  //   34040079 20000289 20000300 24000180 34200006 20040009 200003e4 34040079 20000289 20000300 24000180
  //   34200006 20040009 20000254 240401f9 20000209 20000100 20000289 24000180 34200006 20000209 24000180
  //   20040009 200003e4 20040179 20000289 20000300 24000180 7*0 2004100e 20041001 20041000 20043005
  //   28000006 0 20041009 2000200f 20043007 2800200c 0 20200006 2004207c 2800200d 0 20200006 2004207d
  //   28002003 0 20200006 20042073 2800200b 0 20200006 2004207b 28000059 0 20041059 20400059 20081009
  //   20081006 20081039 2800100a 0 2008105a 28001008 0 20000000 20200006 20040059 2000200f 20040079
  //   20081058 2001c000 20200006 20040069 2000200f 20040079 20101068 2001d000 20101009 20101006 20035000
  //   28000069 0 2010106a 20041069 20400038 24000080 20041009 20800009 20000100 21000009 34000000 20200009
  //   24000000 20800079 21000009 20015000 20014000 20005000 20004000 20400038 24000080 20007009 2c000086
  //   40003a 2c0000c9 40003a 20001001 20006009 34000000 20200009 2c000099 40003a 2c0000a9 40003a 24000000
  //   20800079 21000009 20400038 24000080 20800009 20400038 24000080 21000009 30000000 20400038 24000080
  //   20007009 20400038 24000080 20800009 20400038 24000080 21000009
  //   19  18      17  16
  //   15     14   13  12
  //   Sequencer
  //   11      10      9    8
  //   7        6    5    4
  //   3    2     1    0
  //   next address
endmodule

// MU
module MU__Memory_Unit (
  input  CLK,
  input  MU2,
  input  MU1,
  input  MU0,
  input  [7:0] from_PC_hi,
  input  [7:0] from_ALU,
  input  [7:0] from_PC_lo,
  input  [7:0] from_Stack,
  input  carry,
  output [15:0] \output ,
  output AB_lo_plus_plus
);

  wire and_1_out, and_2_out, and_3_out, and_4_out, and_5_out, d_ff_1_q, or_1_out;
  wire [7:0] address_hi_adress_high_1_outputs, address_lo_adress_low_1_output;

  and and_1 (and_1_out, and_3_out, d_ff_1_q);
  or or_1 (or_1_out, and_4_out, and_5_out);
  Address_lo__Adress_low address_lo_adress_low_1 (
    .\input (from_ALU), .\output (address_lo_adress_low_1_output), .clk(CLK), .write_enable(or_1_out));
  Address_hi__Adress_high address_hi_adress_high_1 (
    .inc(and_1_out), .load(and_2_out), .CLK(CLK), .reset(and_4_out),
    .Outputs(address_hi_adress_high_1_outputs), .Inputs(from_ALU));  // open: Cout
  D_Flip_Flop #(.trigger("high")) d_ff_1 (
    .clk(CLK), .D(carry), .Q(d_ff_1_q), .en(and_5_out));  // open: Qn, preset, reset
  Hex_Digit_Display hex_digit_display_1 (.value(address_hi_adress_high_1_outputs[7:4]));  // open: dp
  Hex_Digit_Display hex_digit_display_2 (.value(address_lo_adress_low_1_output[7:4]));  // open: dp
  and and_2 (and_2_out, MU2, ~MU1, MU0);  // AND_Gate
  and and_3 (and_3_out, MU2, MU1, ~MU0);  // AND_Gate
  Hex_Digit_Display hex_digit_display_3 (.value(address_hi_adress_high_1_outputs[3:0]));  // open: dp
  and and_4 (and_4_out, MU2, ~MU1, ~MU0);  // AND_Gate
  Hex_Digit_Display hex_digit_display_4 (.value(address_lo_adress_low_1_output[3:0]));  // open: dp
  and and_5 (and_5_out, MU2, MU1, MU0);
  Mux_8_1__8_bits mux_8_1_8_bits_1 (
    .Input_0(from_PC_hi), .Input_1(8'h1), .Input_2({8{1'b0}}), .Input_3(address_hi_adress_high_1_outputs),
    .Input_4({8{1'b0}}), .Input_5({8{1'b0}}), .Input_6({8{1'b0}}), .Input_7({8{1'b0}}),
    .Output(\output [15:8]), .Select_0(MU0), .Select_1(MU1), .Select_2(MU2));
  Mux_8_1__8_bits mux_8_1_8_bits_2 (
    .Input_0(from_PC_lo), .Input_1(from_Stack), .Input_2({8{1'b0}}),
    .Input_3(address_lo_adress_low_1_output), .Input_4({8{1'b0}}), .Input_5({8{1'b0}}), .Input_6({8{1'b0}}),
    .Input_7({8{1'b0}}), .Output(\output [7:0]), .Select_0(MU0), .Select_1(MU1), .Select_2(MU2));
  and and_6 (AB_lo_plus_plus, ~MU2, MU1, ~MU0);  // AND_Gate
endmodule

// ALU
module ALU__Arithmetic_and_Logic_Unit (
  input  Cin,
  input  [3:0] Functions,
  input  [7:0] A,
  input  [7:0] B,
  output [7:0] Sum,
  output zero,
  output negative,
  output overflow,
  output Cout
);

  wire adder_8_bits_1_cout, and_1_out, and_4_out, and_5_out, and_6_out, and_7_out, nor_1_out, or_2_out,
       shift_1_bit_right_8_bits_1_cout;
  wire [7:0] adder_8_bits_1_s, and_2_out, and_3_out, mux_2_1_8_bits_1_output, mux_2_1_8_bits_2_output,
       or_1_out, shift_1_bit_right_8_bits_1_output, xor_1_out, xor_2_out;

  and and_1 (and_1_out, Functions[3], ~and_7_out);  // AND_Gate
  Mux_2_1__8_bits mux_2_1_8_bits_1 (.Input_0(A), .Input_1(B), .Output(mux_2_1_8_bits_1_output), .Select(and_1_out));
  assign xor_1_out = mux_2_1_8_bits_1_output ^ B;  // XOR_Gate xor_1, 8 bits wide
  assign and_2_out = mux_2_1_8_bits_1_output & B;  // AND_Gate and_2, 8 bits wide
  assign or_1_out = mux_2_1_8_bits_1_output | A;  // OR_Gate or_1, 8 bits wide
  assign and_3_out = {8{Functions[2]}} & B;  // AND_Gate and_3, 8 bits wide
  assign xor_2_out = {8{Functions[1]}} ^ and_3_out;  // XOR_Gate xor_2, 8 bits wide
  and and_4 (and_4_out, Functions[3], or_2_out);
  Shift_1_bit_right__8_bits shift_1_bit_right_8_bits_1 (
    .Input(B), .Output(shift_1_bit_right_8_bits_1_output), .Cout(shift_1_bit_right_8_bits_1_cout),
    .Cin(and_4_out));
  and and_5 (and_5_out, Cin, Functions[0]);
  or or_2 (or_2_out, and_5_out, and_7_out, nor_1_out);
  Adder__8_bits adder_8_bits_1 (
    .A(mux_2_1_8_bits_1_output), .B(xor_2_out), .S(adder_8_bits_1_s), .Cin(or_2_out),
    .Cout(adder_8_bits_1_cout), .overflow(overflow));
  Mux_2_1__1_bit mux_2_1_1_bit_1 (
    .Input_0(adder_8_bits_1_cout), .Input_1(shift_1_bit_right_8_bits_1_cout), .Output(Cout),
    .Select(and_6_out));
  Mux_2_1__8_bits mux_2_1_8_bits_2 (
    .Input_0(xor_1_out), .Input_1(adder_8_bits_1_s), .Output(mux_2_1_8_bits_2_output), .Select(Functions[3]));
  and and_6 (and_6_out, ~Functions[2], Functions[1], Functions[0]);  // AND_Gate
  and and_7 (and_7_out, Functions[3], Functions[2], Functions[1], Functions[0]);
  nor nor_1 (nor_1_out, Functions[2], Functions[1]);
  Mux_8_1__8_bits mux_8_1_8_bits_1 (
    .Input_0(mux_2_1_8_bits_2_output), .Input_1(and_2_out), .Input_2(adder_8_bits_1_s),
    .Input_3(shift_1_bit_right_8_bits_1_output), .Input_4(adder_8_bits_1_s), .Input_5(adder_8_bits_1_s),
    .Input_6(or_1_out), .Input_7(adder_8_bits_1_s), .Output({negative, Sum[6:0]}), .Select_0(Functions[0]),
    .Select_1(Functions[1]), .Select_2(Functions[2]));
  nor nor_2 (zero, Sum[0], Sum[1], Sum[2], Sum[3], Sum[4], Sum[5], Sum[6], negative);

  assign Sum[7] = negative;
endmodule

// Interrupt
module Interrupt_Controller (
  input  clk,
  input  \break ,
  input  i_flag,
  input  RST_,
  input  NMI_,
  input  IRQ_,
  output mux1,
  output Interrupt,
  output rst,
  output set_B_flag,
  output mux2_2,
  output mux2_1,
  output mux2_0
);

  wire and_1_out, and_2_out, and_3_out, and_4_out, and_5_out, and_6_out, and_7_out, and_8_out, and_9_out,
       and_10_out, and_11_out, and_13_out, and_14_out, d_ff_1_q, d_ff_2_q, d_ff_3_q, d_ff_3_qn, d_ff_4_q,
       d_ff_5_q, d_ff_5_qn, nor_1_out, nor_2_out, nor_3_out, not_1_out, not_2_out, or_2_out, or_4_out,
       serial_to_parallel_shifter_8_bits_1_output_0, serial_to_parallel_shifter_8_bits_1_output_1,
       serial_to_parallel_shifter_8_bits_1_output_2, serial_to_parallel_shifter_8_bits_1_output_3,
       serial_to_parallel_shifter_8_bits_1_output_4, serial_to_parallel_shifter_8_bits_1_output_6,
       serial_to_parallel_shifter_8_bits_1_output_7;

  D_Flip_Flop d_ff_1 (.Q(d_ff_1_q), .preset(d_ff_2_q), .reset(and_7_out));  // open: clk, D, Qn, en
  nor nor_1 (nor_1_out, RST_, d_ff_1_q);
  nor nor_2 (nor_2_out, NMI_, d_ff_1_q);
  nor nor_3 (nor_3_out, IRQ_, i_flag, d_ff_1_q);
  and and_1 (and_1_out, d_ff_3_q, and_7_out);
  and and_2 (and_2_out, and_4_out, and_7_out);
  and and_3 (and_3_out, or_2_out, and_7_out);
  D_Flip_Flop d_ff_2 (.clk(clk), .D(\break ), .Q(d_ff_2_q));  // open: Qn, preset, en, reset
  D_Flip_Flop d_ff_3 (
    .clk(clk), .D(nor_1_out), .Q(d_ff_3_q), .Qn(d_ff_3_qn), .en(d_ff_3_qn), .reset(and_1_out));  // open: preset
  D_Flip_Flop d_ff_4 (.clk(nor_2_out), .D(1'b1), .Q(d_ff_4_q), .reset(and_2_out));  // open: Qn, preset, en
  D_Flip_Flop d_ff_5 (
    .clk(clk), .D(nor_3_out), .Q(d_ff_5_q), .Qn(d_ff_5_qn), .en(d_ff_5_qn), .reset(and_3_out));  // open: preset
  or or_1 (Interrupt, d_ff_5_q, d_ff_4_q, d_ff_3_q);
  and and_4 (and_4_out, ~d_ff_3_q, d_ff_4_q);  // AND_Gate
  and and_5 (and_5_out, ~d_ff_3_q, ~d_ff_4_q, d_ff_5_q);  // AND_Gate
  not not_1 (not_1_out, Interrupt);
  or or_2 (or_2_out, not_1_out, and_5_out);
  not not_2 (not_2_out, clk);
  and and_6 (and_6_out, serial_to_parallel_shifter_8_bits_1_output_0, serial_to_parallel_shifter_8_bits_1_output_1);
  Serial_to_Parallel_Shifter__8_bits serial_to_parallel_shifter_8_bits_1 (
    .Input(d_ff_2_q), .clk(not_2_out), .reset(and_7_out),
    .Output_0(serial_to_parallel_shifter_8_bits_1_output_0),
    .Output_1(serial_to_parallel_shifter_8_bits_1_output_1),
    .Output_2(serial_to_parallel_shifter_8_bits_1_output_2),
    .Output_3(serial_to_parallel_shifter_8_bits_1_output_3),
    .Output_4(serial_to_parallel_shifter_8_bits_1_output_4), .Output_5(mux2_0),
    .Output_6(serial_to_parallel_shifter_8_bits_1_output_6),
    .Output_7(serial_to_parallel_shifter_8_bits_1_output_7));
  and and_7 (and_7_out, serial_to_parallel_shifter_8_bits_1_output_3, serial_to_parallel_shifter_8_bits_1_output_4);
  and and_8 (and_8_out, or_2_out, mux2_0);
  and and_9 (and_9_out, d_ff_3_q, and_6_out);
  or or_3 (mux2_2, and_8_out, and_9_out);
  and and_10 (and_10_out, serial_to_parallel_shifter_8_bits_1_output_0, serial_to_parallel_shifter_8_bits_1_output_1);
  and and_11 (and_11_out, serial_to_parallel_shifter_8_bits_1_output_1, serial_to_parallel_shifter_8_bits_1_output_2);
  or or_4 (or_4_out, serial_to_parallel_shifter_8_bits_1_output_0, serial_to_parallel_shifter_8_bits_1_output_2, serial_to_parallel_shifter_8_bits_1_output_4);
  and and_12 (set_B_flag, serial_to_parallel_shifter_8_bits_1_output_3, not_1_out);
  and and_13 (and_13_out, and_4_out, and_6_out);
  and and_14 (and_14_out, d_ff_3_q, mux2_0);
  or or_5 (mux2_1, and_14_out, and_13_out);
  or or_6 (mux1, and_10_out, mux2_0, serial_to_parallel_shifter_8_bits_1_output_6, and_11_out);
  and and_15 (rst, d_ff_3_q, or_4_out);

  // Notes on the sheet:
  //   locking mechanism
  //   finishing signal
  //   Notes :
  //   priority circuit
  //   - All interruptions do the same BRK micro-instructions sequence
  //   Except for interruption vector, which is controlled by mux outputs
  //   - The Shifter is used as a tracker for BRK micro-instructions
  //   - Micro-instructions 1 and 9 codes are the same, but they don't conflict
  //   - The first micro-instruction in BRK is 0 (not 1, 1 is the second)
  //   - rst output prevent writing PC and P on the stack for RST interrupt
  //   rst
  //   nmi
  //   irq or brk
  //   Shifter output codes :
  //   1000 0000 : micro-instruction 1 of BRK instruction
  //   0100 0000 : micro-instruction 2 of BRK instruction
  //   0010 0000 : micro-instruction 3 of BRK instruction
  //   0001 0000 : micro-instruction 4 of BRK instruction
  //   0000 1000 : micro-instruction 5 of BRK instruction
  //   0000 0100 : micro-instruction 6 of BRK instruction
  //   0000 0010 : micro-instruction 7 of BRK instruction
  //   0000 0001: micro-instruction 8 of BRK instruction
  //   1000 0000 : micro-instruction 9 of BRK instruction
  //   1100 0000 : micro-instruction A of BRK instruction
  //   0110 0000 : micro-instruction B of BRK instruction
  //   0011 0000 : micro-instruction C of BRK instruction
  //   0001 1000 : micro-instruction D of BRK instruction
endmodule

// IR
module IR__Istruction_Register (
  input  clk,
  input  write_enable,
  input  [7:0] \input ,
  output [7:0] \output 
);

  D_Flip_Flop d_ff_1 (.clk(clk), .D(\input [0]), .Q(\output [0]), .en(write_enable));  // open: Qn, preset, reset
  D_Flip_Flop d_ff_2 (.clk(clk), .D(\input [1]), .Q(\output [1]), .en(write_enable));  // open: Qn, preset, reset
  D_Flip_Flop d_ff_3 (.clk(clk), .D(\input [2]), .Q(\output [2]), .en(write_enable));  // open: Qn, preset, reset
  D_Flip_Flop d_ff_4 (.clk(clk), .D(\input [3]), .Q(\output [3]), .en(write_enable));  // open: Qn, preset, reset
  D_Flip_Flop d_ff_5 (.clk(clk), .D(\input [4]), .Q(\output [4]), .en(write_enable));  // open: Qn, preset, reset
  D_Flip_Flop d_ff_6 (.clk(clk), .D(\input [5]), .Q(\output [5]), .en(write_enable));  // open: Qn, preset, reset
  D_Flip_Flop d_ff_7 (.clk(clk), .D(\input [6]), .Q(\output [6]), .en(write_enable));  // open: Qn, preset, reset
  D_Flip_Flop d_ff_8 (.clk(clk), .D(\input [7]), .Q(\output [7]), .en(write_enable));  // open: Qn, preset, reset

  // Notes on the sheet:
  //   8 bits register
endmodule

// PC-hi
module PC_hi__Program_Counter_high (
  input  enable,
  input  load,
  input  CLK,
  input  reset,
  input  dec_inc_,
  input  [7:0] Inputs,
  output [7:0] Outputs,
  output Cout
);

  wire and_1_out, and_2_out, and_3_out, and_4_out, and_5_out, and_6_out, and_7_out, j_k_ff_1_qn, j_k_ff_2_qn,
       j_k_ff_3_qn, j_k_ff_4_qn, j_k_ff_5_qn, j_k_ff_6_qn, j_k_ff_7_qn, j_k_ff_8_qn, mux_2_1_1_bit_1_output,
       mux_2_1_1_bit_2_output, mux_2_1_1_bit_3_output, mux_2_1_1_bit_4_output, mux_2_1_1_bit_5_output,
       mux_2_1_1_bit_6_output, mux_2_1_1_bit_7_output, mux_2_1_1_bit_8_output, mux_2_1_1_bit_9_output,
       mux_2_1_1_bit_10_output, mux_2_1_1_bit_11_output, mux_2_1_1_bit_12_output, mux_2_1_1_bit_13_output,
       mux_2_1_1_bit_14_output, mux_2_1_1_bit_15_output, mux_2_1_1_bit_16_output, xor_1_out, xor_2_out,
       xor_3_out, xor_4_out, xor_5_out, xor_6_out, xor_7_out, xor_8_out;

  Mux_2_1__1_bit mux_2_1_1_bit_1 (
    .Input_0(enable), .Input_1(Inputs[0]), .Output(mux_2_1_1_bit_1_output), .Select(load));
  Mux_2_1__1_bit mux_2_1_1_bit_2 (
    .Input_0(and_1_out), .Input_1(Inputs[1]), .Output(mux_2_1_1_bit_2_output), .Select(load));
  Mux_2_1__1_bit mux_2_1_1_bit_3 (
    .Input_0(and_2_out), .Input_1(Inputs[2]), .Output(mux_2_1_1_bit_3_output), .Select(load));
  Mux_2_1__1_bit mux_2_1_1_bit_4 (
    .Input_0(and_3_out), .Input_1(Inputs[3]), .Output(mux_2_1_1_bit_4_output), .Select(load));
  Mux_2_1__1_bit mux_2_1_1_bit_5 (
    .Input_0(and_4_out), .Input_1(Inputs[4]), .Output(mux_2_1_1_bit_5_output), .Select(load));
  Mux_2_1__1_bit mux_2_1_1_bit_6 (
    .Input_0(and_5_out), .Input_1(Inputs[5]), .Output(mux_2_1_1_bit_6_output), .Select(load));
  Mux_2_1__1_bit mux_2_1_1_bit_7 (
    .Input_0(and_6_out), .Input_1(Inputs[6]), .Output(mux_2_1_1_bit_7_output), .Select(load));
  Mux_2_1__1_bit mux_2_1_1_bit_8 (
    .Input_0(and_7_out), .Input_1(Inputs[7]), .Output(mux_2_1_1_bit_8_output), .Select(load));
  xor xor_1 (xor_1_out, load, mux_2_1_1_bit_1_output);
  xor xor_2 (xor_2_out, load, mux_2_1_1_bit_2_output);
  xor xor_3 (xor_3_out, load, mux_2_1_1_bit_3_output);
  xor xor_4 (xor_4_out, load, mux_2_1_1_bit_4_output);
  xor xor_5 (xor_5_out, load, mux_2_1_1_bit_5_output);
  xor xor_6 (xor_6_out, load, mux_2_1_1_bit_6_output);
  xor xor_7 (xor_7_out, load, mux_2_1_1_bit_7_output);
  xor xor_8 (xor_8_out, load, mux_2_1_1_bit_8_output);
  J_K_Flip_Flop j_k_ff_1 (
    .J(mux_2_1_1_bit_1_output), .clk(CLK), .K(xor_1_out), .Q(Outputs[0]), .Qn(j_k_ff_1_qn), .reset(reset));  // open: preset, en
  J_K_Flip_Flop j_k_ff_2 (
    .J(mux_2_1_1_bit_2_output), .clk(CLK), .K(xor_2_out), .Q(Outputs[1]), .Qn(j_k_ff_2_qn), .reset(reset));  // open: preset, en
  J_K_Flip_Flop j_k_ff_3 (
    .J(mux_2_1_1_bit_3_output), .clk(CLK), .K(xor_3_out), .Q(Outputs[2]), .Qn(j_k_ff_3_qn), .reset(reset));  // open: preset, en
  J_K_Flip_Flop j_k_ff_4 (
    .J(mux_2_1_1_bit_4_output), .clk(CLK), .K(xor_4_out), .Q(Outputs[3]), .Qn(j_k_ff_4_qn), .reset(reset));  // open: preset, en
  J_K_Flip_Flop j_k_ff_5 (
    .J(mux_2_1_1_bit_5_output), .clk(CLK), .K(xor_5_out), .Q(Outputs[4]), .Qn(j_k_ff_5_qn), .reset(reset));  // open: preset, en
  J_K_Flip_Flop j_k_ff_6 (
    .J(mux_2_1_1_bit_6_output), .clk(CLK), .K(xor_6_out), .Q(Outputs[5]), .Qn(j_k_ff_6_qn), .reset(reset));  // open: preset, en
  J_K_Flip_Flop j_k_ff_7 (
    .J(mux_2_1_1_bit_7_output), .clk(CLK), .K(xor_7_out), .Q(Outputs[6]), .Qn(j_k_ff_7_qn), .reset(reset));  // open: preset, en
  J_K_Flip_Flop j_k_ff_8 (
    .J(mux_2_1_1_bit_8_output), .clk(CLK), .K(xor_8_out), .Q(Outputs[7]), .Qn(j_k_ff_8_qn), .reset(reset));  // open: preset, en
  Mux_2_1__1_bit mux_2_1_1_bit_9 (
    .Input_0(Outputs[0]), .Input_1(j_k_ff_1_qn), .Output(mux_2_1_1_bit_9_output), .Select(dec_inc_));
  Mux_2_1__1_bit mux_2_1_1_bit_10 (
    .Input_0(Outputs[1]), .Input_1(j_k_ff_2_qn), .Output(mux_2_1_1_bit_10_output), .Select(dec_inc_));
  Mux_2_1__1_bit mux_2_1_1_bit_11 (
    .Input_0(Outputs[2]), .Input_1(j_k_ff_3_qn), .Output(mux_2_1_1_bit_11_output), .Select(dec_inc_));
  Mux_2_1__1_bit mux_2_1_1_bit_12 (
    .Input_0(Outputs[3]), .Input_1(j_k_ff_4_qn), .Output(mux_2_1_1_bit_12_output), .Select(dec_inc_));
  Mux_2_1__1_bit mux_2_1_1_bit_13 (
    .Input_0(Outputs[4]), .Input_1(j_k_ff_5_qn), .Output(mux_2_1_1_bit_13_output), .Select(dec_inc_));
  Mux_2_1__1_bit mux_2_1_1_bit_14 (
    .Input_0(Outputs[5]), .Input_1(j_k_ff_6_qn), .Output(mux_2_1_1_bit_14_output), .Select(dec_inc_));
  Mux_2_1__1_bit mux_2_1_1_bit_15 (
    .Input_0(Outputs[6]), .Input_1(j_k_ff_7_qn), .Output(mux_2_1_1_bit_15_output), .Select(dec_inc_));
  Mux_2_1__1_bit mux_2_1_1_bit_16 (
    .Input_0(Outputs[7]), .Input_1(j_k_ff_8_qn), .Output(mux_2_1_1_bit_16_output), .Select(dec_inc_));
  and and_1 (and_1_out, mux_2_1_1_bit_9_output, enable);
  and and_2 (and_2_out, mux_2_1_1_bit_10_output, and_1_out);
  and and_3 (and_3_out, mux_2_1_1_bit_11_output, and_2_out);
  and and_4 (and_4_out, mux_2_1_1_bit_12_output, and_3_out);
  and and_5 (and_5_out, mux_2_1_1_bit_13_output, and_4_out);
  and and_6 (and_6_out, mux_2_1_1_bit_14_output, and_5_out);
  and and_7 (and_7_out, mux_2_1_1_bit_15_output, and_6_out);
  and and_8 (Cout, mux_2_1_1_bit_16_output, and_7_out);

  // Notes on the sheet:
  //   enable: pull=up
  //   load: pull=up
  //   8 bits universal counter
endmodule

// PC-lo
module PC_lo__Program_Counter_Low (
  input  inc,
  input  load,
  input  CLK,
  input  reset,
  input  [7:0] Inputs,
  output [7:0] Outputs,
  output Cout
);

  wire and_1_out, and_2_out, and_3_out, and_4_out, and_5_out, and_6_out, and_7_out, mux_2_1_1_bit_1_output,
       mux_2_1_1_bit_2_output, mux_2_1_1_bit_3_output, mux_2_1_1_bit_4_output, mux_2_1_1_bit_5_output,
       mux_2_1_1_bit_6_output, mux_2_1_1_bit_7_output, mux_2_1_1_bit_8_output, xor_1_out, xor_2_out,
       xor_3_out, xor_4_out, xor_5_out, xor_6_out, xor_7_out, xor_8_out;

  Mux_2_1__1_bit mux_2_1_1_bit_1 (.Input_0(inc), .Input_1(Inputs[0]), .Output(mux_2_1_1_bit_1_output), .Select(load));
  Mux_2_1__1_bit mux_2_1_1_bit_2 (
    .Input_0(and_1_out), .Input_1(Inputs[1]), .Output(mux_2_1_1_bit_2_output), .Select(load));
  Mux_2_1__1_bit mux_2_1_1_bit_3 (
    .Input_0(and_2_out), .Input_1(Inputs[2]), .Output(mux_2_1_1_bit_3_output), .Select(load));
  Mux_2_1__1_bit mux_2_1_1_bit_4 (
    .Input_0(and_3_out), .Input_1(Inputs[3]), .Output(mux_2_1_1_bit_4_output), .Select(load));
  Mux_2_1__1_bit mux_2_1_1_bit_5 (
    .Input_0(and_4_out), .Input_1(Inputs[4]), .Output(mux_2_1_1_bit_5_output), .Select(load));
  Mux_2_1__1_bit mux_2_1_1_bit_6 (
    .Input_0(and_5_out), .Input_1(Inputs[5]), .Output(mux_2_1_1_bit_6_output), .Select(load));
  Mux_2_1__1_bit mux_2_1_1_bit_7 (
    .Input_0(and_6_out), .Input_1(Inputs[6]), .Output(mux_2_1_1_bit_7_output), .Select(load));
  Mux_2_1__1_bit mux_2_1_1_bit_8 (
    .Input_0(and_7_out), .Input_1(Inputs[7]), .Output(mux_2_1_1_bit_8_output), .Select(load));
  xor xor_1 (xor_1_out, load, mux_2_1_1_bit_1_output);
  xor xor_2 (xor_2_out, load, mux_2_1_1_bit_2_output);
  xor xor_3 (xor_3_out, load, mux_2_1_1_bit_3_output);
  xor xor_4 (xor_4_out, load, mux_2_1_1_bit_4_output);
  xor xor_5 (xor_5_out, load, mux_2_1_1_bit_5_output);
  xor xor_6 (xor_6_out, load, mux_2_1_1_bit_6_output);
  xor xor_7 (xor_7_out, load, mux_2_1_1_bit_7_output);
  xor xor_8 (xor_8_out, load, mux_2_1_1_bit_8_output);
  J_K_Flip_Flop j_k_ff_1 (
    .J(mux_2_1_1_bit_1_output), .clk(CLK), .K(xor_1_out), .Q(Outputs[0]), .reset(reset));  // open: Qn, preset, en
  and and_1 (and_1_out, Outputs[0], inc);
  J_K_Flip_Flop j_k_ff_2 (
    .J(mux_2_1_1_bit_2_output), .clk(CLK), .K(xor_2_out), .Q(Outputs[1]), .reset(reset));  // open: Qn, preset, en
  and and_2 (and_2_out, Outputs[1], and_1_out);
  J_K_Flip_Flop j_k_ff_3 (
    .J(mux_2_1_1_bit_3_output), .clk(CLK), .K(xor_3_out), .Q(Outputs[2]), .reset(reset));  // open: Qn, preset, en
  and and_3 (and_3_out, Outputs[2], and_2_out);
  J_K_Flip_Flop j_k_ff_4 (
    .J(mux_2_1_1_bit_4_output), .clk(CLK), .K(xor_4_out), .Q(Outputs[3]), .reset(reset));  // open: Qn, preset, en
  and and_4 (and_4_out, Outputs[3], and_3_out);
  J_K_Flip_Flop j_k_ff_5 (
    .J(mux_2_1_1_bit_5_output), .clk(CLK), .K(xor_5_out), .Q(Outputs[4]), .reset(reset));  // open: Qn, preset, en
  and and_5 (and_5_out, Outputs[4], and_4_out);
  J_K_Flip_Flop j_k_ff_6 (
    .J(mux_2_1_1_bit_6_output), .clk(CLK), .K(xor_6_out), .Q(Outputs[5]), .reset(reset));  // open: Qn, preset, en
  and and_6 (and_6_out, Outputs[5], and_5_out);
  J_K_Flip_Flop j_k_ff_7 (
    .J(mux_2_1_1_bit_7_output), .clk(CLK), .K(xor_7_out), .Q(Outputs[6]), .reset(reset));  // open: Qn, preset, en
  and and_7 (and_7_out, Outputs[6], and_6_out);
  J_K_Flip_Flop j_k_ff_8 (
    .J(mux_2_1_1_bit_8_output), .clk(CLK), .K(xor_8_out), .Q(Outputs[7]), .reset(reset));  // open: Qn, preset, en
  and and_8 (Cout, Outputs[7], and_7_out);

  // Notes on the sheet:
  //   inc: pull=up
  //   load: pull=up
  //   8 bits counter
endmodule

// Acc
module A__Accumulator (
  input  clk,
  input  write_enable,
  input  [7:0] \input ,
  output [7:0] \output 
);

  D_Flip_Flop d_ff_1 (.clk(clk), .D(\input [0]), .Q(\output [0]), .en(write_enable));  // open: Qn, preset, reset
  D_Flip_Flop d_ff_2 (.clk(clk), .D(\input [1]), .Q(\output [1]), .en(write_enable));  // open: Qn, preset, reset
  D_Flip_Flop d_ff_3 (.clk(clk), .D(\input [2]), .Q(\output [2]), .en(write_enable));  // open: Qn, preset, reset
  D_Flip_Flop d_ff_4 (.clk(clk), .D(\input [3]), .Q(\output [3]), .en(write_enable));  // open: Qn, preset, reset
  D_Flip_Flop d_ff_5 (.clk(clk), .D(\input [4]), .Q(\output [4]), .en(write_enable));  // open: Qn, preset, reset
  D_Flip_Flop d_ff_6 (.clk(clk), .D(\input [5]), .Q(\output [5]), .en(write_enable));  // open: Qn, preset, reset
  D_Flip_Flop d_ff_7 (.clk(clk), .D(\input [6]), .Q(\output [6]), .en(write_enable));  // open: Qn, preset, reset
  D_Flip_Flop d_ff_8 (.clk(clk), .D(\input [7]), .Q(\output [7]), .en(write_enable));  // open: Qn, preset, reset

  // Notes on the sheet:
  //   8 bits register
endmodule

// X
module X__Index_X (
  input  clk,
  input  write_enable,
  input  [7:0] \input ,
  output [7:0] \output 
);

  D_Flip_Flop d_ff_1 (.clk(clk), .D(\input [0]), .Q(\output [0]), .en(write_enable));  // open: Qn, preset, reset
  D_Flip_Flop d_ff_2 (.clk(clk), .D(\input [1]), .Q(\output [1]), .en(write_enable));  // open: Qn, preset, reset
  D_Flip_Flop d_ff_3 (.clk(clk), .D(\input [2]), .Q(\output [2]), .en(write_enable));  // open: Qn, preset, reset
  D_Flip_Flop d_ff_4 (.clk(clk), .D(\input [3]), .Q(\output [3]), .en(write_enable));  // open: Qn, preset, reset
  D_Flip_Flop d_ff_5 (.clk(clk), .D(\input [4]), .Q(\output [4]), .en(write_enable));  // open: Qn, preset, reset
  D_Flip_Flop d_ff_6 (.clk(clk), .D(\input [5]), .Q(\output [5]), .en(write_enable));  // open: Qn, preset, reset
  D_Flip_Flop d_ff_7 (.clk(clk), .D(\input [6]), .Q(\output [6]), .en(write_enable));  // open: Qn, preset, reset
  D_Flip_Flop d_ff_8 (.clk(clk), .D(\input [7]), .Q(\output [7]), .en(write_enable));  // open: Qn, preset, reset

  // Notes on the sheet:
  //   8 bits register
endmodule

// Y
module Y__Index_Y (
  input  clk,
  input  write_enable,
  input  [7:0] \input ,
  output [7:0] \output 
);

  D_Flip_Flop d_ff_1 (.clk(clk), .D(\input [0]), .Q(\output [0]), .en(write_enable));  // open: Qn, preset, reset
  D_Flip_Flop d_ff_2 (.clk(clk), .D(\input [1]), .Q(\output [1]), .en(write_enable));  // open: Qn, preset, reset
  D_Flip_Flop d_ff_3 (.clk(clk), .D(\input [2]), .Q(\output [2]), .en(write_enable));  // open: Qn, preset, reset
  D_Flip_Flop d_ff_4 (.clk(clk), .D(\input [3]), .Q(\output [3]), .en(write_enable));  // open: Qn, preset, reset
  D_Flip_Flop d_ff_5 (.clk(clk), .D(\input [4]), .Q(\output [4]), .en(write_enable));  // open: Qn, preset, reset
  D_Flip_Flop d_ff_6 (.clk(clk), .D(\input [5]), .Q(\output [5]), .en(write_enable));  // open: Qn, preset, reset
  D_Flip_Flop d_ff_7 (.clk(clk), .D(\input [6]), .Q(\output [6]), .en(write_enable));  // open: Qn, preset, reset
  D_Flip_Flop d_ff_8 (.clk(clk), .D(\input [7]), .Q(\output [7]), .en(write_enable));  // open: Qn, preset, reset

  // Notes on the sheet:
  //   8 bits register
endmodule

// SP
module S__Stack_Pointer (
  input  clk,
  input  write_enable,
  input  [7:0] \input ,
  output [7:0] \output 
);

  D_Flip_Flop d_ff_1 (.clk(clk), .D(\input [0]), .Q(\output [0]), .en(write_enable));  // open: Qn, preset, reset
  D_Flip_Flop d_ff_2 (.clk(clk), .D(\input [1]), .Q(\output [1]), .en(write_enable));  // open: Qn, preset, reset
  D_Flip_Flop d_ff_3 (.clk(clk), .D(\input [2]), .Q(\output [2]), .en(write_enable));  // open: Qn, preset, reset
  D_Flip_Flop d_ff_4 (.clk(clk), .D(\input [3]), .Q(\output [3]), .en(write_enable));  // open: Qn, preset, reset
  D_Flip_Flop d_ff_5 (.clk(clk), .D(\input [4]), .Q(\output [4]), .en(write_enable));  // open: Qn, preset, reset
  D_Flip_Flop d_ff_6 (.clk(clk), .D(\input [5]), .Q(\output [5]), .en(write_enable));  // open: Qn, preset, reset
  D_Flip_Flop d_ff_7 (.clk(clk), .D(\input [6]), .Q(\output [6]), .en(write_enable));  // open: Qn, preset, reset
  D_Flip_Flop d_ff_8 (.clk(clk), .D(\input [7]), .Q(\output [7]), .en(write_enable));  // open: Qn, preset, reset

  // Notes on the sheet:
  //   8 bits register
endmodule

// Flags Register (P)
module Flags__Status_Processor_Register (
  input  clk,
  input  N_in,
  input  V_in,
  input  B_in,
  input  Z_in,
  input  C_in,
  input  cfg2,
  input  cfg1,
  input  cfg0,
  input  F2,
  input  F1,
  input  F0,
  input  [7:0] Memory_input,
  input  SO,
  output [7:0] processor_status_register_output,
  output N_out,
  output V_out,
  output out,
  output B_out,
  output D_out,
  output I_out,
  output Z_out,
  output C_out
);

  wire and_1_out, and_2_out, and_3_out, and_4_out, and_5_out, and_6_out, and_7_out, and_8_out, and_9_out,
       and_10_out, controlled_buffer_1_out, controlled_buffer_2_out, controlled_buffer_3_out,
       controlled_buffer_4_out, controlled_buffer_5_out, controlled_buffer_6_out, controlled_buffer_7_out,
       controlled_buffer_8_out, controlled_buffer_9_out, decoder_3_8_1_bit_1_output_0,
       decoder_3_8_1_bit_1_output_1, decoder_3_8_1_bit_1_output_2, decoder_3_8_1_bit_1_output_6,
       decoder_3_8_1_bit_1_output_7, not_1_out, not_2_out, or_1_out, or_2_out, or_3_out, or_4_out, undriven;
  wire [7:0] mux_2_1_8_bits_1_output;

  Mux_2_1__8_bits mux_2_1_8_bits_1 (
    .Input_0({N_in, V_in, 4'b0000, Z_in, C_in}), .Input_1(Memory_input), .Output(mux_2_1_8_bits_1_output),
    .Select(and_3_out));
  not not_1 (not_1_out, clk);
  and and_1 (and_1_out, clk, not_1_out, and_4_out);
  not not_2 (not_2_out, clk);
  and and_2 (and_2_out, clk, not_2_out, and_6_out);
  assign controlled_buffer_1_out = and_2_out ? decoder_3_8_1_bit_1_output_7 : 1'bz;  // Controlled_Buffer controlled_buffer_1
  assign controlled_buffer_2_out = and_1_out ? decoder_3_8_1_bit_1_output_7 : 1'bz;  // Controlled_Buffer controlled_buffer_2
  and and_3 (and_3_out, cfg2, cfg1);
  D_Flip_Flop d_ff_1 (
    .clk(clk), .D(mux_2_1_8_bits_1_output[7]), .Q(N_out), .preset(controlled_buffer_2_out), .en(or_1_out),
    .reset(controlled_buffer_1_out));  // open: Qn
  and and_4 (and_4_out, cfg2, ~cfg1, ~cfg0);  // AND_Gate
  D_Flip_Flop d_ff_2 (
    .clk(clk), .D(mux_2_1_8_bits_1_output[6]), .Q(processor_status_register_output[6]), .preset(SO),
    .en(or_2_out), .reset(controlled_buffer_3_out));  // open: Qn
  assign controlled_buffer_3_out = and_2_out ? decoder_3_8_1_bit_1_output_6 : 1'bz;  // Controlled_Buffer controlled_buffer_3
  and and_5 (and_5_out, ~cfg2, cfg0);  // AND_Gate
  and and_6 (and_6_out, cfg2, ~cfg1, cfg0);  // AND_Gate
  or or_1 (or_1_out, and_5_out, cfg1);
  D_Flip_Flop d_ff_3 (.clk(clk), .Q(out), .preset(1'b1), .en(1'b0), .reset(1'b0));  // open: D, Qn
  and and_7 (and_7_out, cfg2, cfg1);
  and and_8 (and_8_out, cfg2, cfg1, cfg0);
  or or_2 (or_2_out, and_7_out, and_10_out);
  D_Flip_Flop d_ff_4 (.clk(clk));  // open: D, Q, Qn, preset, en, reset
  and and_9 (and_9_out, ~cfg2, cfg1);  // AND_Gate
  and and_10 (and_10_out, cfg1, cfg0);
  or or_3 (or_3_out, and_5_out, and_10_out, and_9_out);
  or or_4 (or_4_out, and_10_out, and_9_out);
  D_Flip_Flop d_ff_5 (.clk(clk), .D(undriven), .Q(D_out), .preset(1'b0), .en(1'b0), .reset(1'b1));  // open: Qn
  assign controlled_buffer_4_out = and_1_out ? decoder_3_8_1_bit_1_output_2 : 1'bz;  // Controlled_Buffer controlled_buffer_4
  D_Flip_Flop d_ff_6 (
    .clk(clk), .D(mux_2_1_8_bits_1_output[2]), .Q(I_out), .preset(controlled_buffer_4_out), .en(and_8_out),
    .reset(controlled_buffer_5_out));  // open: Qn
  assign controlled_buffer_5_out = and_2_out ? decoder_3_8_1_bit_1_output_2 : 1'bz;  // Controlled_Buffer controlled_buffer_5
  Decoder_3_8__1_bit decoder_3_8_1_bit_1 (
    .output_0(decoder_3_8_1_bit_1_output_0), .output_1(decoder_3_8_1_bit_1_output_1),
    .output_2(decoder_3_8_1_bit_1_output_2), .output_6(decoder_3_8_1_bit_1_output_6),
    .output_7(decoder_3_8_1_bit_1_output_7), .Input_2(F2), .Input_1(F1), .Input_0(F0));  // open: output_3, output_4, output_5
  D_Flip_Flop d_ff_7 (
    .clk(clk), .D(mux_2_1_8_bits_1_output[1]), .Q(processor_status_register_output[1]),
    .preset(controlled_buffer_7_out), .en(or_3_out), .reset(controlled_buffer_6_out));  // open: Qn
  assign controlled_buffer_6_out = and_2_out ? decoder_3_8_1_bit_1_output_1 : 1'bz;  // Controlled_Buffer controlled_buffer_6
  assign controlled_buffer_7_out = and_1_out ? decoder_3_8_1_bit_1_output_1 : 1'bz;  // Controlled_Buffer controlled_buffer_7
  D_Flip_Flop d_ff_8 (
    .clk(clk), .D(mux_2_1_8_bits_1_output[0]), .Q(C_out), .preset(controlled_buffer_9_out), .en(or_4_out),
    .reset(controlled_buffer_8_out));  // open: Qn
  assign controlled_buffer_8_out = and_2_out ? decoder_3_8_1_bit_1_output_0 : 1'bz;  // Controlled_Buffer controlled_buffer_8
  assign controlled_buffer_9_out = and_1_out ? decoder_3_8_1_bit_1_output_0 : 1'bz;  // Controlled_Buffer controlled_buffer_9

  assign B_out = B_in;
  assign {processor_status_register_output[7], processor_status_register_output[5:2], processor_status_register_output[0]} = {N_out, out, B_in, D_out, I_out, C_out};
  assign V_out = processor_status_register_output[6];
  assign Z_out = processor_status_register_output[1];

  // Notes on the sheet:
  //   rising edge
  //   pulse circuit
  //   Note : the pulse circuit prevent flipflop asynchronous set/reset to last all the clock period, which risks to spread to the next period
  //   Flags controller
endmodule

// OUT
module OUT__Data_output_register (
  input  clk,
  input  write_enable,
  input  [7:0] \input ,
  output [7:0] \output 
);

  D_Flip_Flop d_ff_1 (.clk(clk), .D(\input [0]), .Q(\output [0]), .en(write_enable));  // open: Qn, preset, reset
  D_Flip_Flop d_ff_2 (.clk(clk), .D(\input [1]), .Q(\output [1]), .en(write_enable));  // open: Qn, preset, reset
  D_Flip_Flop d_ff_3 (.clk(clk), .D(\input [2]), .Q(\output [2]), .en(write_enable));  // open: Qn, preset, reset
  D_Flip_Flop d_ff_4 (.clk(clk), .D(\input [3]), .Q(\output [3]), .en(write_enable));  // open: Qn, preset, reset
  D_Flip_Flop d_ff_5 (.clk(clk), .D(\input [4]), .Q(\output [4]), .en(write_enable));  // open: Qn, preset, reset
  D_Flip_Flop d_ff_6 (.clk(clk), .D(\input [5]), .Q(\output [5]), .en(write_enable));  // open: Qn, preset, reset
  D_Flip_Flop d_ff_7 (.clk(clk), .D(\input [6]), .Q(\output [6]), .en(write_enable));  // open: Qn, preset, reset
  D_Flip_Flop d_ff_8 (.clk(clk), .D(\input [7]), .Q(\output [7]), .en(write_enable));  // open: Qn, preset, reset

  // Notes on the sheet:
  //   8 bits register
endmodule

// AB-hi
module Address_Bus__high (
  input  clk,
  input  write_enable,
  input  [7:0] \input ,
  output [7:0] \output 
);

  D_Flip_Flop d_ff_1 (.clk(clk), .D(\input [0]), .Q(\output [0]), .en(write_enable));  // open: Qn, preset, reset
  D_Flip_Flop d_ff_2 (.clk(clk), .D(\input [1]), .Q(\output [1]), .en(write_enable));  // open: Qn, preset, reset
  D_Flip_Flop d_ff_3 (.clk(clk), .D(\input [2]), .Q(\output [2]), .en(write_enable));  // open: Qn, preset, reset
  D_Flip_Flop d_ff_4 (.clk(clk), .D(\input [3]), .Q(\output [3]), .en(write_enable));  // open: Qn, preset, reset
  D_Flip_Flop d_ff_5 (.clk(clk), .D(\input [4]), .Q(\output [4]), .en(write_enable));  // open: Qn, preset, reset
  D_Flip_Flop d_ff_6 (.clk(clk), .D(\input [5]), .Q(\output [5]), .en(write_enable));  // open: Qn, preset, reset
  D_Flip_Flop d_ff_7 (.clk(clk), .D(\input [6]), .Q(\output [6]), .en(write_enable));  // open: Qn, preset, reset
  D_Flip_Flop d_ff_8 (.clk(clk), .D(\input [7]), .Q(\output [7]), .en(write_enable));  // open: Qn, preset, reset

  // Notes on the sheet:
  //   8 bits register
endmodule

// AB-lo
module Address_Bus__low_register (
  input  inc,
  input  load,
  input  CLK,
  input  reset,
  input  [7:0] Inputs,
  output [7:0] Outputs,
  output Cout
);

  wire and_1_out, and_2_out, and_3_out, and_4_out, and_5_out, and_6_out, and_7_out, mux_2_1_1_bit_1_output,
       mux_2_1_1_bit_2_output, mux_2_1_1_bit_3_output, mux_2_1_1_bit_4_output, mux_2_1_1_bit_5_output,
       mux_2_1_1_bit_6_output, mux_2_1_1_bit_7_output, mux_2_1_1_bit_8_output, xor_1_out, xor_2_out,
       xor_3_out, xor_4_out, xor_5_out, xor_6_out, xor_7_out, xor_8_out;

  Mux_2_1__1_bit mux_2_1_1_bit_1 (.Input_0(inc), .Input_1(Inputs[0]), .Output(mux_2_1_1_bit_1_output), .Select(load));
  Mux_2_1__1_bit mux_2_1_1_bit_2 (
    .Input_0(and_1_out), .Input_1(Inputs[1]), .Output(mux_2_1_1_bit_2_output), .Select(load));
  Mux_2_1__1_bit mux_2_1_1_bit_3 (
    .Input_0(and_2_out), .Input_1(Inputs[2]), .Output(mux_2_1_1_bit_3_output), .Select(load));
  Mux_2_1__1_bit mux_2_1_1_bit_4 (
    .Input_0(and_3_out), .Input_1(Inputs[3]), .Output(mux_2_1_1_bit_4_output), .Select(load));
  Mux_2_1__1_bit mux_2_1_1_bit_5 (
    .Input_0(and_4_out), .Input_1(Inputs[4]), .Output(mux_2_1_1_bit_5_output), .Select(load));
  Mux_2_1__1_bit mux_2_1_1_bit_6 (
    .Input_0(and_5_out), .Input_1(Inputs[5]), .Output(mux_2_1_1_bit_6_output), .Select(load));
  Mux_2_1__1_bit mux_2_1_1_bit_7 (
    .Input_0(and_6_out), .Input_1(Inputs[6]), .Output(mux_2_1_1_bit_7_output), .Select(load));
  Mux_2_1__1_bit mux_2_1_1_bit_8 (
    .Input_0(and_7_out), .Input_1(Inputs[7]), .Output(mux_2_1_1_bit_8_output), .Select(load));
  xor xor_1 (xor_1_out, load, mux_2_1_1_bit_1_output);
  xor xor_2 (xor_2_out, load, mux_2_1_1_bit_2_output);
  xor xor_3 (xor_3_out, load, mux_2_1_1_bit_3_output);
  xor xor_4 (xor_4_out, load, mux_2_1_1_bit_4_output);
  xor xor_5 (xor_5_out, load, mux_2_1_1_bit_5_output);
  xor xor_6 (xor_6_out, load, mux_2_1_1_bit_6_output);
  xor xor_7 (xor_7_out, load, mux_2_1_1_bit_7_output);
  xor xor_8 (xor_8_out, load, mux_2_1_1_bit_8_output);
  J_K_Flip_Flop j_k_ff_1 (
    .J(mux_2_1_1_bit_1_output), .clk(CLK), .K(xor_1_out), .Q(Outputs[0]), .reset(reset));  // open: Qn, preset, en
  and and_1 (and_1_out, Outputs[0], inc);
  J_K_Flip_Flop j_k_ff_2 (
    .J(mux_2_1_1_bit_2_output), .clk(CLK), .K(xor_2_out), .Q(Outputs[1]), .reset(reset));  // open: Qn, preset, en
  and and_2 (and_2_out, Outputs[1], and_1_out);
  J_K_Flip_Flop j_k_ff_3 (
    .J(mux_2_1_1_bit_3_output), .clk(CLK), .K(xor_3_out), .Q(Outputs[2]), .reset(reset));  // open: Qn, preset, en
  and and_3 (and_3_out, Outputs[2], and_2_out);
  J_K_Flip_Flop j_k_ff_4 (
    .J(mux_2_1_1_bit_4_output), .clk(CLK), .K(xor_4_out), .Q(Outputs[3]), .reset(reset));  // open: Qn, preset, en
  and and_4 (and_4_out, Outputs[3], and_3_out);
  J_K_Flip_Flop j_k_ff_5 (
    .J(mux_2_1_1_bit_5_output), .clk(CLK), .K(xor_5_out), .Q(Outputs[4]), .reset(reset));  // open: Qn, preset, en
  and and_5 (and_5_out, Outputs[4], and_4_out);
  J_K_Flip_Flop j_k_ff_6 (
    .J(mux_2_1_1_bit_6_output), .clk(CLK), .K(xor_6_out), .Q(Outputs[5]), .reset(reset));  // open: Qn, preset, en
  and and_6 (and_6_out, Outputs[5], and_5_out);
  J_K_Flip_Flop j_k_ff_7 (
    .J(mux_2_1_1_bit_7_output), .clk(CLK), .K(xor_7_out), .Q(Outputs[6]), .reset(reset));  // open: Qn, preset, en
  and and_7 (and_7_out, Outputs[6], and_6_out);
  J_K_Flip_Flop j_k_ff_8 (
    .J(mux_2_1_1_bit_8_output), .clk(CLK), .K(xor_8_out), .Q(Outputs[7]), .reset(reset));  // open: Qn, preset, en
  and and_8 (Cout, Outputs[7], and_7_out);

  // Notes on the sheet:
  //   inc: pull=up
  //   load: pull=up
  //   8 bits counter
endmodule

// Address-hi
module Address_hi__Adress_high (
  input  inc,
  input  load,
  input  CLK,
  input  reset,
  input  [7:0] Inputs,
  output [7:0] Outputs,
  output Cout
);

  wire and_1_out, and_2_out, and_3_out, and_4_out, and_5_out, and_6_out, and_7_out, mux_2_1_1_bit_1_output,
       mux_2_1_1_bit_2_output, mux_2_1_1_bit_3_output, mux_2_1_1_bit_4_output, mux_2_1_1_bit_5_output,
       mux_2_1_1_bit_6_output, mux_2_1_1_bit_7_output, mux_2_1_1_bit_8_output, xor_1_out, xor_2_out,
       xor_3_out, xor_4_out, xor_5_out, xor_6_out, xor_7_out, xor_8_out;

  Mux_2_1__1_bit mux_2_1_1_bit_1 (.Input_0(inc), .Input_1(Inputs[0]), .Output(mux_2_1_1_bit_1_output), .Select(load));
  Mux_2_1__1_bit mux_2_1_1_bit_2 (
    .Input_0(and_1_out), .Input_1(Inputs[1]), .Output(mux_2_1_1_bit_2_output), .Select(load));
  Mux_2_1__1_bit mux_2_1_1_bit_3 (
    .Input_0(and_2_out), .Input_1(Inputs[2]), .Output(mux_2_1_1_bit_3_output), .Select(load));
  Mux_2_1__1_bit mux_2_1_1_bit_4 (
    .Input_0(and_3_out), .Input_1(Inputs[3]), .Output(mux_2_1_1_bit_4_output), .Select(load));
  Mux_2_1__1_bit mux_2_1_1_bit_5 (
    .Input_0(and_4_out), .Input_1(Inputs[4]), .Output(mux_2_1_1_bit_5_output), .Select(load));
  Mux_2_1__1_bit mux_2_1_1_bit_6 (
    .Input_0(and_5_out), .Input_1(Inputs[5]), .Output(mux_2_1_1_bit_6_output), .Select(load));
  Mux_2_1__1_bit mux_2_1_1_bit_7 (
    .Input_0(and_6_out), .Input_1(Inputs[6]), .Output(mux_2_1_1_bit_7_output), .Select(load));
  Mux_2_1__1_bit mux_2_1_1_bit_8 (
    .Input_0(and_7_out), .Input_1(Inputs[7]), .Output(mux_2_1_1_bit_8_output), .Select(load));
  xor xor_1 (xor_1_out, load, mux_2_1_1_bit_1_output);
  xor xor_2 (xor_2_out, load, mux_2_1_1_bit_2_output);
  xor xor_3 (xor_3_out, load, mux_2_1_1_bit_3_output);
  xor xor_4 (xor_4_out, load, mux_2_1_1_bit_4_output);
  xor xor_5 (xor_5_out, load, mux_2_1_1_bit_5_output);
  xor xor_6 (xor_6_out, load, mux_2_1_1_bit_6_output);
  xor xor_7 (xor_7_out, load, mux_2_1_1_bit_7_output);
  xor xor_8 (xor_8_out, load, mux_2_1_1_bit_8_output);
  J_K_Flip_Flop j_k_ff_1 (
    .J(mux_2_1_1_bit_1_output), .clk(CLK), .K(xor_1_out), .Q(Outputs[0]), .reset(reset));  // open: Qn, preset, en
  and and_1 (and_1_out, Outputs[0], inc);
  J_K_Flip_Flop j_k_ff_2 (
    .J(mux_2_1_1_bit_2_output), .clk(CLK), .K(xor_2_out), .Q(Outputs[1]), .reset(reset));  // open: Qn, preset, en
  and and_2 (and_2_out, Outputs[1], and_1_out);
  J_K_Flip_Flop j_k_ff_3 (
    .J(mux_2_1_1_bit_3_output), .clk(CLK), .K(xor_3_out), .Q(Outputs[2]), .reset(reset));  // open: Qn, preset, en
  and and_3 (and_3_out, Outputs[2], and_2_out);
  J_K_Flip_Flop j_k_ff_4 (
    .J(mux_2_1_1_bit_4_output), .clk(CLK), .K(xor_4_out), .Q(Outputs[3]), .reset(reset));  // open: Qn, preset, en
  and and_4 (and_4_out, Outputs[3], and_3_out);
  J_K_Flip_Flop j_k_ff_5 (
    .J(mux_2_1_1_bit_5_output), .clk(CLK), .K(xor_5_out), .Q(Outputs[4]), .reset(reset));  // open: Qn, preset, en
  and and_5 (and_5_out, Outputs[4], and_4_out);
  J_K_Flip_Flop j_k_ff_6 (
    .J(mux_2_1_1_bit_6_output), .clk(CLK), .K(xor_6_out), .Q(Outputs[5]), .reset(reset));  // open: Qn, preset, en
  and and_6 (and_6_out, Outputs[5], and_5_out);
  J_K_Flip_Flop j_k_ff_7 (
    .J(mux_2_1_1_bit_7_output), .clk(CLK), .K(xor_7_out), .Q(Outputs[6]), .reset(reset));  // open: Qn, preset, en
  and and_7 (and_7_out, Outputs[6], and_6_out);
  J_K_Flip_Flop j_k_ff_8 (
    .J(mux_2_1_1_bit_8_output), .clk(CLK), .K(xor_8_out), .Q(Outputs[7]), .reset(reset));  // open: Qn, preset, en
  and and_8 (Cout, Outputs[7], and_7_out);

  // Notes on the sheet:
  //   inc: pull=up
  //   load: pull=up
  //   8 bits counter
endmodule

// Address-lo
module Address_lo__Adress_low (
  input  clk,
  input  write_enable,
  input  [7:0] \input ,
  output [7:0] \output 
);

  D_Flip_Flop d_ff_1 (.clk(clk), .D(\input [0]), .Q(\output [0]), .en(write_enable));  // open: Qn, preset, reset
  D_Flip_Flop d_ff_2 (.clk(clk), .D(\input [1]), .Q(\output [1]), .en(write_enable));  // open: Qn, preset, reset
  D_Flip_Flop d_ff_3 (.clk(clk), .D(\input [2]), .Q(\output [2]), .en(write_enable));  // open: Qn, preset, reset
  D_Flip_Flop d_ff_4 (.clk(clk), .D(\input [3]), .Q(\output [3]), .en(write_enable));  // open: Qn, preset, reset
  D_Flip_Flop d_ff_5 (.clk(clk), .D(\input [4]), .Q(\output [4]), .en(write_enable));  // open: Qn, preset, reset
  D_Flip_Flop d_ff_6 (.clk(clk), .D(\input [5]), .Q(\output [5]), .en(write_enable));  // open: Qn, preset, reset
  D_Flip_Flop d_ff_7 (.clk(clk), .D(\input [6]), .Q(\output [6]), .en(write_enable));  // open: Qn, preset, reset
  D_Flip_Flop d_ff_8 (.clk(clk), .D(\input [7]), .Q(\output [7]), .en(write_enable));  // open: Qn, preset, reset

  // Notes on the sheet:
  //   8 bits register
endmodule

// TMP
module TMP__Temporary_register (
  input  clk,
  input  write_enable,
  input  [7:0] \input ,
  output [7:0] \output 
);

  D_Flip_Flop d_ff_1 (.clk(clk), .D(\input [0]), .Q(\output [0]), .en(write_enable));  // open: Qn, preset, reset
  D_Flip_Flop d_ff_2 (.clk(clk), .D(\input [1]), .Q(\output [1]), .en(write_enable));  // open: Qn, preset, reset
  D_Flip_Flop d_ff_3 (.clk(clk), .D(\input [2]), .Q(\output [2]), .en(write_enable));  // open: Qn, preset, reset
  D_Flip_Flop d_ff_4 (.clk(clk), .D(\input [3]), .Q(\output [3]), .en(write_enable));  // open: Qn, preset, reset
  D_Flip_Flop d_ff_5 (.clk(clk), .D(\input [4]), .Q(\output [4]), .en(write_enable));  // open: Qn, preset, reset
  D_Flip_Flop d_ff_6 (.clk(clk), .D(\input [5]), .Q(\output [5]), .en(write_enable));  // open: Qn, preset, reset
  D_Flip_Flop d_ff_7 (.clk(clk), .D(\input [6]), .Q(\output [6]), .en(write_enable));  // open: Qn, preset, reset
  D_Flip_Flop d_ff_8 (.clk(clk), .D(\input [7]), .Q(\output [7]), .en(write_enable));  // open: Qn, preset, reset

  // Notes on the sheet:
  //   8 bits register
endmodule

// SC
module SC__Sequencer_Controller (
  input  Interrupt,
  input  SYNC,
  input  [1:0] Command,
  output Operation_Mapper_Address_Mode_Mapper_,
  output Load_Mapper_Brench_,
  output Load_CAR_,
  output reset
);

  and and_1 (reset, Interrupt, SYNC);
  or or_1 (Load_CAR_, Command[1], Command[0]);

  assign Load_Mapper_Brench_ = Command[1];
  assign Operation_Mapper_Address_Mode_Mapper_ = Command[0];
endmodule

// CAR
module CAR__Control_Address_Register (
  input  load_inc_,
  input  CLK,
  input  reset,
  input  [7:0] Inputs,
  output [7:0] Outputs,
  output Cout
);

  wire and_1_out, and_2_out, and_3_out, and_4_out, and_5_out, and_6_out, and_7_out, mux_2_1_1_bit_1_output,
       mux_2_1_1_bit_2_output, mux_2_1_1_bit_3_output, mux_2_1_1_bit_4_output, mux_2_1_1_bit_5_output,
       mux_2_1_1_bit_6_output, mux_2_1_1_bit_7_output, mux_2_1_1_bit_8_output, not_1_out, xor_1_out,
       xor_2_out, xor_3_out, xor_4_out, xor_5_out, xor_6_out, xor_7_out, xor_8_out;

  not not_1 (not_1_out, load_inc_);
  Mux_2_1__1_bit mux_2_1_1_bit_1 (
    .Input_0(not_1_out), .Input_1(Inputs[0]), .Output(mux_2_1_1_bit_1_output), .Select(load_inc_));
  Mux_2_1__1_bit mux_2_1_1_bit_2 (
    .Input_0(and_1_out), .Input_1(Inputs[1]), .Output(mux_2_1_1_bit_2_output), .Select(load_inc_));
  Mux_2_1__1_bit mux_2_1_1_bit_3 (
    .Input_0(and_2_out), .Input_1(Inputs[2]), .Output(mux_2_1_1_bit_3_output), .Select(load_inc_));
  Mux_2_1__1_bit mux_2_1_1_bit_4 (
    .Input_0(and_3_out), .Input_1(Inputs[3]), .Output(mux_2_1_1_bit_4_output), .Select(load_inc_));
  Mux_2_1__1_bit mux_2_1_1_bit_5 (
    .Input_0(and_4_out), .Input_1(Inputs[4]), .Output(mux_2_1_1_bit_5_output), .Select(load_inc_));
  Mux_2_1__1_bit mux_2_1_1_bit_6 (
    .Input_0(and_5_out), .Input_1(Inputs[5]), .Output(mux_2_1_1_bit_6_output), .Select(load_inc_));
  Mux_2_1__1_bit mux_2_1_1_bit_7 (
    .Input_0(and_6_out), .Input_1(Inputs[6]), .Output(mux_2_1_1_bit_7_output), .Select(load_inc_));
  Mux_2_1__1_bit mux_2_1_1_bit_8 (
    .Input_0(and_7_out), .Input_1(Inputs[7]), .Output(mux_2_1_1_bit_8_output), .Select(load_inc_));
  xor xor_1 (xor_1_out, load_inc_, mux_2_1_1_bit_1_output);
  xor xor_2 (xor_2_out, load_inc_, mux_2_1_1_bit_2_output);
  xor xor_3 (xor_3_out, load_inc_, mux_2_1_1_bit_3_output);
  xor xor_4 (xor_4_out, load_inc_, mux_2_1_1_bit_4_output);
  xor xor_5 (xor_5_out, load_inc_, mux_2_1_1_bit_5_output);
  xor xor_6 (xor_6_out, load_inc_, mux_2_1_1_bit_6_output);
  xor xor_7 (xor_7_out, load_inc_, mux_2_1_1_bit_7_output);
  xor xor_8 (xor_8_out, load_inc_, mux_2_1_1_bit_8_output);
  J_K_Flip_Flop j_k_ff_1 (
    .J(mux_2_1_1_bit_1_output), .clk(CLK), .K(xor_1_out), .Q(Outputs[0]), .reset(reset));  // open: Qn, preset, en
  and and_1 (and_1_out, Outputs[0], not_1_out);
  J_K_Flip_Flop j_k_ff_2 (
    .J(mux_2_1_1_bit_2_output), .clk(CLK), .K(xor_2_out), .Q(Outputs[1]), .reset(reset));  // open: Qn, preset, en
  and and_2 (and_2_out, Outputs[1], and_1_out);
  J_K_Flip_Flop j_k_ff_3 (
    .J(mux_2_1_1_bit_3_output), .clk(CLK), .K(xor_3_out), .Q(Outputs[2]), .reset(reset));  // open: Qn, preset, en
  and and_3 (and_3_out, Outputs[2], and_2_out);
  J_K_Flip_Flop j_k_ff_4 (
    .J(mux_2_1_1_bit_4_output), .clk(CLK), .K(xor_4_out), .Q(Outputs[3]), .reset(reset));  // open: Qn, preset, en
  and and_4 (and_4_out, Outputs[3], and_3_out);
  J_K_Flip_Flop j_k_ff_5 (
    .J(mux_2_1_1_bit_5_output), .clk(CLK), .K(xor_5_out), .Q(Outputs[4]), .reset(reset));  // open: Qn, preset, en
  and and_5 (and_5_out, Outputs[4], and_4_out);
  J_K_Flip_Flop j_k_ff_6 (
    .J(mux_2_1_1_bit_6_output), .clk(CLK), .K(xor_6_out), .Q(Outputs[5]), .reset(reset));  // open: Qn, preset, en
  and and_6 (and_6_out, Outputs[5], and_5_out);
  J_K_Flip_Flop j_k_ff_7 (
    .J(mux_2_1_1_bit_7_output), .clk(CLK), .K(xor_7_out), .Q(Outputs[6]), .reset(reset));  // open: Qn, preset, en
  and and_7 (and_7_out, Outputs[6], and_6_out);
  J_K_Flip_Flop j_k_ff_8 (
    .J(mux_2_1_1_bit_8_output), .clk(CLK), .K(xor_8_out), .Q(Outputs[7]), .reset(reset));  // open: Qn, preset, en
  and and_8 (Cout, Outputs[7], and_7_out);

  // Notes on the sheet:
  //   load_inc_: pull=up
endmodule

// CSR
module CSR__Control_Status_Register (
  input  clk,
  input  Write,
  input  [9:0] next_address_input,
  input  [31:0] signals_input,
  output SC1,
  output SC0,
  output SYNC,
  output R_W_,
  output PC_plus_plus,
  output OUTw,
  output ABw,
  output IRw,
  output PChw,
  output PClw,
  output SPw,
  output TMPw,
  output Yw,
  output Xw,
  output Accw,
  output F2,
  output F1,
  output F0,
  output CF2,
  output CF1,
  output CF0,
  output V2,
  output V1,
  output V0,
  output MU1,
  output MU0,
  output Mux2,
  output Mux1,
  output Mux0,
  output ALU3,
  output ALU2,
  output ALU1,
  output ALU0,
  output AD7,
  output AD6,
  output AD5,
  output AD4,
  output AD3,
  output AD2,
  output AD1,
  output AD0
);

  wire d_ff_42_q;

  D_Flip_Flop d_ff_1 (.clk(clk), .D(next_address_input[0]), .Q(AD0), .en(Write));  // open: Qn, preset, reset
  D_Flip_Flop d_ff_2 (.clk(clk), .D(next_address_input[1]), .Q(AD1), .en(Write));  // open: Qn, preset, reset
  D_Flip_Flop d_ff_3 (.clk(clk), .D(next_address_input[2]), .Q(AD2), .en(Write));  // open: Qn, preset, reset
  D_Flip_Flop d_ff_4 (.clk(clk), .D(next_address_input[3]), .Q(AD3), .en(Write));  // open: Qn, preset, reset
  D_Flip_Flop d_ff_5 (.clk(clk), .D(next_address_input[4]), .Q(AD4), .en(Write));  // open: Qn, preset, reset
  D_Flip_Flop d_ff_6 (.clk(clk), .D(next_address_input[5]), .Q(AD5), .en(Write));  // open: Qn, preset, reset
  D_Flip_Flop d_ff_7 (.clk(clk), .D(next_address_input[6]), .Q(AD6), .en(Write));  // open: Qn, preset, reset
  D_Flip_Flop d_ff_8 (.clk(clk), .D(next_address_input[7]), .Q(AD7), .en(Write));  // open: Qn, preset, reset
  D_Flip_Flop d_ff_9 (.clk(clk), .D(next_address_input[8]), .Q(SC0), .en(Write));  // open: Qn, preset, reset
  D_Flip_Flop d_ff_10 (.clk(clk), .D(next_address_input[9]), .Q(SC1), .en(Write));  // open: Qn, preset, reset
  D_Flip_Flop d_ff_11 (.clk(clk), .D(signals_input[0]), .Q(ALU0), .en(Write));  // open: Qn, preset, reset
  D_Flip_Flop d_ff_12 (.clk(clk), .D(signals_input[1]), .Q(ALU1), .en(Write));  // open: Qn, preset, reset
  D_Flip_Flop d_ff_13 (.clk(clk), .D(signals_input[2]), .Q(ALU2), .en(Write));  // open: Qn, preset, reset
  D_Flip_Flop d_ff_14 (.clk(clk), .D(signals_input[3]), .Q(ALU3), .en(Write));  // open: Qn, preset, reset
  D_Flip_Flop d_ff_15 (.clk(clk), .D(signals_input[4]), .Q(Mux0), .en(Write));  // open: Qn, preset, reset
  D_Flip_Flop d_ff_16 (.clk(clk), .D(signals_input[5]), .Q(Mux1), .en(Write));  // open: Qn, preset, reset
  D_Flip_Flop d_ff_17 (.clk(clk), .D(signals_input[6]), .Q(Mux2), .en(Write));  // open: Qn, preset, reset
  D_Flip_Flop d_ff_18 (.clk(clk), .D(signals_input[7]), .Q(MU0), .en(Write));  // open: Qn, preset, reset
  D_Flip_Flop d_ff_19 (.clk(clk), .D(signals_input[8]), .Q(MU1), .en(Write));  // open: Qn, preset, reset
  D_Flip_Flop d_ff_20 (.clk(clk), .D(signals_input[9]), .Q(V0), .en(Write));  // open: Qn, preset, reset
  D_Flip_Flop d_ff_21 (.clk(clk), .D(signals_input[10]), .Q(V1), .en(Write));  // open: Qn, preset, reset
  D_Flip_Flop d_ff_22 (.clk(clk), .D(signals_input[11]), .Q(V2), .en(Write));  // open: Qn, preset, reset
  D_Flip_Flop d_ff_23 (.clk(clk), .D(signals_input[12]), .Q(CF0), .en(Write));  // open: Qn, preset, reset
  D_Flip_Flop d_ff_24 (.clk(clk), .D(signals_input[13]), .Q(CF1), .en(Write));  // open: Qn, preset, reset
  D_Flip_Flop d_ff_25 (.clk(clk), .D(signals_input[14]), .Q(CF2), .en(Write));  // open: Qn, preset, reset
  D_Flip_Flop d_ff_26 (.clk(clk), .D(signals_input[15]), .Q(F0), .en(Write));  // open: Qn, preset, reset
  D_Flip_Flop d_ff_27 (.clk(clk), .D(signals_input[16]), .Q(F1), .en(Write));  // open: Qn, preset, reset
  D_Flip_Flop d_ff_28 (.clk(clk), .D(signals_input[17]), .Q(F2), .en(Write));  // open: Qn, preset, reset
  D_Flip_Flop d_ff_29 (.clk(clk), .D(signals_input[18]), .Q(Accw), .en(Write));  // open: Qn, preset, reset
  D_Flip_Flop d_ff_30 (.clk(clk), .D(signals_input[19]), .Q(Xw), .en(Write));  // open: Qn, preset, reset
  D_Flip_Flop d_ff_31 (.clk(clk), .D(signals_input[20]), .Q(Yw), .en(Write));  // open: Qn, preset, reset
  D_Flip_Flop d_ff_32 (.clk(clk), .D(signals_input[21]), .Q(TMPw), .en(Write));  // open: Qn, preset, reset
  D_Flip_Flop d_ff_33 (.clk(clk), .D(signals_input[22]), .Q(SPw), .en(Write));  // open: Qn, preset, reset
  D_Flip_Flop d_ff_34 (.clk(clk), .D(signals_input[23]), .Q(PClw), .en(Write));  // open: Qn, preset, reset
  D_Flip_Flop d_ff_35 (.clk(clk), .D(signals_input[24]), .Q(PChw), .en(Write));  // open: Qn, preset, reset
  D_Flip_Flop d_ff_36 (.clk(clk), .D(signals_input[25]), .Q(IRw), .en(Write));  // open: Qn, preset, reset
  D_Flip_Flop d_ff_37 (.clk(clk), .D(signals_input[26]), .Q(ABw), .en(Write));  // open: Qn, preset, reset
  D_Flip_Flop d_ff_38 (.clk(clk), .D(signals_input[27]), .Q(OUTw), .en(Write));  // open: Qn, preset, reset
  D_Flip_Flop d_ff_39 (.clk(clk), .D(signals_input[28]), .Q(PC_plus_plus), .en(Write));  // open: Qn, preset, reset
  D_Flip_Flop d_ff_40 (.clk(clk), .D(signals_input[29]), .Q(R_W_), .en(Write));  // open: Qn, preset, reset
  D_Flip_Flop d_ff_41 (.clk(clk), .D(signals_input[30]), .Q(SYNC), .en(Write));  // open: Qn, preset, reset
  D_Flip_Flop d_ff_42 (.clk(clk), .D(signals_input[31]), .Q(d_ff_42_q), .en(Write));  // open: Qn, preset, reset
endmodule

// BC
module BC__Branch_Controller (
  input  negative,
  input  overflow,
  input  carry,
  input  zero,
  input  [7:0] OpCode,
  input  branch,
  output branch_2
);

  wire and_1_out, and_2_out, and_3_out, and_4_out, and_5_out, and_6_out, and_7_out, and_8_out, and_9_out,
       and_10_out, nand_1_out, or_1_out;

  nand nand_1 (nand_1_out, OpCode[1], OpCode[0]);
  and and_1 (and_1_out, OpCode[4], ~OpCode[3], ~OpCode[2]);  // AND_Gate
  and and_2 (and_2_out, ~OpCode[7], ~OpCode[6], ~OpCode[5], ~negative);  // AND_Gate
  and and_3 (and_3_out, negative, ~OpCode[7], ~OpCode[6], OpCode[5]);  // AND_Gate
  and and_4 (and_4_out, ~OpCode[7], OpCode[6], ~OpCode[5], ~overflow);  // AND_Gate
  and and_5 (and_5_out, overflow, ~OpCode[7], OpCode[6], OpCode[5]);  // AND_Gate
  and and_6 (and_6_out, OpCode[7], ~OpCode[6], ~OpCode[5], ~carry);  // AND_Gate
  and and_7 (and_7_out, carry, OpCode[7], ~OpCode[6], OpCode[5]);  // AND_Gate
  and and_8 (and_8_out, OpCode[7], OpCode[6], ~OpCode[5], ~zero);  // AND_Gate
  and and_9 (and_9_out, zero, OpCode[7], OpCode[6], OpCode[5]);
  and and_10 (and_10_out, and_1_out, nand_1_out);
  or or_1 (or_1_out, and_2_out, and_3_out, and_4_out, and_5_out, and_6_out, and_7_out, and_8_out, and_9_out);
  and and_11 (branch_2, or_1_out, and_10_out, branch);

  // Notes on the sheet:
  //   AAA
  //   Notes :
  //   BBB
  //   CC
  //   - Brunch instructions follow this format : ---.100.00
  //   BPL : AAA=000 and N=0
  //   BMI : AAA=001 and N=1
  //   BVC : AAA=010 and V=0
  //   BVS : AAA=011 and V=1
  //   BCC : AAA=100 and Z=0
  //   BCS : AAA=101 and Z=1
  //   BNE : AAA=110 and N=0
  //   BEQ : AAA=111 and N=1
  //   Bruch instructions : BBB=100 and CC=00
  //   - OpCode binary format (8 bits) is represented AAA.BBB.CC (- means 0 or 1)
endmodule

// Mapper
module Operation_Mapper (
  input  [7:0] OpCode,
  output [7:0] operation_address
);

  wire and_1_out, and_2_out, and_3_out, and_4_out, and_5_out, and_6_out, and_7_out, and_8_out, and_9_out,
       and_10_out, and_11_out, and_12_out, and_13_out, and_14_out, and_15_out, demux_1_2_1_bit_1_output_0,
       demux_1_2_1_bit_1_output_1, demux_1_2_1_bit_2_output_0, demux_1_2_1_bit_2_output_1,
       demux_1_2_1_bit_3_output_0, demux_1_2_1_bit_3_output_1, demux_1_2_1_bit_4_output_0,
       demux_1_2_1_bit_4_output_1, or_1_out;
  wire [3:0] encoder_16_4_1_bits_1_output_0;
  wire [7:0] rom_1_data, rom_2_data;

  and and_1 (and_1_out, ~OpCode[7], ~OpCode[6], ~OpCode[5], OpCode[0]);  // AND_Gate
  and and_2 (and_2_out, ~OpCode[7], ~OpCode[6], OpCode[5], OpCode[0]);  // AND_Gate
  and and_3 (and_3_out, ~OpCode[7], OpCode[6], ~OpCode[5], OpCode[0]);  // AND_Gate
  and and_4 (and_4_out, ~OpCode[7], OpCode[6], OpCode[5], OpCode[0]);  // AND_Gate
  and and_5 (and_5_out, OpCode[7], ~OpCode[6], ~OpCode[5], OpCode[0]);  // AND_Gate
  and and_6 (and_6_out, OpCode[7], ~OpCode[6], OpCode[5], OpCode[0]);  // AND_Gate
  and and_7 (and_7_out, OpCode[7], OpCode[6], ~OpCode[5], OpCode[0]);  // AND_Gate
  and and_8 (and_8_out, OpCode[7], OpCode[6], OpCode[5], OpCode[0]);
  and and_9 (and_9_out, ~OpCode[4], OpCode[3], ~OpCode[2]);  // AND_Gate
  and and_10 (and_10_out, ~OpCode[7], ~OpCode[6], ~OpCode[5], OpCode[1], ~OpCode[0]);  // AND_Gate
  and and_11 (and_11_out, ~OpCode[7], ~OpCode[6], OpCode[5], OpCode[1], ~OpCode[0]);  // AND_Gate
  and and_12 (and_12_out, ~OpCode[7], OpCode[6], ~OpCode[5], OpCode[1], ~OpCode[0]);  // AND_Gate
  and and_13 (and_13_out, ~OpCode[7], OpCode[6], OpCode[5], OpCode[1], ~OpCode[0]);  // AND_Gate
  Demux_1_2__1_bit demux_1_2_1_bit_1 (
    .Input(and_10_out), .Output_0(demux_1_2_1_bit_1_output_0), .Output_1(demux_1_2_1_bit_1_output_1),
    .Select(and_9_out));
  Demux_1_2__1_bit demux_1_2_1_bit_2 (
    .Input(and_11_out), .Output_0(demux_1_2_1_bit_2_output_0), .Output_1(demux_1_2_1_bit_2_output_1),
    .Select(and_9_out));
  Demux_1_2__1_bit demux_1_2_1_bit_3 (
    .Input(and_12_out), .Output_0(demux_1_2_1_bit_3_output_0), .Output_1(demux_1_2_1_bit_3_output_1),
    .Select(and_9_out));
  Demux_1_2__1_bit demux_1_2_1_bit_4 (
    .Input(and_13_out), .Output_0(demux_1_2_1_bit_4_output_0), .Output_1(demux_1_2_1_bit_4_output_1),
    .Select(and_9_out));
  Encoder_16_4__1_bits encoder_16_4_1_bits_1 (
    .input_0(and_1_out), .input_1(and_2_out), .input_2(and_3_out), .input_3(and_4_out), .input_4(and_5_out),
    .input_5(and_6_out), .input_6(and_7_out), .input_7(and_8_out), .input_8(demux_1_2_1_bit_1_output_0),
    .input_9(demux_1_2_1_bit_1_output_1), .input_10(demux_1_2_1_bit_2_output_0),
    .input_11(demux_1_2_1_bit_2_output_1), .input_12(demux_1_2_1_bit_3_output_0),
    .input_13(demux_1_2_1_bit_3_output_1), .input_14(demux_1_2_1_bit_4_output_0),
    .input_15(demux_1_2_1_bit_4_output_1), .output_3(encoder_16_4_1_bits_1_output_0[3]),
    .output_2(encoder_16_4_1_bits_1_output_0[2]), .output_1(encoder_16_4_1_bits_1_output_0[1]),
    .output_0(encoder_16_4_1_bits_1_output_0[0]));  // open: active
  and and_14 (and_14_out, OpCode[0], ~OpCode[1]);  // AND_Gate
  or or_1 (or_1_out, and_14_out, and_15_out);
  and and_15 (and_15_out, ~OpCode[0], OpCode[1], ~OpCode[7]);  // AND_Gate
  ROM #(.addrWidth(7)) rom_1 (.addr(OpCode[7:1]), .data(rom_1_data));  // open: sel
  ROM #(.addrWidth(4)) rom_2 (.addr(encoder_16_4_1_bits_1_output_0), .data(rom_2_data));  // open: sel
  Mux_2_1__8_bits mux_2_1_8_bits_1 (
    .Input_0(rom_1_data), .Input_1(rom_2_data), .Output(operation_address), .Select(or_1_out));

  // Notes on the sheet:
  //   BBB
  //   AAA
  //   BBB
  //   AAA
  //   CC
  //   CC
  //   ORA
  //   AND
  //   EOR
  //   ADC
  //   STA
  //   LDA
  //   CMP
  //   SBC
  //   (B=2) => Acc
  //   ASL
  //   ROL
  //   LSR
  //   ROR
  //   Mem
  //   Acc
  //   Mem
  //   Acc
  //   Mem
  //   Acc
  //   Mem
  //   Acc
  //   AAA
  //   BBB
  //   CC
  //   Notes :
  //   opc = ---.---.-0
  //   Instructions Operation
  //   Address Table (grp0)
  //   Instructions Operation
  //   Address Table (grp1)
  //   ---.---.01 or 0--.---.10
  //   contents of rom_1 (hex, n*v repeats v):
  //   e 0 0 0 9d 7*0 96 0 0 0 a1 0 9f 0 98 0 9f 5*0 97 0 0 0 b1 0 0 0 9b 0 8f 5*0 94 0 0 0 aa 0 0 0 89 0
  //   8c 5*0 95 5*0 85 69 87 6b 85 69 0 0 85 69 88 6c 0 0 82 6d 82 6d 83 6e 82 6d 0 0 82 6d 84 6f 82 6d 7c
  //   0 7c 70 80 72 7c 70 0 0 0 70 81 0 0 70 76 0 76 73 7a 75 76 73 0 0 0 73 7b 0 0 73
  //   contents of rom_2 (hex, n*v repeats v):
  //   50 51 52 53 54 56 57 58 59 5b 5d 5f 61 63 65 67
  //   - Separating instructions in 2 groups helps optimization.
  //   instructions with 8 addressing modes :
  //   - OpCode binary format (8 bits) is represented AAA.BBB.CC (- means 0 or 1)
  //   - The instructions ORA, AND, EOR, ADC, STA, LDA CMP, SBC, ASL, ROL,
  //    LSR, ROR are special, they use 8 different addressing modes.
  //   - Instructions with 8 different addressing modes are like : AAA.---.CC
  //   Choose between instructions with 8
  //    addressing modes and others with less
  //   Notes :
  //   - JMP indirect (100.011.00) is included within absolute mode
  //   - OpCode binary format (8 bits) is represented AAA.BBB.CC (- means 0 or 1)
  //   - Accumulator addressing mode (0--.010.10) is included within implied mode
  //   - special instructions (BRK,JSR,RTI,RTS) are traited after as implied instructions
endmodule

// Mapper
module Address_Mode_Mapper (
  input  [7:0] OpCode,
  output [7:0] Control_Address
);

  wire and_1_out, and_2_out, and_3_out, and_4_out, and_5_out, and_6_out, and_7_out, and_8_out, and_9_out,
       and_10_out, and_11_out, and_12_out, and_13_out, and_14_out, and_15_out, and_16_out, and_17_out,
       and_18_out, or_1_out, or_2_out, or_3_out;
  wire [3:0] encoder_16_4_1_bits_1_output_0;

  and and_1 (and_1_out, OpCode[3], ~OpCode[2], ~OpCode[0]);  // AND_Gate
  and and_2 (and_2_out, OpCode[7], ~OpCode[4], ~OpCode[3], ~OpCode[2], ~OpCode[0]);  // AND_Gate
  and and_3 (and_3_out, ~OpCode[4], OpCode[3], ~OpCode[2], OpCode[0]);  // AND_Gate
  and and_4 (and_4_out, ~OpCode[4], ~OpCode[3], OpCode[2]);  // AND_Gate
  and and_5 (and_5_out, OpCode[4], ~OpCode[3], OpCode[2]);  // AND_Gate
  and and_6 (and_6_out, OpCode[7], ~OpCode[6], OpCode[4], ~OpCode[3], OpCode[2], OpCode[1]);  // AND_Gate
  and and_7 (and_7_out, ~OpCode[4], ~OpCode[3], ~OpCode[2], OpCode[0]);  // AND_Gate
  and and_8 (and_8_out, OpCode[4], ~OpCode[3], ~OpCode[2], OpCode[0]);  // AND_Gate
  and and_9 (and_9_out, OpCode[4], ~OpCode[3], ~OpCode[2], ~OpCode[0]);  // AND_Gate
  and and_10 (and_10_out, ~OpCode[4], OpCode[3], OpCode[2]);  // AND_Gate
  and and_11 (and_11_out, OpCode[4], OpCode[3], OpCode[2]);
  and and_12 (and_12_out, OpCode[7], ~OpCode[6], OpCode[4], OpCode[3], OpCode[2], OpCode[1]);  // AND_Gate
  and and_13 (and_13_out, OpCode[4], OpCode[3], ~OpCode[2], OpCode[0]);  // AND_Gate
  and and_14 (and_14_out, ~OpCode[7], ~OpCode[4], ~OpCode[3], ~OpCode[2], ~OpCode[0]);  // AND_Gate
  and and_15 (and_15_out, ~OpCode[7], OpCode[6], ~OpCode[5], ~OpCode[4], OpCode[3], OpCode[2], ~OpCode[1], ~OpCode[0]);  // AND_Gate
  or or_1 (or_1_out, and_2_out, and_3_out);
  and and_16 (and_16_out, and_5_out, ~and_6_out);  // AND_Gate
  and and_17 (and_17_out, and_10_out, ~and_15_out);  // AND_Gate
  and and_18 (and_18_out, and_11_out, ~and_12_out);  // AND_Gate
  or or_2 (or_2_out, and_12_out, and_13_out);
  or or_3 (or_3_out, and_14_out, and_15_out);
  Encoder_16_4__1_bits encoder_16_4_1_bits_1 (
    .input_0(and_1_out), .input_1(or_1_out), .input_2(and_4_out), .input_3(and_16_out), .input_4(and_6_out),
    .input_5(and_7_out), .input_6(and_8_out), .input_7(and_9_out), .input_8(and_17_out),
    .input_9(and_18_out), .input_10(or_2_out), .input_11(or_3_out), .input_12(1'b0), .input_13(1'b0),
    .input_14(1'b0), .input_15(1'b0), .output_3(encoder_16_4_1_bits_1_output_0[3]),
    .output_2(encoder_16_4_1_bits_1_output_0[2]), .output_1(encoder_16_4_1_bits_1_output_0[1]),
    .output_0(encoder_16_4_1_bits_1_output_0[0]));  // open: active
  ROM #(.addrWidth(4)) rom_1 (.addr(encoder_16_4_1_bits_1_output_0), .data(Control_Address));  // open: sel

  // Notes on the sheet:
  //   BBB
  //   AAA
  //   BBB
  //   AAA
  //   CC
  //   CC
  //   Notes :
  //   zero page,X : ---.101.-- 
  //   implied : ---.-10.-0
  //   zero page : ---.001.--
  //   X,indirect : ---.000.-1
  //   indirect,Y : ---.100.-1
  //   relative : ---.100.-0
  //   absolute : ---.011.--
  //   absolute,X : ---.111.--
  //   LDX abs,Y : 10-.111.1-
  //   absolute,Y : ---.110.-1
  //   JMP abs : 010.011.00
  //   - JMP indirect (100.011.00) is included within absolute mode
  //   immediate : 1--.000.-0 or ---.010.-1
  //   - JMP abs is distinct from others, thus it is treated like special instruction
  //   zero page,Y : 10-.101.1- (STX zpg,Y and LDX zpg,Y)
  //   special instructions : 0--.000.-0 (BRK,JSR,RTI,RTS)
  //   - OpCode binary format (8 bits) is represented AAA.BBB.CC (- means 0 or 1)
  //   - Accumulator addressing mode (0--.010.10) is included within implied mode
  //   - special instructions (BRK,JSR,RTI,RTS) are traited later as implied instructions
  //   excluding STX zpg,Y and LDX zpg,Y
  //   excluding JMP abs
  //   excluding LDX abs,Y
  //   Addressing Mode
  //   Address Table
  //   contents of rom_1 (hex, n*v repeats v):
  //   14 15 16 19 1d 38 40 21 25 2a 31 14
endmodule

// Adder
module Adder__8_bits (
  input  Cin,
  input  [7:0] A,
  input  [7:0] B,
  output [7:0] S,
  output overflow,
  output Cout
);

  wire full_adder_1_cout, full_adder_2_cout, full_adder_3_cout, full_adder_4_cout, full_adder_5_cout,
       full_adder_6_cout, full_adder_7_cout;

  Full_Adder full_adder_1 (.A(A[0]), .B(B[0]), .S(S[0]), .Cin(Cin), .Cout(full_adder_1_cout));
  Full_Adder full_adder_2 (.A(A[1]), .B(B[1]), .S(S[1]), .Cin(full_adder_1_cout), .Cout(full_adder_2_cout));
  Full_Adder full_adder_3 (.A(A[2]), .B(B[2]), .S(S[2]), .Cin(full_adder_2_cout), .Cout(full_adder_3_cout));
  Full_Adder full_adder_4 (.A(A[3]), .B(B[3]), .S(S[3]), .Cin(full_adder_3_cout), .Cout(full_adder_4_cout));
  Full_Adder full_adder_5 (.A(A[4]), .B(B[4]), .S(S[4]), .Cin(full_adder_4_cout), .Cout(full_adder_5_cout));
  Full_Adder full_adder_6 (.A(A[5]), .B(B[5]), .S(S[5]), .Cin(full_adder_5_cout), .Cout(full_adder_6_cout));
  Full_Adder full_adder_7 (.A(A[6]), .B(B[6]), .S(S[6]), .Cin(full_adder_6_cout), .Cout(full_adder_7_cout));
  Full_Adder full_adder_8 (.A(A[7]), .B(B[7]), .S(S[7]), .Cin(full_adder_7_cout), .Cout(Cout));
  xor xor_1 (overflow, full_adder_7_cout, Cout);
endmodule

module Full_Adder (
  input  Cin,
  input  A,
  input  B,
  output S,
  output Cout
);

  wire and_1_out, and_2_out, and_3_out;

  xor xor_1 (S, A, B, Cin);
  and and_1 (and_1_out, A, B);
  and and_2 (and_2_out, A, Cin);
  and and_3 (and_3_out, B, Cin);
  or or_1 (Cout, and_1_out, and_2_out, and_3_out);
endmodule

// >>
module Shift_1_bit_right__8_bits (
  input  [7:0] Input,
  input  Cin,
  output Cout,
  output [7:0] Output
);


  assign Cout = Input[0];
  assign Output = {Cin, Input[7:1]};
endmodule

// Shifter
module Serial_to_Parallel_Shifter__8_bits (
  input  clk,
  input  reset,
  input  Input,
  output Output_0,
  output Output_1,
  output Output_2,
  output Output_3,
  output Output_4,
  output Output_5,
  output Output_6,
  output Output_7
);

  D_Flip_Flop d_ff_1 (.clk(clk), .D(Input), .Q(Output_0), .reset(reset));  // open: Qn, preset, en
  D_Flip_Flop d_ff_2 (.clk(clk), .D(Output_1), .Q(Output_2), .reset(reset));  // open: Qn, preset, en
  D_Flip_Flop d_ff_3 (.clk(clk), .D(Output_0), .Q(Output_1), .reset(reset));  // open: Qn, preset, en
  D_Flip_Flop d_ff_4 (.clk(clk), .D(Output_2), .Q(Output_3), .reset(reset));  // open: Qn, preset, en
  D_Flip_Flop d_ff_5 (.clk(clk), .D(Output_3), .Q(Output_4), .reset(reset));  // open: Qn, preset, en
  D_Flip_Flop d_ff_6 (.clk(clk), .D(Output_4), .Q(Output_5), .reset(reset));  // open: Qn, preset, en
  D_Flip_Flop d_ff_7 (.clk(clk), .D(Output_5), .Q(Output_6), .reset(reset));  // open: Qn, preset, en
  D_Flip_Flop d_ff_8 (.clk(clk), .D(Output_6), .Q(Output_7), .reset(reset));  // open: Qn, preset, en
endmodule

// Mux 2-1
module Mux_2_1__1_bit (
  input  Select,
  input  Input_0,
  input  Input_1,
  output Output
);

  wire and_1_out, and_2_out, not_1_out;

  not not_1 (not_1_out, Select);
  and and_1 (and_1_out, not_1_out, Input_0);
  and and_2 (and_2_out, Select, Input_1);
  or or_1 (Output, and_1_out, and_2_out);
endmodule

// Mux 2-1
module Mux_2_1__8_bits (
  input  Select,
  input  [7:0] Input_0,
  input  [7:0] Input_1,
  output [7:0] Output
);

  wire [7:0] and_1_out, and_2_out;
  wire [7:7] not_1_out;

  not not_1 (not_1_out[7], Select);
  assign and_1_out = {8{not_1_out[7]}} & Input_0;  // AND_Gate and_1, 8 bits wide
  assign and_2_out = {8{Select}} & Input_1;  // AND_Gate and_2, 8 bits wide
  assign Output = and_1_out | and_2_out;  // OR_Gate or_1, 8 bits wide
endmodule

// Mux 4-1
module Mux_4_1__1_bit (
  input  Select_0,
  input  Select_1,
  input  Input_0,
  input  Input_1,
  input  Input_2,
  input  Input_3,
  output Output
);

  wire mux_2_1_1_bit_1_output, mux_2_1_1_bit_2_output;

  Mux_2_1__1_bit mux_2_1_1_bit_1 (
    .Input_0(Input_0), .Input_1(Input_1), .Output(mux_2_1_1_bit_1_output), .Select(Select_0));
  Mux_2_1__1_bit mux_2_1_1_bit_2 (
    .Input_0(Input_2), .Input_1(Input_3), .Output(mux_2_1_1_bit_2_output), .Select(Select_0));
  Mux_2_1__1_bit mux_2_1_1_bit_3 (
    .Input_0(mux_2_1_1_bit_1_output), .Input_1(mux_2_1_1_bit_2_output), .Output(Output), .Select(Select_1));
endmodule

// Mux 4-1
module Mux_4_1__8_bits (
  input  Select_0,
  input  Select_1,
  input  [7:0] Input_0,
  input  [7:0] Input_1,
  input  [7:0] Input_2,
  input  [7:0] Input_3,
  output [7:0] Output
);

  wire [7:0] mux_2_1_8_bits_1_output, mux_2_1_8_bits_2_output;

  Mux_2_1__8_bits mux_2_1_8_bits_1 (
    .Input_0(Input_0), .Input_1(Input_1), .Output(mux_2_1_8_bits_1_output), .Select(Select_0));
  Mux_2_1__8_bits mux_2_1_8_bits_2 (
    .Input_0(Input_2), .Input_1(Input_3), .Output(mux_2_1_8_bits_2_output), .Select(Select_0));
  Mux_2_1__8_bits mux_2_1_8_bits_3 (
    .Input_0(mux_2_1_8_bits_1_output), .Input_1(mux_2_1_8_bits_2_output), .Output(Output), .Select(Select_1));
endmodule
// Mux 8-1
module Mux_8_1__1_bit (
  input  Select_0,
  input  Select_1,
  input  Select_2,
  input  Input_0,
  input  Input_1,
  input  Input_2,
  input  Input_3,
  input  Input_4,
  input  Input_5,
  input  Input_6,
  input  Input_7,
  output Output
);

  wire mux_2_1_1_bit_1_output, mux_2_1_1_bit_2_output, mux_2_1_1_bit_3_output, mux_2_1_1_bit_4_output,
       mux_2_1_1_bit_5_output, mux_2_1_1_bit_6_output;

  Mux_2_1__1_bit mux_2_1_1_bit_1 (
    .Input_0(Input_0), .Input_1(Input_1), .Output(mux_2_1_1_bit_1_output), .Select(Select_0));
  Mux_2_1__1_bit mux_2_1_1_bit_2 (
    .Input_0(Input_2), .Input_1(Input_3), .Output(mux_2_1_1_bit_2_output), .Select(Select_0));
  Mux_2_1__1_bit mux_2_1_1_bit_3 (
    .Input_0(Input_4), .Input_1(Input_5), .Output(mux_2_1_1_bit_3_output), .Select(Select_0));
  Mux_2_1__1_bit mux_2_1_1_bit_4 (
    .Input_0(Input_6), .Input_1(Input_7), .Output(mux_2_1_1_bit_4_output), .Select(Select_0));
  Mux_2_1__1_bit mux_2_1_1_bit_5 (
    .Input_0(mux_2_1_1_bit_1_output), .Input_1(mux_2_1_1_bit_2_output), .Output(mux_2_1_1_bit_5_output),
    .Select(Select_1));
  Mux_2_1__1_bit mux_2_1_1_bit_6 (
    .Input_0(mux_2_1_1_bit_3_output), .Input_1(mux_2_1_1_bit_4_output), .Output(mux_2_1_1_bit_6_output),
    .Select(Select_1));
  Mux_2_1__1_bit mux_2_1_1_bit_7 (
    .Input_0(mux_2_1_1_bit_5_output), .Input_1(mux_2_1_1_bit_6_output), .Output(Output), .Select(Select_2));
endmodule

// Mux 8-1
module Mux_8_1__8_bits (
  input  Select_0,
  input  Select_1,
  input  Select_2,
  input  [7:0] Input_0,
  input  [7:0] Input_1,
  input  [7:0] Input_2,
  input  [7:0] Input_3,
  input  [7:0] Input_4,
  input  [7:0] Input_5,
  input  [7:0] Input_6,
  input  [7:0] Input_7,
  output [7:0] Output
);

  wire [7:0] mux_2_1_8_bits_1_output, mux_2_1_8_bits_2_output, mux_2_1_8_bits_3_output,
       mux_2_1_8_bits_4_output, mux_2_1_8_bits_5_output, mux_2_1_8_bits_6_output;

  Mux_2_1__8_bits mux_2_1_8_bits_1 (
    .Input_0(Input_0), .Input_1(Input_1), .Output(mux_2_1_8_bits_1_output), .Select(Select_0));
  Mux_2_1__8_bits mux_2_1_8_bits_2 (
    .Input_0(Input_2), .Input_1(Input_3), .Output(mux_2_1_8_bits_2_output), .Select(Select_0));
  Mux_2_1__8_bits mux_2_1_8_bits_3 (
    .Input_0(Input_4), .Input_1(Input_5), .Output(mux_2_1_8_bits_3_output), .Select(Select_0));
  Mux_2_1__8_bits mux_2_1_8_bits_4 (
    .Input_0(Input_6), .Input_1(Input_7), .Output(mux_2_1_8_bits_4_output), .Select(Select_0));
  Mux_2_1__8_bits mux_2_1_8_bits_5 (
    .Input_0(mux_2_1_8_bits_1_output), .Input_1(mux_2_1_8_bits_2_output), .Output(mux_2_1_8_bits_5_output),
    .Select(Select_1));
  Mux_2_1__8_bits mux_2_1_8_bits_6 (
    .Input_0(mux_2_1_8_bits_3_output), .Input_1(mux_2_1_8_bits_4_output), .Output(mux_2_1_8_bits_6_output),
    .Select(Select_1));
  Mux_2_1__8_bits mux_2_1_8_bits_7 (
    .Input_0(mux_2_1_8_bits_5_output), .Input_1(mux_2_1_8_bits_6_output), .Output(Output), .Select(Select_2));
endmodule

// Demux
module Demux_1_2__1_bit (
  input  Select,
  input  Input,
  output Output_0,
  output Output_1
);

  wire not_1_out;

  not not_1 (not_1_out, Select);
  and and_1 (Output_0, not_1_out, Input);
  and and_2 (Output_1, Select, Input);
endmodule

// Decoder 3-8
module Decoder_3_8__1_bit (
  input  Input_2,
  input  Input_1,
  input  Input_0,
  output output_0,
  output output_1,
  output output_2,
  output output_3,
  output output_4,
  output output_5,
  output output_6,
  output output_7
);

  wire not_1_out, not_2_out, not_3_out;

  not not_1 (not_1_out, Input_2);
  not not_2 (not_2_out, Input_1);
  not not_3 (not_3_out, Input_0);
  and and_1 (output_0, not_3_out, not_2_out, not_1_out);
  and and_2 (output_1, Input_0, not_2_out, not_1_out);
  and and_3 (output_2, not_3_out, Input_1, not_1_out);
  and and_4 (output_3, Input_0, Input_1, not_1_out);
  and and_5 (output_4, not_3_out, not_2_out, Input_2);
  and and_6 (output_5, Input_0, not_2_out, Input_2);
  and and_7 (output_6, not_3_out, Input_1, Input_2);
  and and_8 (output_7, Input_0, Input_1, Input_2);
endmodule

// Encoder 4-2
module Encoder_4_2__1_bit (
  input  input_0,
  input  input_1,
  input  input_2,
  input  input_3,
  output output_1,
  output output_0,
  output active
);

  wire or_2_out, or_3_out;

  or or_1 (active, input_0, input_1, input_2, input_3);
  or or_2 (or_2_out, input_2, input_3);
  or or_3 (or_3_out, input_1, input_3);
  assign output_1 = active ? or_2_out : 1'bz;  // Controlled_Buffer controlled_buffer_1
  assign output_0 = active ? or_3_out : 1'bz;  // Controlled_Buffer controlled_buffer_2
endmodule

// Encoder 16-4
module Encoder_16_4__1_bits (
  input  input_0,
  input  input_1,
  input  input_2,
  input  input_3,
  input  input_4,
  input  input_5,
  input  input_6,
  input  input_7,
  input  input_8,
  input  input_9,
  input  input_10,
  input  input_11,
  input  input_12,
  input  input_13,
  input  input_14,
  input  input_15,
  output output_3,
  output output_2,
  output output_1,
  output output_0,
  output active
);

  wire encoder_4_2_1_bit_1_active, encoder_4_2_1_bit_1_output_0, encoder_4_2_1_bit_1_output_1,
       encoder_4_2_1_bit_2_active, encoder_4_2_1_bit_3_active, encoder_4_2_1_bit_4_active,
       encoder_4_2_1_bit_5_output_0, encoder_4_2_1_bit_5_output_1;

  Encoder_4_2__1_bit encoder_4_2_1_bit_1 (
    .input_0(input_4), .input_1(input_5), .input_2(input_6), .input_3(input_7),
    .output_1(encoder_4_2_1_bit_1_output_1), .output_0(encoder_4_2_1_bit_1_output_0),
    .active(encoder_4_2_1_bit_1_active));
  Encoder_4_2__1_bit encoder_4_2_1_bit_2 (
    .input_0(input_8), .input_1(input_9), .input_2(input_10), .input_3(input_11),
    .output_1(encoder_4_2_1_bit_1_output_1), .output_0(encoder_4_2_1_bit_1_output_0),
    .active(encoder_4_2_1_bit_2_active));
  Encoder_4_2__1_bit encoder_4_2_1_bit_3 (
    .input_0(input_12), .input_1(input_13), .input_2(input_14), .input_3(input_15),
    .output_1(encoder_4_2_1_bit_1_output_1), .output_0(encoder_4_2_1_bit_1_output_0),
    .active(encoder_4_2_1_bit_3_active));
  or or_1 (active, encoder_4_2_1_bit_3_active, encoder_4_2_1_bit_2_active, encoder_4_2_1_bit_1_active, encoder_4_2_1_bit_4_active);
  Encoder_4_2__1_bit encoder_4_2_1_bit_4 (
    .input_0(input_0), .input_1(input_1), .input_2(input_2), .input_3(input_3),
    .output_1(encoder_4_2_1_bit_1_output_1), .output_0(encoder_4_2_1_bit_1_output_0),
    .active(encoder_4_2_1_bit_4_active));
  Encoder_4_2__1_bit encoder_4_2_1_bit_5 (
    .input_0(encoder_4_2_1_bit_4_active), .input_1(encoder_4_2_1_bit_1_active),
    .input_2(encoder_4_2_1_bit_2_active), .input_3(encoder_4_2_1_bit_3_active),
    .output_1(encoder_4_2_1_bit_5_output_1), .output_0(encoder_4_2_1_bit_5_output_0));  // open: active
  assign output_3 = active ? encoder_4_2_1_bit_5_output_1 : 1'bz;  // Controlled_Buffer controlled_buffer_1
  assign output_2 = active ? encoder_4_2_1_bit_5_output_0 : 1'bz;  // Controlled_Buffer controlled_buffer_2
  assign output_1 = active ? encoder_4_2_1_bit_1_output_1 : 1'bz;  // Controlled_Buffer controlled_buffer_3
  assign output_0 = active ? encoder_4_2_1_bit_1_output_0 : 1'bz;  // Controlled_Buffer controlled_buffer_4
endmodule

module Rising_Eadge_Detector (
  input  clk,
  input  \input ,
  output \output 
);

  wire and_1_out, d_ff_1_q;

  and and_1 (and_1_out, \input , ~d_ff_1_q);  // AND_Gate
  D_Flip_Flop d_ff_1 (.clk(clk), .D(\input ), .Q(d_ff_1_q));  // open: Qn, preset, en, reset
  D_Flip_Flop d_ff_2 (.clk(clk), .D(and_1_out), .Q(\output ));  // open: Qn, preset, en, reset
endmodule
