// Logisim project Simplistic 6502 architecture.circ as structural Verilog: 41 circuits, main circuit 6502 + RAM + ROM
module _6502___RAM___ROM (
);

  wire clock_1_out, ls6502_logisim_6502_cpu_1_address_bus_15, ls6502_logisim_6502_cpu_1_r_w_, not_1_out,
       not_2_out;
  wire [7:0] controlled_buffer_1_out, ls6502_logisim_6502_cpu_1_data_output;
  wire [14:0] ls6502_logisim_6502_cpu_1_address_bus_0;

  not not_1 (not_1_out, ls6502_logisim_6502_cpu_1_r_w_);
  assign controlled_buffer_1_out = not_1_out ? ls6502_logisim_6502_cpu_1_data_output : 8'bz;  // Controlled_Buffer controlled_buffer_1
  LS6502__Logisim_6502_cpu ls6502_logisim_6502_cpu_1 (
    .R_W_(ls6502_logisim_6502_cpu_1_r_w_), .PHI0(clock_1_out),
    .Address_Bus_0(ls6502_logisim_6502_cpu_1_address_bus_0[0]),
    .Address_Bus_1(ls6502_logisim_6502_cpu_1_address_bus_0[1]),
    .Address_Bus_2(ls6502_logisim_6502_cpu_1_address_bus_0[2]),
    .Address_Bus_3(ls6502_logisim_6502_cpu_1_address_bus_0[3]),
    .Address_Bus_4(ls6502_logisim_6502_cpu_1_address_bus_0[4]),
    .Address_Bus_5(ls6502_logisim_6502_cpu_1_address_bus_0[5]),
    .Address_Bus_6(ls6502_logisim_6502_cpu_1_address_bus_0[6]),
    .Address_Bus_7(ls6502_logisim_6502_cpu_1_address_bus_0[7]),
    .Address_Bus_8(ls6502_logisim_6502_cpu_1_address_bus_0[8]),
    .Address_Bus_9(ls6502_logisim_6502_cpu_1_address_bus_0[9]),
    .Address_Bus_10(ls6502_logisim_6502_cpu_1_address_bus_0[10]),
    .Address_Bus_11(ls6502_logisim_6502_cpu_1_address_bus_0[11]),
    .Address_Bus_12(ls6502_logisim_6502_cpu_1_address_bus_0[12]),
    .Address_Bus_13(ls6502_logisim_6502_cpu_1_address_bus_0[13]),
    .Address_Bus_14(ls6502_logisim_6502_cpu_1_address_bus_0[14]),
    .Address_Bus_15(ls6502_logisim_6502_cpu_1_address_bus_15), .Data_input(controlled_buffer_1_out),
    .Data_output(ls6502_logisim_6502_cpu_1_data_output));  // open: RDY_, RST_, NMI_, IRQ_, BE, SO_, SYNC, PHI1, PHI2, VSS, N_C, VSS_2, VCC, N_C_2
  Clock clock_1 (.out(clock_1_out));
  not not_2 (not_2_out, ls6502_logisim_6502_cpu_1_address_bus_15);
  RAM #(.addrWidth(15), .bus("asynch")) ram_1 (
    .addr(ls6502_logisim_6502_cpu_1_address_bus_0), .data(controlled_buffer_1_out), .sel(not_2_out),
    .ld(ls6502_logisim_6502_cpu_1_r_w_));  // open: clr
  ROM #(.addrWidth(15)) rom_1 (
    .addr(ls6502_logisim_6502_cpu_1_address_bus_0), .data(controlled_buffer_1_out),
    .sel(ls6502_logisim_6502_cpu_1_address_bus_15));

  // Notes on the sheet:
  //   their ROMs.
  //   This simplistic architecture around the Logisim 6502 cpu(LS6502)
  //   contains by default Klaus Dormann 6502 Benchmark, you should
  //   manually before executing it, put the address $8000 internally
  //   in the PC register (PC-hi and PC-lo), and the value $10 in CAR
  //   register under CU circuit. Others examples like Factorial and
  //   Fibonacci should work directly without modification by loading
  //   Vss
  //   RDY
  //   PHI1
  //   IRQ\
  //   N.C.
  //   NMI\
  //   SYNC
  //   Vcc
  //   AB0
  //   AB1
  //   AB2
  //   AB3
  //   AB4
  //   AB5
  //   AB6
  //   AB7
  //   AB8
  //   AB9
  //   AB10
  //   AB11
  //   RST\
  //   R/W_
  //   AB15
  //   AB14
  //   AB13
  //   AB12
  //   PHI2
  //   SO
  //   PHI0
  //   BE
  //   N.C.
  //   DB0
  //   DB1
  //   DB2
  //   DB3
  //   DB4
  //   DB5
  //   DB6
  //   DB7
  //   Vss
  //   RAM
  //   32 Ko ($0000-$7FFF)
  //   contents of rom_1 (hex, n*v repeats v):
  //   d8 a2 ff 9a a9 0 8d 0 2 a2 5 4c 33 80 a0 5 d0 8 4c 12 80 10*88 f0 17 4c 21 80 10*ca f0 de 4c 30 80
  //   d0 f4 4c 35 80 ad 0 2 c9 0 d0 fe a9 1 8d 0 2 ad 0 2 c9 1 d0 fe a9 2 8d 0 2 c0 1 d0 3 4c 54 80 a9 0
  //   c9 0 d0 fe 90 fe 30 fe c9 1 f0 fe b0 fe 10 fe aa e0 0 d0 fe 90 fe 30 fe e0 1 f0 fe b0 fe 10 fe a8 c0
  //   0 d0 fe 90 fe 30 fe c0 1 f0 fe b0 fe 10 fe ad 0 2 c9 2 d0 fe a9 3 8d 0 2 a2 ff 9a a9 55 48 a9 aa 48
  //   cd fe 1 d0 fe ba 8a c9 fd d0 fe 68 c9 aa d0 fe 68 c9 55 d0 fe cd ff 1 d0 fe ba e0 ff d0 fe ad 0 2 c9
  //   3 d0 fe a9 4 8d 0 2 a9 ff 29 ef 48 28 10 1a 50 1b 90 1c d0 1d 30 3 4c db 80 70 3 4c e0 80 b0 3 4c e5
  //   80 f0 f 4c ea 80 4c ed 80 4c f0 80 4c f3 80 4c f6 80 8 ba e0 fe d0 fe 68 9 8 c9 ef d0 fe ba e0 ff d0
  //   fe a9 0 29 ef 48 28 30 1a 70 1b b0 1c f0 1d 10 3 4c 1b 81 50 3 4c 20 81 90 3 4c 25 81 d0 f 4c 2a 81
  //   4c 2d 81 4c 30 81 4c 33 81 4c 36 81 8 68 9 8 c9 28 d0 fe a9 2 29 ef 48 28 d0 2 f0 3 4c 4b 81 b0 2 90
  //   3 4c 52 81 30 2 10 3 4c 59 81 70 2 50 3 4c 60 81 a9 1 29 ef 48 28 f0 2 d0 3 4c 6d 81 90 2 b0 3 4c 74
  //   81 30 2 10 3 4c 7b 81 70 2 50 3 4c 82 81 a9 80 29 ef 48 28 f0 2 d0 3 4c 8f 81 b0 2 90 3 4c 96 81 10
  //   2 30 3 4c 9d 81 70 2 50 3 4c a4 81 a9 40 29 ef 48 28 f0 2 d0 3 4c b1 81 b0 2 90 3 4c b8 81 30 2 10 3
  //   4c bf 81 50 2 70 3 4c c6 81 a9 fd 29 ef 48 28 f0 2 d0 3 4c d3 81 90 2 b0 3 4c da 81 10 2 30 3 4c e1
  //   81 50 2 70 3 4c e8 81 a9 fe 29 ef 48 28 d0 2 f0 3 4c f5 81 b0 2 90 3 4c fc 81 10 2 30 3 4c 3 82 50 2
  //   70 3 4c a 82 a9 7f 29 ef 48 28 d0 2 f0 3 4c 17 82 90 2 b0 3 4c 1e 82 30 2 10 3 4c 25 82 50 2 70 3 4c
  //   2c 82 a9 bf 29 ef 48 28 d0 2 f0 3 4c 39 82 90 2 b0 3 4c 40 82 10 2 30 3 4c 47 82 70 2 50 3 4c 4e 82
  //   ad 0 2 c9 4 d0 fe a9 5 8d 0 2 a2 55 a0 aa a9 ff 29 ef 48 a9 1 28 48 8 c9 1 d0 fe 68 48 9 8 c9 ef d0
  //   fe 28 a9 0 29 ef 48 a9 0 28 48 8 c9 0 d0 fe 68 48 9 8 c9 28 d0 fe 28 a9 ff 29 ef 48 a9 ff 28 48 8 c9
  //   ff d0 fe 68 48 9 8 c9 ef d0 fe 28 a9 0 29 ef 48 a9 1 28 48 8 c9 1 d0 fe 68 48 9 8 c9 28 d0 fe 28 a9
  //   ff 29 ef 48 a9 0 28 48 8 c9 0 d0 fe 68 48 9 8 c9 ef d0 fe 28 a9 0 29 ef 48 a9 ff 28 48 8 c9 ff d0 fe
  //   68 48 9 8 c9 28 d0 fe 28 a9 ff 29 ef 48 a9 0 28 68 8 c9 ff d0 fe 68 48 9 8 c9 ed d0 fe 28 a9 0 29 ef
  //   48 a9 ff 28 68 8 c9 0 d0 fe 68 48 9 8 c9 2a d0 fe 28 a9 ff 29 ef 48 a9 fe 28 68 8 c9 1 d0 fe 68 48 9
  //   8 c9 6d d0 fe 28 a9 0 29 ef 48 a9 0 28 68 8 c9 ff d0 fe 68 48 9 8 c9 a8 d0 fe 28 a9 ff 29 ef 48 a9
  //   ff 28 68 8 c9 0 d0 fe 68 48 9 8 c9 6f d0 fe 28 a9 0 29 ef 48 a9 fe 28 68 8 c9 1 d0 fe 68 48 9 8 c9
  //   28 d0 fe 28 e0 55 d0 fe c0 aa d0 fe ad 0 2 c9 5 d0 fe a9 6 8d 0 2 a9 0 29 ef 48 a9 3c 28 49 c3 8 c9
  //   ff d0 fe 68 48 9 8 c9 a8 d0 fe 28 a9 0 29 ef 48 a9 c3 28 49 c3 8 c9 0 d0 fe 68 48 9 8 c9 2a d0 fe 28
  //   ad 0 2 c9 6 d0 fe a9 7 8d 0 2 a2 24 a0 42 a9 0 29 ef 48 a9 18 28 ea 8 c9 18 d0 fe 68 48 9 8 c9 28 d0
  //   fe 28 e0 24 d0 fe c0 42 d0 fe a2 db a0 bd a9 ff 29 ef 48 a9 e7 28 ea 8 c9 e7 d0 fe 68 48 9 8 c9 ef
  //   d0 fe 28 e0 db d0 fe c0 bd d0 fe ad 0 2 c9 7 d0 fe a9 8 8d 0 2 a9 0 29 ef 48 28 a9 46 a2 41 a0 52 4c
  //   67 b5 ea ea d0 fe e8 e8 f0 fe 10 fe 90 fe 50 fe c9 ec d0 fe e0 42 d0 fe c0 4f d0 fe ca c8 c8 c8 49
  //   aa 4c 4f 84 ea ea d0 fe e8 e8 f0 fe 30 fe 90 fe 50 fe c9 46 d0 fe e0 41 d0 fe c0 52 d0 fe ad 0 2 c9
  //   8 d0 fe a9 9 8d 0 2 a9 0 29 ef 48 28 a9 49 a2 4e a0 44 6c 98 b5 ea d0 fe 88 88 8 88 88 88 28 f0 fe
  //   10 fe 90 fe 50 fe c9 e3 d0 fe e0 4f d0 fe c0 3e d0 fe ba e0 ff d0 fe ad 0 2 c9 9 d0 fe a9 a 8d 0 2
  //   a9 0 29 ef 48 28 a9 4a a2 53 a0 52 20 d9 b5 8 88 88 88 28 f0 fe 10 fe 90 fe 50 fe c9 e0 d0 fe e0 54
  //   d0 fe c0 4c d0 fe ba e0 ff d0 fe ad 0 2 c9 a d0 fe a9 b 8d 0 2 a9 0 29 ef 48 a9 42 a2 52 a0 4b 28 0
  //   88 8 88 88 88 c9 e8 d0 fe e0 53 d0 fe c0 45 d0 fe 68 9 8 c9 28 d0 fe ba e0 ff d0 fe a9 ff 29 ef 48
  //   a9 bd a2 ad a0 b4 28 0 88 8 88 88 88 c9 17 d0 fe e0 ae d0 fe c0 ae d0 fe 68 9 8 c9 ef d0 fe ba e0 ff
  //   d0 fe ad 0 2 c9 b d0 fe a9 c 8d 0 2 a9 ff 29 ef 48 28 18 8 68 48 9 8 c9 ee d0 fe 28 38 8 68 48 9 8
  //   c9 ef d0 fe 28 58 8 68 48 9 8 c9 eb d0 fe 28 78 8 68 48 9 8 c9 ef d0 fe 28 d8 8 68 48 9 8 c9 ef d0
  //   fe 28 f8 8 68 48 9 8 c9 ef d0 fe 28 b8 8 68 48 9 8 c9 af d0 fe 28 a9 0 29 ef 48 28 8 68 48 9 8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
  //   ROM
  //   32 Ko ($8000-$FFFF)
endmodule

// 6502
module LS6502__Logisim_6502_cpu (
  input  PHI0,
  input  RDY_,
  input  RST_,
  input  NMI_,
  input  IRQ_,
  input  BE,
  input  SO_,
  input  [7:0] Data_input,
  input  VCC,
  input  VSS,
  input  VSS_2,
  input  N_C,
  input  N_C_2,
  output PHI1,
  output PHI2,
  output Address_Bus_0,
  output Address_Bus_1,
  output Address_Bus_2,
  output Address_Bus_3,
  output Address_Bus_4,
  output Address_Bus_5,
  output Address_Bus_6,
  output Address_Bus_7,
  output Address_Bus_8,
  output Address_Bus_9,
  output Address_Bus_10,
  output Address_Bus_11,
  output Address_Bus_12,
  output Address_Bus_13,
  output Address_Bus_14,
  output Address_Bus_15,
  output [7:0] Data_output,
  output R_W_,
  output SYNC
);

  wire ABw, Accw, ALU0, ALU1, ALU2, ALU3, and_1_out, and_3_out, and_4_out, B, B7, brch, brk, C, CF0, CF1,
       CF2, clk, D, d_ff_1_qn, F0, F1, F2, flags_status_processor_register_1_out, I, Int,
       interrupt_controller_1_mux1, interrupt_controller_1_mux2_0, interrupt_controller_1_mux2_1,
       interrupt_controller_1_mux2_2, IRw, MU0, MU1, MU2, mu_memory_unit_1_ab_lo_plus_plus, Mux0, Mux1, Mux2,
       N, not_1_out, or_1_out, or_2_out, or_3_out, OUTw, pc_lo_program_counter_low_1_cout, PC_plus_plus,
       PChw, PClw, R_W__t, rst, SO, SPw, SYNC_t, TMPw, to_B, to_C, to_N, to_V, to_Z, V, xor_1_out, Xw, Yw, Z;
  wire [2:0] mux_8_1_8_bits_2_output_2;
  wire [3:0] cu_control_unit_1_car_value, cu_control_unit_1_car_value_2,
       flags_status_processor_register_1_processor_status_register_output,
       flags_status_processor_register_1_processor_status_register_output_2, mux_8_1_8_bits_1_output,
       mux_8_1_8_bits_1_output_2, mux_8_1_8_bits_2_output;
  wire [7:0] a_accumulator_1_output, address_bus_high_1_output, address_bus_low_register_1_outputs,
       alu_arithmetic_and_logic_unit_1_sum, ir_istruction_register_1_output, mux_2_1_8_bits_1_output,
       out_data_output_register_1_output, pc_hi_program_counter_high_1_outputs,
       pc_lo_program_counter_low_1_outputs, s_stack_pointer_1_output, tmp_temporary_register_1_output,
       x_index_x_1_output, y_index_y_1_output;
  wire [15:0] mu_memory_unit_1_output;

  Pull_Resistor #(.pull(1)) pull_resistor_1 (.node(RDY_));
  Pull_Resistor #(.pull(1)) pull_resistor_2 (.node(RST_));
  Pull_Resistor #(.pull(1)) pull_resistor_3 (.node(NMI_));
  Pull_Resistor #(.pull(1)) pull_resistor_4 (.node(IRQ_));
  Pull_Resistor #(.pull(1)) pull_resistor_5 (.node(BE));
  Pull_Resistor #(.pull(1)) pull_resistor_6 (.node(SO_));
  not not_1 (not_1_out, SO_);
  Interrupt_Controller interrupt_controller_1 (
    .clk(clk), .i_flag(I), .\break (brk), .mux1(interrupt_controller_1_mux1),
    .mux2_0(interrupt_controller_1_mux2_0), .mux2_1(interrupt_controller_1_mux2_1),
    .mux2_2(interrupt_controller_1_mux2_2), .set_B_flag(to_B), .Interrupt(Int), .rst(rst), .NMI_(NMI_),
    .RST_(RST_), .IRQ_(IRQ_));
  Mux_8_1__8_bits mux_8_1_8_bits_1 (
    .Input_0({8{1'b1}}), .Input_1(8'hfa), .Input_2(8'hfb), .Input_3(8'hfc), .Input_4(8'hfd), .Input_5(8'hfe),
    .Input_6({8{1'b0}}), .Input_7({8{1'b0}}), .Output({mux_8_1_8_bits_1_output_2, mux_8_1_8_bits_1_output}),
    .Select_0(interrupt_controller_1_mux2_0), .Select_1(interrupt_controller_1_mux2_1),
    .Select_2(interrupt_controller_1_mux2_2));
  Rising_Eadge_Detector R_E_D (.\input (not_1_out), .\output (SO), .clk(clk));
  Hex_Digit_Display hex_digit_display_1 (.value(mux_8_1_8_bits_1_output_2));  // open: dp
  and and_1 (and_1_out, ~RDY_, R_W__t);  // AND_Gate
  Hex_Digit_Display hex_digit_display_2 (.value(mux_8_1_8_bits_1_output));  // open: dp
  not not_2 (PHI1, PHI0);
  D_Flip_Flop d_ff_1 (.clk(PHI0), .D(and_1_out), .Qn(d_ff_1_qn));  // open: Q, preset, en, reset
  and and_2 (clk, d_ff_1_qn, PHI1);
  Mux_2_1__8_bits mux_2_1_8_bits_1 (
    .Input_0(alu_arithmetic_and_logic_unit_1_sum),
    .Input_1({mux_8_1_8_bits_1_output_2, mux_8_1_8_bits_1_output}), .Output(mux_2_1_8_bits_1_output),
    .Select(interrupt_controller_1_mux1));
  not not_3 (PHI2, PHI1);
  IR__Istruction_Register ir_istruction_register_1 (
    .\input (alu_arithmetic_and_logic_unit_1_sum), .\output (ir_istruction_register_1_output), .clk(clk),
    .write_enable(IRw));
  xor xor_1 (xor_1_out, to_C, B7);
  and and_3 (and_3_out, xor_1_out, brch);
  or or_1 (or_1_out, and_3_out, pc_lo_program_counter_low_1_cout);
  PC_hi__Program_Counter_high pc_hi_program_counter_high_1 (
    .enable(or_1_out), .load(PChw), .CLK(clk), .reset(1'b0), .Outputs(pc_hi_program_counter_high_1_outputs),
    .Inputs(alu_arithmetic_and_logic_unit_1_sum), .dec_inc_(and_4_out));  // open: Cout
  or or_2 (or_2_out, brch, PClw);
  PC_lo__Program_Counter_Low pc_lo_program_counter_low_1 (
    .Outputs(pc_lo_program_counter_low_1_outputs), .Inputs(alu_arithmetic_and_logic_unit_1_sum),
    .Cout(pc_lo_program_counter_low_1_cout), .CLK(clk), .reset(1'b0), .inc(PC_plus_plus), .load(or_2_out));
  S__Stack_Pointer s_stack_pointer_1 (
    .\input (alu_arithmetic_and_logic_unit_1_sum), .\output (s_stack_pointer_1_output), .clk(clk),
    .write_enable(SPw));
  LED led_1 (.in(V));
  LED led_2 (.in(N));
  X__Index_X x_index_x_1 (
    .\input (alu_arithmetic_and_logic_unit_1_sum), .\output (x_index_x_1_output), .clk(clk), .write_enable(Xw));
  Y__Index_Y y_index_y_1 (
    .\input (alu_arithmetic_and_logic_unit_1_sum), .\output (y_index_y_1_output), .clk(clk), .write_enable(Yw));
  TMP__Temporary_register tmp_temporary_register_1 (
    .\input (alu_arithmetic_and_logic_unit_1_sum), .\output (tmp_temporary_register_1_output), .clk(clk),
    .write_enable(TMPw));
  A__Accumulator a_accumulator_1 (
    .\input (alu_arithmetic_and_logic_unit_1_sum), .\output (a_accumulator_1_output), .clk(clk),
    .write_enable(Accw));
  and and_4 (and_4_out, brch, B7, ~to_C);  // AND_Gate
  Flags__Status_Processor_Register flags_status_processor_register_1 (
    .processor_status_register_output({flags_status_processor_register_1_processor_status_register_output_2, flags_status_processor_register_1_processor_status_register_output}),
    .clk(clk), .N_in(to_N), .V_in(to_V), .B_in(to_B), .Z_in(to_Z), .C_in(to_C), .N_out(N), .V_out(V),
    .out(flags_status_processor_register_1_out), .B_out(B), .Z_out(Z), .C_out(C), .SO(SO),
    .Memory_input(alu_arithmetic_and_logic_unit_1_sum), .D_out(D), .I_out(I), .F2(F2), .F1(F1), .F0(F0),
    .cfg2(CF2), .cfg1(CF1), .cfg0(CF0));
  LED led_3 (.in(B));
  LED led_4 (.in(flags_status_processor_register_1_out));
  Hex_Digit_Display hex_digit_display_3 (.value(ir_istruction_register_1_output[7:4]));  // open: dp
  Hex_Digit_Display hex_digit_display_4 (.value(mux_2_1_8_bits_1_output[7:4]));  // open: dp
  Hex_Digit_Display hex_digit_display_5 (.value(pc_hi_program_counter_high_1_outputs[7:4]));  // open: dp
  Hex_Digit_Display hex_digit_display_6 (.value(pc_lo_program_counter_low_1_outputs[7:4]));  // open: dp
  Hex_Digit_Display hex_digit_display_7 (.value(s_stack_pointer_1_output[7:4]));  // open: dp
  LED led_5 (.in(I));
  LED led_6 (.in(D));
  Hex_Digit_Display hex_digit_display_8 (.value(x_index_x_1_output[7:4]));  // open: dp
  Hex_Digit_Display hex_digit_display_9 (.value(y_index_y_1_output[7:4]));  // open: dp
  Hex_Digit_Display hex_digit_display_10 (.value(tmp_temporary_register_1_output[7:4]));  // open: dp
  Hex_Digit_Display hex_digit_display_11 (.value(a_accumulator_1_output[7:4]));  // open: dp
  Hex_Digit_Display hex_digit_display_12 (.value(ir_istruction_register_1_output[3:0]));  // open: dp
  // Probe on ir_istruction_register_1_output
  Hex_Digit_Display hex_digit_display_13 (.value(mux_2_1_8_bits_1_output[3:0]));  // open: dp
  Hex_Digit_Display hex_digit_display_14 (.value(pc_hi_program_counter_high_1_outputs[3:0]));  // open: dp
  Hex_Digit_Display hex_digit_display_15 (.value(pc_lo_program_counter_low_1_outputs[3:0]));  // open: dp
  Hex_Digit_Display hex_digit_display_16 (.value(s_stack_pointer_1_output[3:0]));  // open: dp
  LED led_7 (.in(Z));
  LED led_8 (.in(C));
  Hex_Digit_Display hex_digit_display_17 (.value(x_index_x_1_output[3:0]));  // open: dp
  Hex_Digit_Display hex_digit_display_18 (.value(y_index_y_1_output[3:0]));  // open: dp
  Hex_Digit_Display hex_digit_display_19 (.value(tmp_temporary_register_1_output[3:0]));  // open: dp
  Hex_Digit_Display hex_digit_display_20 (.value(a_accumulator_1_output[3:0]));  // open: dp
  // Probe on a_accumulator_1_output
  Hex_Digit_Display hex_digit_display_21 (.value(alu_arithmetic_and_logic_unit_1_sum[7:4]));  // open: dp
  Hex_Digit_Display hex_digit_display_22 (.value(alu_arithmetic_and_logic_unit_1_sum[3:0]));  // open: dp
  Hex_Digit_Display hex_digit_display_23 (.value(flags_status_processor_register_1_processor_status_register_output_2));  // open: dp
  // Probe on x_index_x_1_output
  // Probe on y_index_y_1_output
  or or_3 (or_3_out, rst, R_W__t);
  LED u_SYNC (.in(SYNC_t));
  LED u_R_W_ (.in(or_3_out));
  // Probe on pc_hi_program_counter_high_1_outputs
  // Probe on pc_lo_program_counter_low_1_outputs
  // Probe on s_stack_pointer_1_output
  Hex_Digit_Display hex_digit_display_24 (.value(flags_status_processor_register_1_processor_status_register_output));  // open: dp
  // Probe on {flags_status_processor_register_1_processor_status_register_output_2, flags_status_processor_register_1_processor_status_register_output}
  Hex_Digit_Display hex_digit_display_25 (.value({B7, mux_8_1_8_bits_2_output_2}));  // open: dp
  ALU__Arithmetic_and_Logic_Unit alu_arithmetic_and_logic_unit_1 (
    .A(a_accumulator_1_output), .B({B7, mux_8_1_8_bits_2_output_2, mux_8_1_8_bits_2_output}), .Cin(C),
    .Sum(alu_arithmetic_and_logic_unit_1_sum), .Cout(to_C), .zero(to_Z), .negative(to_N), .overflow(to_V),
    .Functions({ALU3, ALU2, ALU1, ALU0}));
  LED u_OUTw (.in(OUTw));
  LED u_ABw (.in(ABw));
  LED u_PC_plus_plus (.in(PC_plus_plus));
  MU__Memory_Unit mu_memory_unit_1 (
    .MU2(MU2), .MU1(MU1), .MU0(MU0), .from_ALU(mux_2_1_8_bits_1_output), .CLK(clk), .carry(to_C),
    .from_PC_hi(pc_hi_program_counter_high_1_outputs), .\output (mu_memory_unit_1_output),
    .from_PC_lo(pc_lo_program_counter_low_1_outputs), .from_Stack(s_stack_pointer_1_output),
    .AB_lo_plus_plus(mu_memory_unit_1_ab_lo_plus_plus));
  Mux_8_1__8_bits mux_8_1_8_bits_2 (
    .Input_0(Data_input), .Input_1(pc_hi_program_counter_high_1_outputs),
    .Input_2(pc_lo_program_counter_low_1_outputs), .Input_3(s_stack_pointer_1_output),
    .Input_4({flags_status_processor_register_1_processor_status_register_output_2, flags_status_processor_register_1_processor_status_register_output}),
    .Input_5(x_index_x_1_output), .Input_6(y_index_y_1_output), .Input_7(tmp_temporary_register_1_output),
    .Output({B7, mux_8_1_8_bits_2_output_2, mux_8_1_8_bits_2_output}), .Select_0(Mux0), .Select_1(Mux1),
    .Select_2(Mux2));
  Hex_Digit_Display hex_digit_display_26 (.value(mux_8_1_8_bits_2_output));  // open: dp
  LED u_IRw (.in(IRw));
  LED u_PChw (.in(PChw));
  LED u_PClw (.in(PClw));
  LED u_SPw (.in(SPw));
  LED u_TMPw (.in(TMPw));
  LED u_Yw (.in(Yw));
  LED u_Xw (.in(Xw));
  LED u_Accw (.in(Accw));
  CU__Control_Unit cu_control_unit_1 (
    .CLK(clk), .OpCode(ir_istruction_register_1_output), .ALU3(ALU3), .ALU2(ALU2), .ALU1(ALU1), .ALU0(ALU0),
    .Mux2(Mux2), .Mux1(Mux1), .Mux0(Mux0), .MU1(MU1), .MU0(MU0), .brk(brk), .MU2(MU2), .CF2(CF2), .CF1(CF1),
    .CF0(CF0), .F2(F2), .F1(F1), .F0(F0), .TMPw(TMPw), .Yw(Yw), .Xw(Xw), .Accw(Accw), .IRw(IRw), .PChw(PChw),
    .PClw(PClw), .SPw(SPw), .OUTw(OUTw), .ABw(ABw), .R_W_(R_W__t), .SYNC(SYNC_t),
    .PC_plus_plus(PC_plus_plus), .Negative(N), .Ovreflow(V), .Zero(Z), .Carry(C), .brch(brch),
    .Interrupt(Int), .CAR_value({cu_control_unit_1_car_value_2, cu_control_unit_1_car_value}));
  LED u_F0 (.in(F0));
  LED u_F2 (.in(F2));
  LED u_F1 (.in(F1));
  Hex_Digit_Display hex_digit_display_27 (.value(mu_memory_unit_1_output[15:12]));  // open: dp
  Hex_Digit_Display hex_digit_display_28 (.value(mu_memory_unit_1_output[11:8]));  // open: dp
  LED u_CF2 (.in(CF2));
  LED u_CF1 (.in(CF1));
  LED u_CF0 (.in(CF0));
  LED u_brch (.in(brch));
  Hex_Digit_Display hex_digit_display_29 (.value(mu_memory_unit_1_output[3:0]));  // open: dp
  Hex_Digit_Display hex_digit_display_30 (.value(mu_memory_unit_1_output[7:4]));  // open: dp
  OUT__Data_output_register out_data_output_register_1 (
    .\input (alu_arithmetic_and_logic_unit_1_sum), .\output (out_data_output_register_1_output), .clk(clk),
    .write_enable(OUTw));
  LED u_MU2 (.in(MU2));
  LED u_MU1 (.in(MU1));
  LED u_brk (.in(brk));
  Hex_Digit_Display hex_digit_display_31 (.value(out_data_output_register_1_output[7:4]));  // open: dp
  Hex_Digit_Display hex_digit_display_32 (.value(out_data_output_register_1_output[3:0]));  // open: dp
  LED u_Mux2 (.in(Mux2));
  LED u_Mux1 (.in(Mux1));
  LED u_MU0 (.in(MU0));
  Hex_Digit_Display hex_digit_display_33 (.value(cu_control_unit_1_car_value_2));  // open: dp
  LED u_ALU3 (.in(ALU3));
  LED u_ALU2 (.in(ALU2));
  LED u_ALU1 (.in(ALU1));
  LED u_Mux0 (.in(Mux0));
  Address_Bus__high address_bus_high_1 (
    .\input (mu_memory_unit_1_output[15:8]), .\output (address_bus_high_1_output), .clk(clk),
    .write_enable(ABw));
  Address_Bus__low_register address_bus_low_register_1 (
    .Inputs(mu_memory_unit_1_output[7:0]), .Outputs(address_bus_low_register_1_outputs),
    .inc(mu_memory_unit_1_ab_lo_plus_plus), .load(ABw), .CLK(clk), .reset(1'b0));  // open: Cout
  Hex_Digit_Display hex_digit_display_34 (.value(cu_control_unit_1_car_value));  // open: dp
  // Probe on {cu_control_unit_1_car_value_2, cu_control_unit_1_car_value}
  LED u_ALU0 (.in(ALU0));
  Hex_Digit_Display hex_digit_display_35 (.value(address_bus_high_1_output[7:4]));  // open: dp
  Hex_Digit_Display hex_digit_display_36 (.value(Data_input[7:4]));  // open: dp
  Hex_Digit_Display hex_digit_display_37 (.value(address_bus_low_register_1_outputs[7:4]));  // open: dp
  Hex_Digit_Display hex_digit_display_38 (.value(address_bus_high_1_output[3:0]));  // open: dp
  Hex_Digit_Display hex_digit_display_39 (.value(Data_input[3:0]));  // open: dp
  assign Data_output = BE ? out_data_output_register_1_output : 8'bz;  // Controlled_Buffer controlled_buffer_1
  Hex_Digit_Display hex_digit_display_40 (.value(address_bus_low_register_1_outputs[3:0]));  // open: dp
  assign {Address_Bus_15, Address_Bus_14, Address_Bus_13, Address_Bus_12, Address_Bus_11, Address_Bus_10, Address_Bus_9, Address_Bus_8, Address_Bus_7, Address_Bus_6, Address_Bus_5, Address_Bus_4, Address_Bus_3, Address_Bus_2, Address_Bus_1, Address_Bus_0} = BE ? {address_bus_high_1_output, address_bus_low_register_1_outputs} : 16'bz;  // Controlled_Buffer controlled_buffer_2
  Pull_Resistor pull_resistor_7 (.node(Data_input));
  assign R_W_ = BE ? R_W__t : 1'bz;  // Controlled_Buffer controlled_buffer_3
  and and_5 (SYNC, SYNC_t, clk);

  // Notes on the sheet:
  //   001: write NZ
  //   Control Flags [CF] codes :
  //   000: write nothing
  //   010: write NZC
  //   011: write NZCV
  //   110: write NV from M7 and M6
  //   111: write all flags from stack
  //   100: set flag with code [F2,F1,F0]
  //   101: reset flag with code [F2,F1,F0]
  //   Clock
  //   Circuit
  //   ALU commands :
  //   0000: A^B
  //   0001: A&B
  //   0010: A-1
  //   0011: 0>>B>>C
  //   0100: A+B
  //   0101: A+B+C
  //   0110: A
  //   0111: A-B-(C-1)
  //   From ALU
  //   branch across 256 page
  //   boundary manager
  //   1000: B+1
  //   1001: B
  //   1010: B-1
  //   1011: C>>B>>C
  //   1100: C<<B<<0
  //   1101: C<<B<<C
  //   1110: A|B
  //   1111: A-B
  //   MU commands :
  //   001: [01,SP]
  //   010: AB-lo++
  //   011: [@hi,@lo]
  //   000: PC:[PC-hi,PC-lo]
  //   101: write ALU on @hi
  //   110: @hi++ if Carry
  //   Micro-instrucrion
  //   register (CAR) value :
  //   100: write ALU on @lo and @hi <- 0
  //   111: write ALU on @lo and write Carry
  //    @hi and @lo are 2 internal 8bits registers
endmodule

// CU
module CU__Control_Unit (
  input  CLK,
  input  Interrupt,
  input  Negative,
  input  Ovreflow,
  input  Carry,
  input  Zero,
  input  [7:0] OpCode,
  output [7:0] CAR_value,
  output OUTw,
  output ABw,
  output IRw,
  output SYNC,
  output PChw,
  output R_W_,
  output ALU3,
  output PClw,
  output PC_plus_plus,
  output CF2,
  output MU2,
  output Mux2,
  output ALU2,
  output SPw,
  output CF1,
  output MU1,
  output Mux1,
  output ALU1,
  output TMPw,
  output F2,
  output F1,
  output F0,
  output CF0,
  output brk,
  output MU0,
  output Mux0,
  output ALU0,
  output Yw,
  output Xw,
  output Accw,
  output brch
);

  wire csr_control_status_register_1_v2, not_1_out, sc_sequencer_controller_1_load_car_,
       sc_sequencer_controller_1_load_mapper_brench_,
       sc_sequencer_controller_1_operation_mapper_address_mode_mapper_, sc_sequencer_controller_1_reset;
  wire [1:0] csr_control_status_register_1_sc0;
  wire [3:0] address_mode_mapper_1_control_address, address_mode_mapper_1_control_address_2;
  wire [7:0] csr_control_status_register_1_ad0, mux_2_1_8_bits_1_output, mux_2_1_8_bits_2_output,
       operation_mapper_1_operation_address;
  wire [9:0] rom_1_data;
  wire [31:0] rom_2_data;

  BC__Branch_Controller bc_branch_controller_1 (
    .negative(Negative), .overflow(Ovreflow), .carry(Carry), .zero(Zero), .branch_2(brch), .OpCode(OpCode),
    .branch(csr_control_status_register_1_v2));
  SC__Sequencer_Controller sc_sequencer_controller_1 (
    .Interrupt(Interrupt),
    .Operation_Mapper_Address_Mode_Mapper_(sc_sequencer_controller_1_operation_mapper_address_mode_mapper_),
    .Load_Mapper_Brench_(sc_sequencer_controller_1_load_mapper_brench_),
    .Load_CAR_(sc_sequencer_controller_1_load_car_), .Command(csr_control_status_register_1_sc0),
    .reset(sc_sequencer_controller_1_reset), .SYNC(SYNC));
  Address_Mode_Mapper address_mode_mapper_1 (
    .Control_Address({address_mode_mapper_1_control_address_2, address_mode_mapper_1_control_address}),
    .OpCode(OpCode));
  Hex_Digit_Display hex_digit_display_1 (.value(address_mode_mapper_1_control_address));  // open: dp
  Hex_Digit_Display hex_digit_display_2 (.value(address_mode_mapper_1_control_address_2));  // open: dp
  Hex_Digit_Display hex_digit_display_3 (.value(CAR_value[7:4]));  // open: dp
  Hex_Digit_Display hex_digit_display_4 (.value(operation_mapper_1_operation_address[7:4]));  // open: dp
  Hex_Digit_Display hex_digit_display_5 (.value(operation_mapper_1_operation_address[3:0]));  // open: dp
  Operation_Mapper operation_mapper_1 (.OpCode(OpCode), .operation_address(operation_mapper_1_operation_address));
  Mux_2_1__8_bits mux_2_1_8_bits_1 (
    .Input_0({address_mode_mapper_1_control_address_2, address_mode_mapper_1_control_address}),
    .Input_1(operation_mapper_1_operation_address), .Output(mux_2_1_8_bits_1_output),
    .Select(sc_sequencer_controller_1_operation_mapper_address_mode_mapper_));
  Mux_2_1__8_bits mux_2_1_8_bits_2 (
    .Input_0(csr_control_status_register_1_ad0), .Input_1(mux_2_1_8_bits_1_output),
    .Output(mux_2_1_8_bits_2_output), .Select(sc_sequencer_controller_1_load_mapper_brench_));
  CAR__Control_Address_Register car_control_address_register_1 (
    .load_inc_(sc_sequencer_controller_1_load_car_), .CLK(CLK), .reset(sc_sequencer_controller_1_reset),
    .Inputs(mux_2_1_8_bits_2_output), .Outputs(CAR_value));  // open: Cout
  Hex_Digit_Display hex_digit_display_6 (.value(CAR_value[3:0]));  // open: dp
  not not_1 (not_1_out, CLK);
  ROM #(.dataWidth(10)) rom_1 (.addr(CAR_value), .data(rom_1_data));  // open: sel
  ROM #(.dataWidth(32)) rom_2 (.addr(CAR_value), .data(rom_2_data));  // open: sel
  CSR__Control_Status_Register csr_control_status_register_1 (
    .clk(not_1_out), .Write(1'b1), .V0(MU2), .MU1(MU1), .MU0(MU0), .Mux2(Mux2), .Mux1(Mux1), .Mux0(Mux0),
    .ALU3(ALU3), .ALU2(ALU2), .ALU1(ALU1), .ALU0(ALU0), .Xw(Xw), .Accw(Accw), .F2(F2), .F1(F1), .F0(F0),
    .CF2(CF2), .CF1(CF1), .CF0(CF0), .V2(csr_control_status_register_1_v2), .V1(brk), .OUTw(OUTw), .ABw(ABw),
    .IRw(IRw), .PChw(PChw), .PClw(PClw), .SPw(SPw), .TMPw(TMPw), .Yw(Yw), .signals_input(rom_2_data),
    .SC1(csr_control_status_register_1_sc0[1]), .SC0(csr_control_status_register_1_sc0[0]),
    .next_address_input(rom_1_data), .AD7(csr_control_status_register_1_ad0[7]),
    .AD6(csr_control_status_register_1_ad0[6]), .AD5(csr_control_status_register_1_ad0[5]),
    .AD4(csr_control_status_register_1_ad0[4]), .AD3(csr_control_status_register_1_ad0[3]),
    .AD2(csr_control_status_register_1_ad0[2]), .AD1(csr_control_status_register_1_ad0[1]),
    .AD0(csr_control_status_register_1_ad0[0]), .SYNC(SYNC), .R_W_(R_W_), .PC_plus_plus(PC_plus_plus));

  // Notes on the sheet:
  //   SC cmds :
  //   00 : CAR++
  //   01 : CAR <- next address
  //   11 : CAR <- Operation Mapper
  //   Address Mode
  //   10 : CAR <- Operation Address Mode Mapper
  //   Operation
  //   30      29     28
  //   27  26  25  24
  //   MP ROM
  //   (addresses+SC cmds)
  //   MP ROM
  //   (signals)
  //   23  22  21  20
  //   contents of rom_1 (hex, n*v repeats v):
  //   13*0 110 100 0 0 0 200 0 300 300 0 0 300 0 0 0 300 0 0 0 300 0 0 0 110 4*0 300 6*0 300 6*0 300 7*0
  //   300 8*0 300 7*0 4*110 0 4*110 0 110 0 110 0 110 0 110 0 110 0 110 0 110 0 110 0 6*110 0 110 110 0
  //   110 110 0 0 0 110 110 110 0 0 0 6*110 0 110 110 110 0 0 110 0 0 110 4*0 5*110 0 0 110 0 110 0 110 0
  //   110 8*0 110 6*0 110 8*0 110
  //   contents of rom_2 (hex, n*v repeats v):
  //   2c000499 40003a 2c0000a9 40003a 2c0000c9 40003a 20000200 20000280 24000580 20800409 20000200
  //   20000280 24014180 21000009 30000000 0 64000000 32000009 20000000 0 20000000 34000000 34000000
  //   20000209 24000180 34200006 20040009 20000254 240401f9 34200006 20040009 20000264 240401f9 34200006
  //   20040029 20000804 20040079 34000000 20000209 34000000 20000289 24000180 34200006 20040009 200003d4
  //   34040079 20000289 20000300 24000180 34200006 20040009 200003e4 34040079 20000289 20000300 24000180
  //   34200006 20040009 20000254 240401f9 20000209 20000100 20000289 24000180 34200006 20000209 24000180
  //   20040009 200003e4 20040179 20000289 20000300 24000180 7*0 2004100e 20041001 20041000 20043005
  //   28000006 0 20041009 2000200f 20043007 2800200c 0 20200006 2004207c 2800200d 0 20200006 2004207d
  //   28002003 0 20200006 20042073 2800200b 0 20200006 2004207b 28000059 0 20041059 20400059 20081009
  //   20081006 20081039 2800100a 0 2008105a 28001008 0 20000000 20200006 20040059 2000200f 20040079
  //   20081058 2001c000 20200006 20040069 2000200f 20040079 20101068 2001d000 20101009 20101006 20035000
  //   28000069 0 2010106a 20041069 20400038 24000080 20041009 20800009 20000100 21000009 34000000 20200009
  //   24000000 20800079 21000009 20015000 20014000 20005000 20004000 20400038 24000080 20007009 2c000086
  //   40003a 2c0000c9 40003a 20001001 20006009 34000000 20200009 2c000099 40003a 2c0000a9 40003a 24000000
  //   20800079 21000009 20400038 24000080 20800009 20400038 24000080 21000009 30000000 20400038 24000080
  //   20007009 20400038 24000080 20800009 20400038 24000080 21000009
  //   19  18      17  16
  //   15     14   13  12
  //   Sequencer
  //   11      10      9    8
  //   7        6    5    4
  //   3    2     1    0
  //   next address
endmodule

// MU
module MU__Memory_Unit (
  input  CLK,
  input  MU2,
  input  MU1,
  input  MU0,
  input  [7:0] from_PC_hi,
  input  [7:0] from_ALU,
  input  [7:0] from_PC_lo,
  input  [7:0] from_Stack,
  input  carry,
  output [15:0] \output ,
  output AB_lo_plus_plus
);

  wire and_1_out, and_2_out, and_3_out, and_4_out, and_5_out, d_ff_1_q, or_1_out;
  wire [7:0] address_hi_adress_high_1_outputs, address_lo_adress_low_1_output;

  and and_1 (and_1_out, and_3_out, d_ff_1_q);
  or or_1 (or_1_out, and_4_out, and_5_out);
  Address_lo__Adress_low address_lo_adress_low_1 (
    .\input (from_ALU), .\output (address_lo_adress_low_1_output), .clk(CLK), .write_enable(or_1_out));
  Address_hi__Adress_high address_hi_adress_high_1 (
    .inc(and_1_out), .load(and_2_out), .CLK(CLK), .reset(and_4_out),
    .Outputs(address_hi_adress_high_1_outputs), .Inputs(from_ALU));  // open: Cout
  D_Flip_Flop #(.trigger("high")) d_ff_1 (
    .clk(CLK), .D(carry), .Q(d_ff_1_q), .en(and_5_out));  // open: Qn, preset, reset
  Hex_Digit_Display hex_digit_display_1 (.value(address_hi_adress_high_1_outputs[7:4]));  // open: dp
  Hex_Digit_Display hex_digit_display_2 (.value(address_lo_adress_low_1_output[7:4]));  // open: dp
  and and_2 (and_2_out, MU2, ~MU1, MU0);  // AND_Gate
  and and_3 (and_3_out, MU2, MU1, ~MU0);  // AND_Gate
  Hex_Digit_Display hex_digit_display_3 (.value(address_hi_adress_high_1_outputs[3:0]));  // open: dp
  and and_4 (and_4_out, MU2, ~MU1, ~MU0);  // AND_Gate
  Hex_Digit_Display hex_digit_display_4 (.value(address_lo_adress_low_1_output[3:0]));  // open: dp
  and and_5 (and_5_out, MU2, MU1, MU0);
  Mux_8_1__8_bits mux_8_1_8_bits_1 (
    .Input_0(from_PC_hi), .Input_1(8'h1), .Input_2({8{1'b0}}), .Input_3(address_hi_adress_high_1_outputs),
    .Input_4({8{1'b0}}), .Input_5({8{1'b0}}), .Input_6({8{1'b0}}), .Input_7({8{1'b0}}),
    .Output(\output [15:8]), .Select_0(MU0), .Select_1(MU1), .Select_2(MU2));
  Mux_8_1__8_bits mux_8_1_8_bits_2 (
    .Input_0(from_PC_lo), .Input_1(from_Stack), .Input_2({8{1'b0}}),
    .Input_3(address_lo_adress_low_1_output), .Input_4({8{1'b0}}), .Input_5({8{1'b0}}), .Input_6({8{1'b0}}),
    .Input_7({8{1'b0}}), .Output(\output [7:0]), .Select_0(MU0), .Select_1(MU1), .Select_2(MU2));
  and and_6 (AB_lo_plus_plus, ~MU2, MU1, ~MU0);  // AND_Gate
endmodule

// ALU
module ALU__Arithmetic_and_Logic_Unit (
  input  Cin,
  input  [3:0] Functions,
  input  [7:0] A,
  input  [7:0] B,
  output [7:0] Sum,
  output zero,
  output negative,
  output overflow,
  output Cout
);

  wire adder_8_bits_1_cout, and_1_out, and_4_out, and_5_out, and_6_out, and_7_out, nor_1_out, or_2_out,
       shift_1_bit_right_8_bits_1_cout;
  wire [7:0] adder_8_bits_1_s, and_2_out, and_3_out, mux_2_1_8_bits_1_output, mux_2_1_8_bits_2_output,
       or_1_out, shift_1_bit_right_8_bits_1_output, xor_1_out, xor_2_out;

  and and_1 (and_1_out, Functions[3], ~and_7_out);  // AND_Gate
  Mux_2_1__8_bits mux_2_1_8_bits_1 (.Input_0(A), .Input_1(B), .Output(mux_2_1_8_bits_1_output), .Select(and_1_out));
  assign xor_1_out = mux_2_1_8_bits_1_output ^ B;  // XOR_Gate xor_1, 8 bits wide
  assign and_2_out = mux_2_1_8_bits_1_output & B;  // AND_Gate and_2, 8 bits wide
  assign or_1_out = mux_2_1_8_bits_1_output | A;  // OR_Gate or_1, 8 bits wide
  assign and_3_out = {8{Functions[2]}} & B;  // AND_Gate and_3, 8 bits wide
  assign xor_2_out = {8{Functions[1]}} ^ and_3_out;  // XOR_Gate xor_2, 8 bits wide
  and and_4 (and_4_out, Functions[3], or_2_out);
  Shift_1_bit_right__8_bits shift_1_bit_right_8_bits_1 (
    .Input(B), .Output(shift_1_bit_right_8_bits_1_output), .Cout(shift_1_bit_right_8_bits_1_cout),
    .Cin(and_4_out));
  and and_5 (and_5_out, Cin, Functions[0]);
  or or_2 (or_2_out, and_5_out, and_7_out, nor_1_out);
  Adder__8_bits adder_8_bits_1 (
    .A(mux_2_1_8_bits_1_output), .B(xor_2_out), .S(adder_8_bits_1_s), .Cin(or_2_out),
    .Cout(adder_8_bits_1_cout), .overflow(overflow));
  Mux_2_1__1_bit mux_2_1_1_bit_1 (
    .Input_0(adder_8_bits_1_cout), .Input_1(shift_1_bit_right_8_bits_1_cout), .Output(Cout),
    .Select(and_6_out));
  Mux_2_1__8_bits mux_2_1_8_bits_2 (
    .Input_0(xor_1_out), .Input_1(adder_8_bits_1_s), .Output(mux_2_1_8_bits_2_output), .Select(Functions[3]));
  and and_6 (and_6_out, ~Functions[2], Functions[1], Functions[0]);  // AND_Gate
  and and_7 (and_7_out, Functions[3], Functions[2], Functions[1], Functions[0]);
  nor nor_1 (nor_1_out, Functions[2], Functions[1]);
  Mux_8_1__8_bits mux_8_1_8_bits_1 (
    .Input_0(mux_2_1_8_bits_2_output), .Input_1(and_2_out), .Input_2(adder_8_bits_1_s),
    .Input_3(shift_1_bit_right_8_bits_1_output), .Input_4(adder_8_bits_1_s), .Input_5(adder_8_bits_1_s),
    .Input_6(or_1_out), .Input_7(adder_8_bits_1_s), .Output({negative, Sum[6:0]}), .Select_0(Functions[0]),
    .Select_1(Functions[1]), .Select_2(Functions[2]));
  nor nor_2 (zero, Sum[0], Sum[1], Sum[2], Sum[3], Sum[4], Sum[5], Sum[6], negative);

  assign Sum[7] = negative;
endmodule

// Interrupt
module Interrupt_Controller (
  input  clk,
  input  \break ,
  input  i_flag,
  input  RST_,
  input  NMI_,
  input  IRQ_,
  output mux1,
  output Interrupt,
  output rst,
  output set_B_flag,
  output mux2_2,
  output mux2_1,
  output mux2_0
);

  wire and_1_out, and_2_out, and_3_out, and_4_out, and_5_out, and_6_out, and_7_out, and_8_out, and_9_out,
       and_10_out, and_11_out, and_13_out, and_14_out, d_ff_1_q, d_ff_2_q, d_ff_3_q, d_ff_3_qn, d_ff_4_q,
       d_ff_5_q, d_ff_5_qn, nor_1_out, nor_2_out, nor_3_out, not_1_out, not_2_out, or_2_out, or_4_out,
       serial_to_parallel_shifter_8_bits_1_output_0, serial_to_parallel_shifter_8_bits_1_output_1,
       serial_to_parallel_shifter_8_bits_1_output_2, serial_to_parallel_shifter_8_bits_1_output_3,
       serial_to_parallel_shifter_8_bits_1_output_4, serial_to_parallel_shifter_8_bits_1_output_6,
       serial_to_parallel_shifter_8_bits_1_output_7;

  D_Flip_Flop d_ff_1 (.Q(d_ff_1_q), .preset(d_ff_2_q), .reset(and_7_out));  // open: clk, D, Qn, en
  nor nor_1 (nor_1_out, RST_, d_ff_1_q);
  nor nor_2 (nor_2_out, NMI_, d_ff_1_q);
  nor nor_3 (nor_3_out, IRQ_, i_flag, d_ff_1_q);
  and and_1 (and_1_out, d_ff_3_q, and_7_out);
  and and_2 (and_2_out, and_4_out, and_7_out);
  and and_3 (and_3_out, or_2_out, and_7_out);
  D_Flip_Flop d_ff_2 (.clk(clk), .D(\break ), .Q(d_ff_2_q));  // open: Qn, preset, en, reset
  D_Flip_Flop d_ff_3 (
    .clk(clk), .D(nor_1_out), .Q(d_ff_3_q), .Qn(d_ff_3_qn), .en(d_ff_3_qn), .reset(and_1_out));  // open: preset
  D_Flip_Flop d_ff_4 (.clk(nor_2_out), .D(1'b1), .Q(d_ff_4_q), .reset(and_2_out));  // open: Qn, preset, en
  D_Flip_Flop d_ff_5 (
    .clk(clk), .D(nor_3_out), .Q(d_ff_5_q), .Qn(d_ff_5_qn), .en(d_ff_5_qn), .reset(and_3_out));  // open: preset
  or or_1 (Interrupt, d_ff_5_q, d_ff_4_q, d_ff_3_q);
  and and_4 (and_4_out, ~d_ff_3_q, d_ff_4_q);  // AND_Gate
  and and_5 (and_5_out, ~d_ff_3_q, ~d_ff_4_q, d_ff_5_q);  // AND_Gate
  not not_1 (not_1_out, Interrupt);
  or or_2 (or_2_out, not_1_out, and_5_out);
  not not_2 (not_2_out, clk);
  and and_6 (and_6_out, serial_to_parallel_shifter_8_bits_1_output_0, serial_to_parallel_shifter_8_bits_1_output_1);
  Serial_to_Parallel_Shifter__8_bits serial_to_parallel_shifter_8_bits_1 (
    .Input(d_ff_2_q), .clk(not_2_out), .reset(and_7_out),
    .Output_0(serial_to_parallel_shifter_8_bits_1_output_0),
    .Output_1(serial_to_parallel_shifter_8_bits_1_output_1),
    .Output_2(serial_to_parallel_shifter_8_bits_1_output_2),
    .Output_3(serial_to_parallel_shifter_8_bits_1_output_3),
    .Output_4(serial_to_parallel_shifter_8_bits_1_output_4), .Output_5(mux2_0),
    .Output_6(serial_to_parallel_shifter_8_bits_1_output_6),
    .Output_7(serial_to_parallel_shifter_8_bits_1_output_7));
  and and_7 (and_7_out, serial_to_parallel_shifter_8_bits_1_output_3, serial_to_parallel_shifter_8_bits_1_output_4);
  and and_8 (and_8_out, or_2_out, mux2_0);
  and and_9 (and_9_out, d_ff_3_q, and_6_out);
  or or_3 (mux2_2, and_8_out, and_9_out);
  and and_10 (and_10_out, serial_to_parallel_shifter_8_bits_1_output_0, serial_to_parallel_shifter_8_bits_1_output_1);
  and and_11 (and_11_out, serial_to_parallel_shifter_8_bits_1_output_1, serial_to_parallel_shifter_8_bits_1_output_2);
  or or_4 (or_4_out, serial_to_parallel_shifter_8_bits_1_output_0, serial_to_parallel_shifter_8_bits_1_output_2, serial_to_parallel_shifter_8_bits_1_output_4);
  and and_12 (set_B_flag, serial_to_parallel_shifter_8_bits_1_output_3, not_1_out);
  and and_13 (and_13_out, and_4_out, and_6_out);
  and and_14 (and_14_out, d_ff_3_q, mux2_0);
  or or_5 (mux2_1, and_14_out, and_13_out);
  or or_6 (mux1, and_10_out, mux2_0, serial_to_parallel_shifter_8_bits_1_output_6, and_11_out);
  and and_15 (rst, d_ff_3_q, or_4_out);

  // Notes on the sheet:
  //   locking mechanism
  //   finishing signal
  //   Notes :
  //   priority circuit
  //   - All interruptions do the same BRK micro-instructions sequence
  //   Except for interruption vector, which is controlled by mux outputs
  //   - The Shifter is used as a tracker for BRK micro-instructions
  //   - Micro-instructions 1 and 9 codes are the same, but they don't conflict
  //   - The first micro-instruction in BRK is 0 (not 1, 1 is the second)
  //   - rst output prevent writing PC and P on the stack for RST interrupt
  //   rst
  //   nmi
  //   irq or brk
  //   Shifter output codes :
  //   1000 0000 : micro-instruction 1 of BRK instruction
  //   0100 0000 : micro-instruction 2 of BRK instruction
  //   0010 0000 : micro-instruction 3 of BRK instruction
  //   0001 0000 : micro-instruction 4 of BRK instruction
  //   0000 1000 : micro-instruction 5 of BRK instruction
  //   0000 0100 : micro-instruction 6 of BRK instruction
  //   0000 0010 : micro-instruction 7 of BRK instruction
  //   0000 0001: micro-instruction 8 of BRK instruction
  //   1000 0000 : micro-instruction 9 of BRK instruction
  //   1100 0000 : micro-instruction A of BRK instruction
  //   0110 0000 : micro-instruction B of BRK instruction
  //   0011 0000 : micro-instruction C of BRK instruction
  //   0001 1000 : micro-instruction D of BRK instruction
endmodule

// IR
module IR__Istruction_Register (
  input  clk,
  input  write_enable,
  input  [7:0] \input ,
  output [7:0] \output 
);

  D_Flip_Flop d_ff_1 (.clk(clk), .D(\input [0]), .Q(\output [0]), .en(write_enable));  // open: Qn, preset, reset
  D_Flip_Flop d_ff_2 (.clk(clk), .D(\input [1]), .Q(\output [1]), .en(write_enable));  // open: Qn, preset, reset
  D_Flip_Flop d_ff_3 (.clk(clk), .D(\input [2]), .Q(\output [2]), .en(write_enable));  // open: Qn, preset, reset
  D_Flip_Flop d_ff_4 (.clk(clk), .D(\input [3]), .Q(\output [3]), .en(write_enable));  // open: Qn, preset, reset
  D_Flip_Flop d_ff_5 (.clk(clk), .D(\input [4]), .Q(\output [4]), .en(write_enable));  // open: Qn, preset, reset
  D_Flip_Flop d_ff_6 (.clk(clk), .D(\input [5]), .Q(\output [5]), .en(write_enable));  // open: Qn, preset, reset
  D_Flip_Flop d_ff_7 (.clk(clk), .D(\input [6]), .Q(\output [6]), .en(write_enable));  // open: Qn, preset, reset
  D_Flip_Flop d_ff_8 (.clk(clk), .D(\input [7]), .Q(\output [7]), .en(write_enable));  // open: Qn, preset, reset

  // Notes on the sheet:
  //   8 bits register
endmodule

// PC-hi
module PC_hi__Program_Counter_high (
  input  enable,
  input  load,
  input  CLK,
  input  reset,
  input  dec_inc_,
  input  [7:0] Inputs,
  output [7:0] Outputs,
  output Cout
);

  wire and_1_out, and_2_out, and_3_out, and_4_out, and_5_out, and_6_out, and_7_out, j_k_ff_1_qn, j_k_ff_2_qn,
       j_k_ff_3_qn, j_k_ff_4_qn, j_k_ff_5_qn, j_k_ff_6_qn, j_k_ff_7_qn, j_k_ff_8_qn, mux_2_1_1_bit_1_output,
       mux_2_1_1_bit_2_output, mux_2_1_1_bit_3_output, mux_2_1_1_bit_4_output, mux_2_1_1_bit_5_output,
       mux_2_1_1_bit_6_output, mux_2_1_1_bit_7_output, mux_2_1_1_bit_8_output, mux_2_1_1_bit_9_output,
       mux_2_1_1_bit_10_output, mux_2_1_1_bit_11_output, mux_2_1_1_bit_12_output, mux_2_1_1_bit_13_output,
       mux_2_1_1_bit_14_output, mux_2_1_1_bit_15_output, mux_2_1_1_bit_16_output, xor_1_out, xor_2_out,
       xor_3_out, xor_4_out, xor_5_out, xor_6_out, xor_7_out, xor_8_out;

  Mux_2_1__1_bit mux_2_1_1_bit_1 (
    .Input_0(enable), .Input_1(Inputs[0]), .Output(mux_2_1_1_bit_1_output), .Select(load));
  Mux_2_1__1_bit mux_2_1_1_bit_2 (
    .Input_0(and_1_out), .Input_1(Inputs[1]), .Output(mux_2_1_1_bit_2_output), .Select(load));
  Mux_2_1__1_bit mux_2_1_1_bit_3 (
    .Input_0(and_2_out), .Input_1(Inputs[2]), .Output(mux_2_1_1_bit_3_output), .Select(load));
  Mux_2_1__1_bit mux_2_1_1_bit_4 (
    .Input_0(and_3_out), .Input_1(Inputs[3]), .Output(mux_2_1_1_bit_4_output), .Select(load));
  Mux_2_1__1_bit mux_2_1_1_bit_5 (
    .Input_0(and_4_out), .Input_1(Inputs[4]), .Output(mux_2_1_1_bit_5_output), .Select(load));
  Mux_2_1__1_bit mux_2_1_1_bit_6 (
    .Input_0(and_5_out), .Input_1(Inputs[5]), .Output(mux_2_1_1_bit_6_output), .Select(load));
  Mux_2_1__1_bit mux_2_1_1_bit_7 (
    .Input_0(and_6_out), .Input_1(Inputs[6]), .Output(mux_2_1_1_bit_7_output), .Select(load));
  Mux_2_1__1_bit mux_2_1_1_bit_8 (
    .Input_0(and_7_out), .Input_1(Inputs[7]), .Output(mux_2_1_1_bit_8_output), .Select(load));
  xor xor_1 (xor_1_out, load, mux_2_1_1_bit_1_output);
  xor xor_2 (xor_2_out, load, mux_2_1_1_bit_2_output);
  xor xor_3 (xor_3_out, load, mux_2_1_1_bit_3_output);
  xor xor_4 (xor_4_out, load, mux_2_1_1_bit_4_output);
  xor xor_5 (xor_5_out, load, mux_2_1_1_bit_5_output);
  xor xor_6 (xor_6_out, load, mux_2_1_1_bit_6_output);
  xor xor_7 (xor_7_out, load, mux_2_1_1_bit_7_output);
  xor xor_8 (xor_8_out, load, mux_2_1_1_bit_8_output);
  J_K_Flip_Flop j_k_ff_1 (
    .J(mux_2_1_1_bit_1_output), .clk(CLK), .K(xor_1_out), .Q(Outputs[0]), .Qn(j_k_ff_1_qn), .reset(reset));  // open: preset, en
  J_K_Flip_Flop j_k_ff_2 (
    .J(mux_2_1_1_bit_2_output), .clk(CLK), .K(xor_2_out), .Q(Outputs[1]), .Qn(j_k_ff_2_qn), .reset(reset));  // open: preset, en
  J_K_Flip_Flop j_k_ff_3 (
    .J(mux_2_1_1_bit_3_output), .clk(CLK), .K(xor_3_out), .Q(Outputs[2]), .Qn(j_k_ff_3_qn), .reset(reset));  // open: preset, en
  J_K_Flip_Flop j_k_ff_4 (
    .J(mux_2_1_1_bit_4_output), .clk(CLK), .K(xor_4_out), .Q(Outputs[3]), .Qn(j_k_ff_4_qn), .reset(reset));  // open: preset, en
  J_K_Flip_Flop j_k_ff_5 (
    .J(mux_2_1_1_bit_5_output), .clk(CLK), .K(xor_5_out), .Q(Outputs[4]), .Qn(j_k_ff_5_qn), .reset(reset));  // open: preset, en
  J_K_Flip_Flop j_k_ff_6 (
    .J(mux_2_1_1_bit_6_output), .clk(CLK), .K(xor_6_out), .Q(Outputs[5]), .Qn(j_k_ff_6_qn), .reset(reset));  // open: preset, en
  J_K_Flip_Flop j_k_ff_7 (
    .J(mux_2_1_1_bit_7_output), .clk(CLK), .K(xor_7_out), .Q(Outputs[6]), .Qn(j_k_ff_7_qn), .reset(reset));  // open: preset, en
  J_K_Flip_Flop j_k_ff_8 (
    .J(mux_2_1_1_bit_8_output), .clk(CLK), .K(xor_8_out), .Q(Outputs[7]), .Qn(j_k_ff_8_qn), .reset(reset));  // open: preset, en
  Mux_2_1__1_bit mux_2_1_1_bit_9 (
    .Input_0(Outputs[0]), .Input_1(j_k_ff_1_qn), .Output(mux_2_1_1_bit_9_output), .Select(dec_inc_));
  Mux_2_1__1_bit mux_2_1_1_bit_10 (
    .Input_0(Outputs[1]), .Input_1(j_k_ff_2_qn), .Output(mux_2_1_1_bit_10_output), .Select(dec_inc_));
  Mux_2_1__1_bit mux_2_1_1_bit_11 (
    .Input_0(Outputs[2]), .Input_1(j_k_ff_3_qn), .Output(mux_2_1_1_bit_11_output), .Select(dec_inc_));
  Mux_2_1__1_bit mux_2_1_1_bit_12 (
    .Input_0(Outputs[3]), .Input_1(j_k_ff_4_qn), .Output(mux_2_1_1_bit_12_output), .Select(dec_inc_));
  Mux_2_1__1_bit mux_2_1_1_bit_13 (
    .Input_0(Outputs[4]), .Input_1(j_k_ff_5_qn), .Output(mux_2_1_1_bit_13_output), .Select(dec_inc_));
  Mux_2_1__1_bit mux_2_1_1_bit_14 (
    .Input_0(Outputs[5]), .Input_1(j_k_ff_6_qn), .Output(mux_2_1_1_bit_14_output), .Select(dec_inc_));
  Mux_2_1__1_bit mux_2_1_1_bit_15 (
    .Input_0(Outputs[6]), .Input_1(j_k_ff_7_qn), .Output(mux_2_1_1_bit_15_output), .Select(dec_inc_));
  Mux_2_1__1_bit mux_2_1_1_bit_16 (
    .Input_0(Outputs[7]), .Input_1(j_k_ff_8_qn), .Output(mux_2_1_1_bit_16_output), .Select(dec_inc_));
  and and_1 (and_1_out, mux_2_1_1_bit_9_output, enable);
  and and_2 (and_2_out, mux_2_1_1_bit_10_output, and_1_out);
  and and_3 (and_3_out, mux_2_1_1_bit_11_output, and_2_out);
  and and_4 (and_4_out, mux_2_1_1_bit_12_output, and_3_out);
  and and_5 (and_5_out, mux_2_1_1_bit_13_output, and_4_out);
  and and_6 (and_6_out, mux_2_1_1_bit_14_output, and_5_out);
  and and_7 (and_7_out, mux_2_1_1_bit_15_output, and_6_out);
  and and_8 (Cout, mux_2_1_1_bit_16_output, and_7_out);

  // Notes on the sheet:
  //   load: pull=up
  //   enable: pull=up
  //   8 bits universal counter
endmodule

// PC-lo
module PC_lo__Program_Counter_Low (
  input  inc,
  input  load,
  input  CLK,
  input  reset,
  input  [7:0] Inputs,
  output [7:0] Outputs,
  output Cout
);

  wire and_1_out, and_2_out, and_3_out, and_4_out, and_5_out, and_6_out, and_7_out, mux_2_1_1_bit_1_output,
       mux_2_1_1_bit_2_output, mux_2_1_1_bit_3_output, mux_2_1_1_bit_4_output, mux_2_1_1_bit_5_output,
       mux_2_1_1_bit_6_output, mux_2_1_1_bit_7_output, mux_2_1_1_bit_8_output, xor_1_out, xor_2_out,
       xor_3_out, xor_4_out, xor_5_out, xor_6_out, xor_7_out, xor_8_out;

  Mux_2_1__1_bit mux_2_1_1_bit_1 (.Input_0(inc), .Input_1(Inputs[0]), .Output(mux_2_1_1_bit_1_output), .Select(load));
  Mux_2_1__1_bit mux_2_1_1_bit_2 (
    .Input_0(and_1_out), .Input_1(Inputs[1]), .Output(mux_2_1_1_bit_2_output), .Select(load));
  Mux_2_1__1_bit mux_2_1_1_bit_3 (
    .Input_0(and_2_out), .Input_1(Inputs[2]), .Output(mux_2_1_1_bit_3_output), .Select(load));
  Mux_2_1__1_bit mux_2_1_1_bit_4 (
    .Input_0(and_3_out), .Input_1(Inputs[3]), .Output(mux_2_1_1_bit_4_output), .Select(load));
  Mux_2_1__1_bit mux_2_1_1_bit_5 (
    .Input_0(and_4_out), .Input_1(Inputs[4]), .Output(mux_2_1_1_bit_5_output), .Select(load));
  Mux_2_1__1_bit mux_2_1_1_bit_6 (
    .Input_0(and_5_out), .Input_1(Inputs[5]), .Output(mux_2_1_1_bit_6_output), .Select(load));
  Mux_2_1__1_bit mux_2_1_1_bit_7 (
    .Input_0(and_6_out), .Input_1(Inputs[6]), .Output(mux_2_1_1_bit_7_output), .Select(load));
  Mux_2_1__1_bit mux_2_1_1_bit_8 (
    .Input_0(and_7_out), .Input_1(Inputs[7]), .Output(mux_2_1_1_bit_8_output), .Select(load));
  xor xor_1 (xor_1_out, load, mux_2_1_1_bit_1_output);
  xor xor_2 (xor_2_out, load, mux_2_1_1_bit_2_output);
  xor xor_3 (xor_3_out, load, mux_2_1_1_bit_3_output);
  xor xor_4 (xor_4_out, load, mux_2_1_1_bit_4_output);
  xor xor_5 (xor_5_out, load, mux_2_1_1_bit_5_output);
  xor xor_6 (xor_6_out, load, mux_2_1_1_bit_6_output);
  xor xor_7 (xor_7_out, load, mux_2_1_1_bit_7_output);
  xor xor_8 (xor_8_out, load, mux_2_1_1_bit_8_output);
  J_K_Flip_Flop j_k_ff_1 (
    .J(mux_2_1_1_bit_1_output), .clk(CLK), .K(xor_1_out), .Q(Outputs[0]), .reset(reset));  // open: Qn, preset, en
  and and_1 (and_1_out, Outputs[0], inc);
  J_K_Flip_Flop j_k_ff_2 (
    .J(mux_2_1_1_bit_2_output), .clk(CLK), .K(xor_2_out), .Q(Outputs[1]), .reset(reset));  // open: Qn, preset, en
  and and_2 (and_2_out, Outputs[1], and_1_out);
  J_K_Flip_Flop j_k_ff_3 (
    .J(mux_2_1_1_bit_3_output), .clk(CLK), .K(xor_3_out), .Q(Outputs[2]), .reset(reset));  // open: Qn, preset, en
  and and_3 (and_3_out, Outputs[2], and_2_out);
  J_K_Flip_Flop j_k_ff_4 (
    .J(mux_2_1_1_bit_4_output), .clk(CLK), .K(xor_4_out), .Q(Outputs[3]), .reset(reset));  // open: Qn, preset, en
  and and_4 (and_4_out, Outputs[3], and_3_out);
  J_K_Flip_Flop j_k_ff_5 (
    .J(mux_2_1_1_bit_5_output), .clk(CLK), .K(xor_5_out), .Q(Outputs[4]), .reset(reset));  // open: Qn, preset, en
  and and_5 (and_5_out, Outputs[4], and_4_out);
  J_K_Flip_Flop j_k_ff_6 (
    .J(mux_2_1_1_bit_6_output), .clk(CLK), .K(xor_6_out), .Q(Outputs[5]), .reset(reset));  // open: Qn, preset, en
  and and_6 (and_6_out, Outputs[5], and_5_out);
  J_K_Flip_Flop j_k_ff_7 (
    .J(mux_2_1_1_bit_7_output), .clk(CLK), .K(xor_7_out), .Q(Outputs[6]), .reset(reset));  // open: Qn, preset, en
  and and_7 (and_7_out, Outputs[6], and_6_out);
  J_K_Flip_Flop j_k_ff_8 (
    .J(mux_2_1_1_bit_8_output), .clk(CLK), .K(xor_8_out), .Q(Outputs[7]), .reset(reset));  // open: Qn, preset, en
  and and_8 (Cout, Outputs[7], and_7_out);

  // Notes on the sheet:
  //   load: pull=up
  //   inc: pull=up
  //   8 bits counter
endmodule

// Acc
module A__Accumulator (
  input  clk,
  input  write_enable,
  input  [7:0] \input ,
  output [7:0] \output 
);

  D_Flip_Flop d_ff_1 (.clk(clk), .D(\input [0]), .Q(\output [0]), .en(write_enable));  // open: Qn, preset, reset
  D_Flip_Flop d_ff_2 (.clk(clk), .D(\input [1]), .Q(\output [1]), .en(write_enable));  // open: Qn, preset, reset
  D_Flip_Flop d_ff_3 (.clk(clk), .D(\input [2]), .Q(\output [2]), .en(write_enable));  // open: Qn, preset, reset
  D_Flip_Flop d_ff_4 (.clk(clk), .D(\input [3]), .Q(\output [3]), .en(write_enable));  // open: Qn, preset, reset
  D_Flip_Flop d_ff_5 (.clk(clk), .D(\input [4]), .Q(\output [4]), .en(write_enable));  // open: Qn, preset, reset
  D_Flip_Flop d_ff_6 (.clk(clk), .D(\input [5]), .Q(\output [5]), .en(write_enable));  // open: Qn, preset, reset
  D_Flip_Flop d_ff_7 (.clk(clk), .D(\input [6]), .Q(\output [6]), .en(write_enable));  // open: Qn, preset, reset
  D_Flip_Flop d_ff_8 (.clk(clk), .D(\input [7]), .Q(\output [7]), .en(write_enable));  // open: Qn, preset, reset

  // Notes on the sheet:
  //   8 bits register
endmodule

// X
module X__Index_X (
  input  clk,
  input  write_enable,
  input  [7:0] \input ,
  output [7:0] \output 
);

  D_Flip_Flop d_ff_1 (.clk(clk), .D(\input [0]), .Q(\output [0]), .en(write_enable));  // open: Qn, preset, reset
  D_Flip_Flop d_ff_2 (.clk(clk), .D(\input [1]), .Q(\output [1]), .en(write_enable));  // open: Qn, preset, reset
  D_Flip_Flop d_ff_3 (.clk(clk), .D(\input [2]), .Q(\output [2]), .en(write_enable));  // open: Qn, preset, reset
  D_Flip_Flop d_ff_4 (.clk(clk), .D(\input [3]), .Q(\output [3]), .en(write_enable));  // open: Qn, preset, reset
  D_Flip_Flop d_ff_5 (.clk(clk), .D(\input [4]), .Q(\output [4]), .en(write_enable));  // open: Qn, preset, reset
  D_Flip_Flop d_ff_6 (.clk(clk), .D(\input [5]), .Q(\output [5]), .en(write_enable));  // open: Qn, preset, reset
  D_Flip_Flop d_ff_7 (.clk(clk), .D(\input [6]), .Q(\output [6]), .en(write_enable));  // open: Qn, preset, reset
  D_Flip_Flop d_ff_8 (.clk(clk), .D(\input [7]), .Q(\output [7]), .en(write_enable));  // open: Qn, preset, reset

  // Notes on the sheet:
  //   8 bits register
endmodule

// Y
module Y__Index_Y (
  input  clk,
  input  write_enable,
  input  [7:0] \input ,
  output [7:0] \output 
);

  D_Flip_Flop d_ff_1 (.clk(clk), .D(\input [0]), .Q(\output [0]), .en(write_enable));  // open: Qn, preset, reset
  D_Flip_Flop d_ff_2 (.clk(clk), .D(\input [1]), .Q(\output [1]), .en(write_enable));  // open: Qn, preset, reset
  D_Flip_Flop d_ff_3 (.clk(clk), .D(\input [2]), .Q(\output [2]), .en(write_enable));  // open: Qn, preset, reset
  D_Flip_Flop d_ff_4 (.clk(clk), .D(\input [3]), .Q(\output [3]), .en(write_enable));  // open: Qn, preset, reset
  D_Flip_Flop d_ff_5 (.clk(clk), .D(\input [4]), .Q(\output [4]), .en(write_enable));  // open: Qn, preset, reset
  D_Flip_Flop d_ff_6 (.clk(clk), .D(\input [5]), .Q(\output [5]), .en(write_enable));  // open: Qn, preset, reset
  D_Flip_Flop d_ff_7 (.clk(clk), .D(\input [6]), .Q(\output [6]), .en(write_enable));  // open: Qn, preset, reset
  D_Flip_Flop d_ff_8 (.clk(clk), .D(\input [7]), .Q(\output [7]), .en(write_enable));  // open: Qn, preset, reset

  // Notes on the sheet:
  //   8 bits register
endmodule

// SP
module S__Stack_Pointer (
  input  clk,
  input  write_enable,
  input  [7:0] \input ,
  output [7:0] \output 
);

  D_Flip_Flop d_ff_1 (.clk(clk), .D(\input [0]), .Q(\output [0]), .en(write_enable));  // open: Qn, preset, reset
  D_Flip_Flop d_ff_2 (.clk(clk), .D(\input [1]), .Q(\output [1]), .en(write_enable));  // open: Qn, preset, reset
  D_Flip_Flop d_ff_3 (.clk(clk), .D(\input [2]), .Q(\output [2]), .en(write_enable));  // open: Qn, preset, reset
  D_Flip_Flop d_ff_4 (.clk(clk), .D(\input [3]), .Q(\output [3]), .en(write_enable));  // open: Qn, preset, reset
  D_Flip_Flop d_ff_5 (.clk(clk), .D(\input [4]), .Q(\output [4]), .en(write_enable));  // open: Qn, preset, reset
  D_Flip_Flop d_ff_6 (.clk(clk), .D(\input [5]), .Q(\output [5]), .en(write_enable));  // open: Qn, preset, reset
  D_Flip_Flop d_ff_7 (.clk(clk), .D(\input [6]), .Q(\output [6]), .en(write_enable));  // open: Qn, preset, reset
  D_Flip_Flop d_ff_8 (.clk(clk), .D(\input [7]), .Q(\output [7]), .en(write_enable));  // open: Qn, preset, reset

  // Notes on the sheet:
  //   8 bits register
endmodule

// Flags Register (P)
module Flags__Status_Processor_Register (
  input  clk,
  input  N_in,
  input  V_in,
  input  B_in,
  input  Z_in,
  input  C_in,
  input  cfg2,
  input  cfg1,
  input  cfg0,
  input  F2,
  input  F1,
  input  F0,
  input  [7:0] Memory_input,
  input  SO,
  output [7:0] processor_status_register_output,
  output N_out,
  output V_out,
  output out,
  output B_out,
  output D_out,
  output I_out,
  output Z_out,
  output C_out
);

  wire and_1_out, and_2_out, and_3_out, and_4_out, and_5_out, and_6_out, and_7_out, and_8_out, and_9_out,
       and_10_out, controlled_buffer_1_out, controlled_buffer_2_out, controlled_buffer_3_out,
       controlled_buffer_4_out, controlled_buffer_5_out, controlled_buffer_6_out, controlled_buffer_7_out,
       controlled_buffer_8_out, controlled_buffer_9_out, decoder_3_8_1_bit_1_output_0,
       decoder_3_8_1_bit_1_output_1, decoder_3_8_1_bit_1_output_2, decoder_3_8_1_bit_1_output_6,
       decoder_3_8_1_bit_1_output_7, not_1_out, not_2_out, or_1_out, or_2_out, or_3_out, or_4_out, undriven;
  wire [7:0] mux_2_1_8_bits_1_output;

  Mux_2_1__8_bits mux_2_1_8_bits_1 (
    .Input_0({N_in, V_in, 4'b0000, Z_in, C_in}), .Input_1(Memory_input), .Output(mux_2_1_8_bits_1_output),
    .Select(and_3_out));
  not not_1 (not_1_out, clk);
  and and_1 (and_1_out, clk, not_1_out, and_4_out);
  not not_2 (not_2_out, clk);
  and and_2 (and_2_out, clk, not_2_out, and_6_out);
  assign controlled_buffer_1_out = and_2_out ? decoder_3_8_1_bit_1_output_7 : 1'bz;  // Controlled_Buffer controlled_buffer_1
  assign controlled_buffer_2_out = and_1_out ? decoder_3_8_1_bit_1_output_7 : 1'bz;  // Controlled_Buffer controlled_buffer_2
  and and_3 (and_3_out, cfg2, cfg1);
  D_Flip_Flop d_ff_1 (
    .clk(clk), .D(mux_2_1_8_bits_1_output[7]), .Q(N_out), .preset(controlled_buffer_2_out), .en(or_1_out),
    .reset(controlled_buffer_1_out));  // open: Qn
  and and_4 (and_4_out, cfg2, ~cfg1, ~cfg0);  // AND_Gate
  D_Flip_Flop d_ff_2 (
    .clk(clk), .D(mux_2_1_8_bits_1_output[6]), .Q(processor_status_register_output[6]), .preset(SO),
    .en(or_2_out), .reset(controlled_buffer_3_out));  // open: Qn
  assign controlled_buffer_3_out = and_2_out ? decoder_3_8_1_bit_1_output_6 : 1'bz;  // Controlled_Buffer controlled_buffer_3
  and and_5 (and_5_out, ~cfg2, cfg0);  // AND_Gate
  and and_6 (and_6_out, cfg2, ~cfg1, cfg0);  // AND_Gate
  or or_1 (or_1_out, and_5_out, cfg1);
  D_Flip_Flop d_ff_3 (.clk(clk), .Q(out), .preset(1'b1), .en(1'b0), .reset(1'b0));  // open: D, Qn
  and and_7 (and_7_out, cfg2, cfg1);
  and and_8 (and_8_out, cfg2, cfg1, cfg0);
  or or_2 (or_2_out, and_7_out, and_9_out);
  D_Flip_Flop d_ff_4 (.clk(clk));  // open: D, Q, Qn, preset, en, reset
  and and_9 (and_9_out, cfg1, cfg0);
  and and_10 (and_10_out, ~cfg2, cfg1);  // AND_Gate
  or or_3 (or_3_out, and_5_out, and_9_out, and_10_out);
  or or_4 (or_4_out, and_9_out, and_10_out);
  D_Flip_Flop d_ff_5 (.clk(clk), .D(undriven), .Q(D_out), .preset(1'b0), .en(1'b0), .reset(1'b1));  // open: Qn
  assign controlled_buffer_4_out = and_1_out ? decoder_3_8_1_bit_1_output_2 : 1'bz;  // Controlled_Buffer controlled_buffer_4
  D_Flip_Flop d_ff_6 (
    .clk(clk), .D(mux_2_1_8_bits_1_output[2]), .Q(I_out), .preset(controlled_buffer_4_out), .en(and_8_out),
    .reset(controlled_buffer_5_out));  // open: Qn
  assign controlled_buffer_5_out = and_2_out ? decoder_3_8_1_bit_1_output_2 : 1'bz;  // Controlled_Buffer controlled_buffer_5
  Decoder_3_8__1_bit decoder_3_8_1_bit_1 (
    .output_0(decoder_3_8_1_bit_1_output_0), .output_1(decoder_3_8_1_bit_1_output_1),
    .output_2(decoder_3_8_1_bit_1_output_2), .output_6(decoder_3_8_1_bit_1_output_6),
    .output_7(decoder_3_8_1_bit_1_output_7), .Input_2(F2), .Input_1(F1), .Input_0(F0));  // open: output_3, output_4, output_5
  D_Flip_Flop d_ff_7 (
    .clk(clk), .D(mux_2_1_8_bits_1_output[1]), .Q(processor_status_register_output[1]),
    .preset(controlled_buffer_7_out), .en(or_3_out), .reset(controlled_buffer_6_out));  // open: Qn
  assign controlled_buffer_6_out = and_2_out ? decoder_3_8_1_bit_1_output_1 : 1'bz;  // Controlled_Buffer controlled_buffer_6
  assign controlled_buffer_7_out = and_1_out ? decoder_3_8_1_bit_1_output_1 : 1'bz;  // Controlled_Buffer controlled_buffer_7
  D_Flip_Flop d_ff_8 (
    .clk(clk), .D(mux_2_1_8_bits_1_output[0]), .Q(C_out), .preset(controlled_buffer_9_out), .en(or_4_out),
    .reset(controlled_buffer_8_out));  // open: Qn
  assign controlled_buffer_8_out = and_2_out ? decoder_3_8_1_bit_1_output_0 : 1'bz;  // Controlled_Buffer controlled_buffer_8
  assign controlled_buffer_9_out = and_1_out ? decoder_3_8_1_bit_1_output_0 : 1'bz;  // Controlled_Buffer controlled_buffer_9

  assign B_out = B_in;
  assign {processor_status_register_output[7], processor_status_register_output[5:2], processor_status_register_output[0]} = {N_out, out, B_in, D_out, I_out, C_out};
  assign V_out = processor_status_register_output[6];
  assign Z_out = processor_status_register_output[1];

  // Notes on the sheet:
  //   rising edge
  //   pulse circuit
  //   Note : the pulse circuit prevent flipflop asynchronous set/reset to last all the clock period, which risks to spread to the next period
  //   Flags controller
endmodule

// OUT
module OUT__Data_output_register (
  input  clk,
  input  write_enable,
  input  [7:0] \input ,
  output [7:0] \output 
);

  D_Flip_Flop d_ff_1 (.clk(clk), .D(\input [0]), .Q(\output [0]), .en(write_enable));  // open: Qn, preset, reset
  D_Flip_Flop d_ff_2 (.clk(clk), .D(\input [1]), .Q(\output [1]), .en(write_enable));  // open: Qn, preset, reset
  D_Flip_Flop d_ff_3 (.clk(clk), .D(\input [2]), .Q(\output [2]), .en(write_enable));  // open: Qn, preset, reset
  D_Flip_Flop d_ff_4 (.clk(clk), .D(\input [3]), .Q(\output [3]), .en(write_enable));  // open: Qn, preset, reset
  D_Flip_Flop d_ff_5 (.clk(clk), .D(\input [4]), .Q(\output [4]), .en(write_enable));  // open: Qn, preset, reset
  D_Flip_Flop d_ff_6 (.clk(clk), .D(\input [5]), .Q(\output [5]), .en(write_enable));  // open: Qn, preset, reset
  D_Flip_Flop d_ff_7 (.clk(clk), .D(\input [6]), .Q(\output [6]), .en(write_enable));  // open: Qn, preset, reset
  D_Flip_Flop d_ff_8 (.clk(clk), .D(\input [7]), .Q(\output [7]), .en(write_enable));  // open: Qn, preset, reset

  // Notes on the sheet:
  //   8 bits register
endmodule

// AB-hi
module Address_Bus__high (
  input  clk,
  input  write_enable,
  input  [7:0] \input ,
  output [7:0] \output 
);

  D_Flip_Flop d_ff_1 (.clk(clk), .D(\input [0]), .Q(\output [0]), .en(write_enable));  // open: Qn, preset, reset
  D_Flip_Flop d_ff_2 (.clk(clk), .D(\input [1]), .Q(\output [1]), .en(write_enable));  // open: Qn, preset, reset
  D_Flip_Flop d_ff_3 (.clk(clk), .D(\input [2]), .Q(\output [2]), .en(write_enable));  // open: Qn, preset, reset
  D_Flip_Flop d_ff_4 (.clk(clk), .D(\input [3]), .Q(\output [3]), .en(write_enable));  // open: Qn, preset, reset
  D_Flip_Flop d_ff_5 (.clk(clk), .D(\input [4]), .Q(\output [4]), .en(write_enable));  // open: Qn, preset, reset
  D_Flip_Flop d_ff_6 (.clk(clk), .D(\input [5]), .Q(\output [5]), .en(write_enable));  // open: Qn, preset, reset
  D_Flip_Flop d_ff_7 (.clk(clk), .D(\input [6]), .Q(\output [6]), .en(write_enable));  // open: Qn, preset, reset
  D_Flip_Flop d_ff_8 (.clk(clk), .D(\input [7]), .Q(\output [7]), .en(write_enable));  // open: Qn, preset, reset

  // Notes on the sheet:
  //   8 bits register
endmodule

// AB-lo
module Address_Bus__low_register (
  input  inc,
  input  load,
  input  CLK,
  input  reset,
  input  [7:0] Inputs,
  output [7:0] Outputs,
  output Cout
);

  wire and_1_out, and_2_out, and_3_out, and_4_out, and_5_out, and_6_out, and_7_out, mux_2_1_1_bit_1_output,
       mux_2_1_1_bit_2_output, mux_2_1_1_bit_3_output, mux_2_1_1_bit_4_output, mux_2_1_1_bit_5_output,
       mux_2_1_1_bit_6_output, mux_2_1_1_bit_7_output, mux_2_1_1_bit_8_output, xor_1_out, xor_2_out,
       xor_3_out, xor_4_out, xor_5_out, xor_6_out, xor_7_out, xor_8_out;

  Mux_2_1__1_bit mux_2_1_1_bit_1 (.Input_0(inc), .Input_1(Inputs[0]), .Output(mux_2_1_1_bit_1_output), .Select(load));
  Mux_2_1__1_bit mux_2_1_1_bit_2 (
    .Input_0(and_1_out), .Input_1(Inputs[1]), .Output(mux_2_1_1_bit_2_output), .Select(load));
  Mux_2_1__1_bit mux_2_1_1_bit_3 (
    .Input_0(and_2_out), .Input_1(Inputs[2]), .Output(mux_2_1_1_bit_3_output), .Select(load));
  Mux_2_1__1_bit mux_2_1_1_bit_4 (
    .Input_0(and_3_out), .Input_1(Inputs[3]), .Output(mux_2_1_1_bit_4_output), .Select(load));
  Mux_2_1__1_bit mux_2_1_1_bit_5 (
    .Input_0(and_4_out), .Input_1(Inputs[4]), .Output(mux_2_1_1_bit_5_output), .Select(load));
  Mux_2_1__1_bit mux_2_1_1_bit_6 (
    .Input_0(and_5_out), .Input_1(Inputs[5]), .Output(mux_2_1_1_bit_6_output), .Select(load));
  Mux_2_1__1_bit mux_2_1_1_bit_7 (
    .Input_0(and_6_out), .Input_1(Inputs[6]), .Output(mux_2_1_1_bit_7_output), .Select(load));
  Mux_2_1__1_bit mux_2_1_1_bit_8 (
    .Input_0(and_7_out), .Input_1(Inputs[7]), .Output(mux_2_1_1_bit_8_output), .Select(load));
  xor xor_1 (xor_1_out, load, mux_2_1_1_bit_1_output);
  xor xor_2 (xor_2_out, load, mux_2_1_1_bit_2_output);
  xor xor_3 (xor_3_out, load, mux_2_1_1_bit_3_output);
  xor xor_4 (xor_4_out, load, mux_2_1_1_bit_4_output);
  xor xor_5 (xor_5_out, load, mux_2_1_1_bit_5_output);
  xor xor_6 (xor_6_out, load, mux_2_1_1_bit_6_output);
  xor xor_7 (xor_7_out, load, mux_2_1_1_bit_7_output);
  xor xor_8 (xor_8_out, load, mux_2_1_1_bit_8_output);
  J_K_Flip_Flop j_k_ff_1 (
    .J(mux_2_1_1_bit_1_output), .clk(CLK), .K(xor_1_out), .Q(Outputs[0]), .reset(reset));  // open: Qn, preset, en
  and and_1 (and_1_out, Outputs[0], inc);
  J_K_Flip_Flop j_k_ff_2 (
    .J(mux_2_1_1_bit_2_output), .clk(CLK), .K(xor_2_out), .Q(Outputs[1]), .reset(reset));  // open: Qn, preset, en
  and and_2 (and_2_out, Outputs[1], and_1_out);
  J_K_Flip_Flop j_k_ff_3 (
    .J(mux_2_1_1_bit_3_output), .clk(CLK), .K(xor_3_out), .Q(Outputs[2]), .reset(reset));  // open: Qn, preset, en
  and and_3 (and_3_out, Outputs[2], and_2_out);
  J_K_Flip_Flop j_k_ff_4 (
    .J(mux_2_1_1_bit_4_output), .clk(CLK), .K(xor_4_out), .Q(Outputs[3]), .reset(reset));  // open: Qn, preset, en
  and and_4 (and_4_out, Outputs[3], and_3_out);
  J_K_Flip_Flop j_k_ff_5 (
    .J(mux_2_1_1_bit_5_output), .clk(CLK), .K(xor_5_out), .Q(Outputs[4]), .reset(reset));  // open: Qn, preset, en
  and and_5 (and_5_out, Outputs[4], and_4_out);
  J_K_Flip_Flop j_k_ff_6 (
    .J(mux_2_1_1_bit_6_output), .clk(CLK), .K(xor_6_out), .Q(Outputs[5]), .reset(reset));  // open: Qn, preset, en
  and and_6 (and_6_out, Outputs[5], and_5_out);
  J_K_Flip_Flop j_k_ff_7 (
    .J(mux_2_1_1_bit_7_output), .clk(CLK), .K(xor_7_out), .Q(Outputs[6]), .reset(reset));  // open: Qn, preset, en
  and and_7 (and_7_out, Outputs[6], and_6_out);
  J_K_Flip_Flop j_k_ff_8 (
    .J(mux_2_1_1_bit_8_output), .clk(CLK), .K(xor_8_out), .Q(Outputs[7]), .reset(reset));  // open: Qn, preset, en
  and and_8 (Cout, Outputs[7], and_7_out);

  // Notes on the sheet:
  //   inc: pull=up
  //   load: pull=up
  //   8 bits counter
endmodule

// Address-hi
module Address_hi__Adress_high (
  input  inc,
  input  load,
  input  CLK,
  input  reset,
  input  [7:0] Inputs,
  output [7:0] Outputs,
  output Cout
);

  wire and_1_out, and_2_out, and_3_out, and_4_out, and_5_out, and_6_out, and_7_out, mux_2_1_1_bit_1_output,
       mux_2_1_1_bit_2_output, mux_2_1_1_bit_3_output, mux_2_1_1_bit_4_output, mux_2_1_1_bit_5_output,
       mux_2_1_1_bit_6_output, mux_2_1_1_bit_7_output, mux_2_1_1_bit_8_output, xor_1_out, xor_2_out,
       xor_3_out, xor_4_out, xor_5_out, xor_6_out, xor_7_out, xor_8_out;

  Mux_2_1__1_bit mux_2_1_1_bit_1 (.Input_0(inc), .Input_1(Inputs[0]), .Output(mux_2_1_1_bit_1_output), .Select(load));
  Mux_2_1__1_bit mux_2_1_1_bit_2 (
    .Input_0(and_1_out), .Input_1(Inputs[1]), .Output(mux_2_1_1_bit_2_output), .Select(load));
  Mux_2_1__1_bit mux_2_1_1_bit_3 (
    .Input_0(and_2_out), .Input_1(Inputs[2]), .Output(mux_2_1_1_bit_3_output), .Select(load));
  Mux_2_1__1_bit mux_2_1_1_bit_4 (
    .Input_0(and_3_out), .Input_1(Inputs[3]), .Output(mux_2_1_1_bit_4_output), .Select(load));
  Mux_2_1__1_bit mux_2_1_1_bit_5 (
    .Input_0(and_4_out), .Input_1(Inputs[4]), .Output(mux_2_1_1_bit_5_output), .Select(load));
  Mux_2_1__1_bit mux_2_1_1_bit_6 (
    .Input_0(and_5_out), .Input_1(Inputs[5]), .Output(mux_2_1_1_bit_6_output), .Select(load));
  Mux_2_1__1_bit mux_2_1_1_bit_7 (
    .Input_0(and_6_out), .Input_1(Inputs[6]), .Output(mux_2_1_1_bit_7_output), .Select(load));
  Mux_2_1__1_bit mux_2_1_1_bit_8 (
    .Input_0(and_7_out), .Input_1(Inputs[7]), .Output(mux_2_1_1_bit_8_output), .Select(load));
  xor xor_1 (xor_1_out, load, mux_2_1_1_bit_1_output);
  xor xor_2 (xor_2_out, load, mux_2_1_1_bit_2_output);
  xor xor_3 (xor_3_out, load, mux_2_1_1_bit_3_output);
  xor xor_4 (xor_4_out, load, mux_2_1_1_bit_4_output);
  xor xor_5 (xor_5_out, load, mux_2_1_1_bit_5_output);
  xor xor_6 (xor_6_out, load, mux_2_1_1_bit_6_output);
  xor xor_7 (xor_7_out, load, mux_2_1_1_bit_7_output);
  xor xor_8 (xor_8_out, load, mux_2_1_1_bit_8_output);
  J_K_Flip_Flop j_k_ff_1 (
    .J(mux_2_1_1_bit_1_output), .clk(CLK), .K(xor_1_out), .Q(Outputs[0]), .reset(reset));  // open: Qn, preset, en
  and and_1 (and_1_out, Outputs[0], inc);
  J_K_Flip_Flop j_k_ff_2 (
    .J(mux_2_1_1_bit_2_output), .clk(CLK), .K(xor_2_out), .Q(Outputs[1]), .reset(reset));  // open: Qn, preset, en
  and and_2 (and_2_out, Outputs[1], and_1_out);
  J_K_Flip_Flop j_k_ff_3 (
    .J(mux_2_1_1_bit_3_output), .clk(CLK), .K(xor_3_out), .Q(Outputs[2]), .reset(reset));  // open: Qn, preset, en
  and and_3 (and_3_out, Outputs[2], and_2_out);
  J_K_Flip_Flop j_k_ff_4 (
    .J(mux_2_1_1_bit_4_output), .clk(CLK), .K(xor_4_out), .Q(Outputs[3]), .reset(reset));  // open: Qn, preset, en
  and and_4 (and_4_out, Outputs[3], and_3_out);
  J_K_Flip_Flop j_k_ff_5 (
    .J(mux_2_1_1_bit_5_output), .clk(CLK), .K(xor_5_out), .Q(Outputs[4]), .reset(reset));  // open: Qn, preset, en
  and and_5 (and_5_out, Outputs[4], and_4_out);
  J_K_Flip_Flop j_k_ff_6 (
    .J(mux_2_1_1_bit_6_output), .clk(CLK), .K(xor_6_out), .Q(Outputs[5]), .reset(reset));  // open: Qn, preset, en
  and and_6 (and_6_out, Outputs[5], and_5_out);
  J_K_Flip_Flop j_k_ff_7 (
    .J(mux_2_1_1_bit_7_output), .clk(CLK), .K(xor_7_out), .Q(Outputs[6]), .reset(reset));  // open: Qn, preset, en
  and and_7 (and_7_out, Outputs[6], and_6_out);
  J_K_Flip_Flop j_k_ff_8 (
    .J(mux_2_1_1_bit_8_output), .clk(CLK), .K(xor_8_out), .Q(Outputs[7]), .reset(reset));  // open: Qn, preset, en
  and and_8 (Cout, Outputs[7], and_7_out);

  // Notes on the sheet:
  //   inc: pull=up
  //   load: pull=up
  //   8 bits counter
endmodule

// Address-lo
module Address_lo__Adress_low (
  input  clk,
  input  write_enable,
  input  [7:0] \input ,
  output [7:0] \output 
);

  D_Flip_Flop d_ff_1 (.clk(clk), .D(\input [0]), .Q(\output [0]), .en(write_enable));  // open: Qn, preset, reset
  D_Flip_Flop d_ff_2 (.clk(clk), .D(\input [1]), .Q(\output [1]), .en(write_enable));  // open: Qn, preset, reset
  D_Flip_Flop d_ff_3 (.clk(clk), .D(\input [2]), .Q(\output [2]), .en(write_enable));  // open: Qn, preset, reset
  D_Flip_Flop d_ff_4 (.clk(clk), .D(\input [3]), .Q(\output [3]), .en(write_enable));  // open: Qn, preset, reset
  D_Flip_Flop d_ff_5 (.clk(clk), .D(\input [4]), .Q(\output [4]), .en(write_enable));  // open: Qn, preset, reset
  D_Flip_Flop d_ff_6 (.clk(clk), .D(\input [5]), .Q(\output [5]), .en(write_enable));  // open: Qn, preset, reset
  D_Flip_Flop d_ff_7 (.clk(clk), .D(\input [6]), .Q(\output [6]), .en(write_enable));  // open: Qn, preset, reset
  D_Flip_Flop d_ff_8 (.clk(clk), .D(\input [7]), .Q(\output [7]), .en(write_enable));  // open: Qn, preset, reset

  // Notes on the sheet:
  //   8 bits register
endmodule

// TMP
module TMP__Temporary_register (
  input  clk,
  input  write_enable,
  input  [7:0] \input ,
  output [7:0] \output 
);

  D_Flip_Flop d_ff_1 (.clk(clk), .D(\input [0]), .Q(\output [0]), .en(write_enable));  // open: Qn, preset, reset
  D_Flip_Flop d_ff_2 (.clk(clk), .D(\input [1]), .Q(\output [1]), .en(write_enable));  // open: Qn, preset, reset
  D_Flip_Flop d_ff_3 (.clk(clk), .D(\input [2]), .Q(\output [2]), .en(write_enable));  // open: Qn, preset, reset
  D_Flip_Flop d_ff_4 (.clk(clk), .D(\input [3]), .Q(\output [3]), .en(write_enable));  // open: Qn, preset, reset
  D_Flip_Flop d_ff_5 (.clk(clk), .D(\input [4]), .Q(\output [4]), .en(write_enable));  // open: Qn, preset, reset
  D_Flip_Flop d_ff_6 (.clk(clk), .D(\input [5]), .Q(\output [5]), .en(write_enable));  // open: Qn, preset, reset
  D_Flip_Flop d_ff_7 (.clk(clk), .D(\input [6]), .Q(\output [6]), .en(write_enable));  // open: Qn, preset, reset
  D_Flip_Flop d_ff_8 (.clk(clk), .D(\input [7]), .Q(\output [7]), .en(write_enable));  // open: Qn, preset, reset

  // Notes on the sheet:
  //   8 bits register
endmodule

// SC
module SC__Sequencer_Controller (
  input  Interrupt,
  input  SYNC,
  input  [1:0] Command,
  output Operation_Mapper_Address_Mode_Mapper_,
  output Load_Mapper_Brench_,
  output Load_CAR_,
  output reset
);

  and and_1 (reset, Interrupt, SYNC);
  or or_1 (Load_CAR_, Command[1], Command[0]);

  assign Load_Mapper_Brench_ = Command[1];
  assign Operation_Mapper_Address_Mode_Mapper_ = Command[0];
endmodule

// CAR
module CAR__Control_Address_Register (
  input  load_inc_,
  input  CLK,
  input  reset,
  input  [7:0] Inputs,
  output [7:0] Outputs,
  output Cout
);

  wire and_1_out, and_2_out, and_3_out, and_4_out, and_5_out, and_6_out, and_7_out, mux_2_1_1_bit_1_output,
       mux_2_1_1_bit_2_output, mux_2_1_1_bit_3_output, mux_2_1_1_bit_4_output, mux_2_1_1_bit_5_output,
       mux_2_1_1_bit_6_output, mux_2_1_1_bit_7_output, mux_2_1_1_bit_8_output, not_1_out, xor_1_out,
       xor_2_out, xor_3_out, xor_4_out, xor_5_out, xor_6_out, xor_7_out, xor_8_out;

  not not_1 (not_1_out, load_inc_);
  Mux_2_1__1_bit mux_2_1_1_bit_1 (
    .Input_0(not_1_out), .Input_1(Inputs[0]), .Output(mux_2_1_1_bit_1_output), .Select(load_inc_));
  Mux_2_1__1_bit mux_2_1_1_bit_2 (
    .Input_0(and_1_out), .Input_1(Inputs[1]), .Output(mux_2_1_1_bit_2_output), .Select(load_inc_));
  Mux_2_1__1_bit mux_2_1_1_bit_3 (
    .Input_0(and_2_out), .Input_1(Inputs[2]), .Output(mux_2_1_1_bit_3_output), .Select(load_inc_));
  Mux_2_1__1_bit mux_2_1_1_bit_4 (
    .Input_0(and_3_out), .Input_1(Inputs[3]), .Output(mux_2_1_1_bit_4_output), .Select(load_inc_));
  Mux_2_1__1_bit mux_2_1_1_bit_5 (
    .Input_0(and_4_out), .Input_1(Inputs[4]), .Output(mux_2_1_1_bit_5_output), .Select(load_inc_));
  Mux_2_1__1_bit mux_2_1_1_bit_6 (
    .Input_0(and_5_out), .Input_1(Inputs[5]), .Output(mux_2_1_1_bit_6_output), .Select(load_inc_));
  Mux_2_1__1_bit mux_2_1_1_bit_7 (
    .Input_0(and_6_out), .Input_1(Inputs[6]), .Output(mux_2_1_1_bit_7_output), .Select(load_inc_));
  Mux_2_1__1_bit mux_2_1_1_bit_8 (
    .Input_0(and_7_out), .Input_1(Inputs[7]), .Output(mux_2_1_1_bit_8_output), .Select(load_inc_));
  xor xor_1 (xor_1_out, load_inc_, mux_2_1_1_bit_1_output);
  xor xor_2 (xor_2_out, load_inc_, mux_2_1_1_bit_2_output);
  xor xor_3 (xor_3_out, load_inc_, mux_2_1_1_bit_3_output);
  xor xor_4 (xor_4_out, load_inc_, mux_2_1_1_bit_4_output);
  xor xor_5 (xor_5_out, load_inc_, mux_2_1_1_bit_5_output);
  xor xor_6 (xor_6_out, load_inc_, mux_2_1_1_bit_6_output);
  xor xor_7 (xor_7_out, load_inc_, mux_2_1_1_bit_7_output);
  xor xor_8 (xor_8_out, load_inc_, mux_2_1_1_bit_8_output);
  J_K_Flip_Flop j_k_ff_1 (
    .J(mux_2_1_1_bit_1_output), .clk(CLK), .K(xor_1_out), .Q(Outputs[0]), .reset(reset));  // open: Qn, preset, en
  and and_1 (and_1_out, Outputs[0], not_1_out);
  J_K_Flip_Flop j_k_ff_2 (
    .J(mux_2_1_1_bit_2_output), .clk(CLK), .K(xor_2_out), .Q(Outputs[1]), .reset(reset));  // open: Qn, preset, en
  and and_2 (and_2_out, Outputs[1], and_1_out);
  J_K_Flip_Flop j_k_ff_3 (
    .J(mux_2_1_1_bit_3_output), .clk(CLK), .K(xor_3_out), .Q(Outputs[2]), .reset(reset));  // open: Qn, preset, en
  and and_3 (and_3_out, Outputs[2], and_2_out);
  J_K_Flip_Flop j_k_ff_4 (
    .J(mux_2_1_1_bit_4_output), .clk(CLK), .K(xor_4_out), .Q(Outputs[3]), .reset(reset));  // open: Qn, preset, en
  and and_4 (and_4_out, Outputs[3], and_3_out);
  J_K_Flip_Flop j_k_ff_5 (
    .J(mux_2_1_1_bit_5_output), .clk(CLK), .K(xor_5_out), .Q(Outputs[4]), .reset(reset));  // open: Qn, preset, en
  and and_5 (and_5_out, Outputs[4], and_4_out);
  J_K_Flip_Flop j_k_ff_6 (
    .J(mux_2_1_1_bit_6_output), .clk(CLK), .K(xor_6_out), .Q(Outputs[5]), .reset(reset));  // open: Qn, preset, en
  and and_6 (and_6_out, Outputs[5], and_5_out);
  J_K_Flip_Flop j_k_ff_7 (
    .J(mux_2_1_1_bit_7_output), .clk(CLK), .K(xor_7_out), .Q(Outputs[6]), .reset(reset));  // open: Qn, preset, en
  and and_7 (and_7_out, Outputs[6], and_6_out);
  J_K_Flip_Flop j_k_ff_8 (
    .J(mux_2_1_1_bit_8_output), .clk(CLK), .K(xor_8_out), .Q(Outputs[7]), .reset(reset));  // open: Qn, preset, en
  and and_8 (Cout, Outputs[7], and_7_out);

  // Notes on the sheet:
  //   load_inc_: pull=up
endmodule

// CSR
module CSR__Control_Status_Register (
  input  clk,
  input  Write,
  input  [9:0] next_address_input,
  input  [31:0] signals_input,
  output SC1,
  output SC0,
  output SYNC,
  output R_W_,
  output PC_plus_plus,
  output OUTw,
  output ABw,
  output IRw,
  output PChw,
  output PClw,
  output SPw,
  output TMPw,
  output Yw,
  output Xw,
  output Accw,
  output F2,
  output F1,
  output F0,
  output CF2,
  output CF1,
  output CF0,
  output V2,
  output V1,
  output V0,
  output MU1,
  output MU0,
  output Mux2,
  output Mux1,
  output Mux0,
  output ALU3,
  output ALU2,
  output ALU1,
  output ALU0,
  output AD7,
  output AD6,
  output AD5,
  output AD4,
  output AD3,
  output AD2,
  output AD1,
  output AD0
);

  wire d_ff_42_q;

  D_Flip_Flop d_ff_1 (.clk(clk), .D(next_address_input[0]), .Q(AD0), .en(Write));  // open: Qn, preset, reset
  D_Flip_Flop d_ff_2 (.clk(clk), .D(next_address_input[1]), .Q(AD1), .en(Write));  // open: Qn, preset, reset
  D_Flip_Flop d_ff_3 (.clk(clk), .D(next_address_input[2]), .Q(AD2), .en(Write));  // open: Qn, preset, reset
  D_Flip_Flop d_ff_4 (.clk(clk), .D(next_address_input[3]), .Q(AD3), .en(Write));  // open: Qn, preset, reset
  D_Flip_Flop d_ff_5 (.clk(clk), .D(next_address_input[4]), .Q(AD4), .en(Write));  // open: Qn, preset, reset
  D_Flip_Flop d_ff_6 (.clk(clk), .D(next_address_input[5]), .Q(AD5), .en(Write));  // open: Qn, preset, reset
  D_Flip_Flop d_ff_7 (.clk(clk), .D(next_address_input[6]), .Q(AD6), .en(Write));  // open: Qn, preset, reset
  D_Flip_Flop d_ff_8 (.clk(clk), .D(next_address_input[7]), .Q(AD7), .en(Write));  // open: Qn, preset, reset
  D_Flip_Flop d_ff_9 (.clk(clk), .D(next_address_input[8]), .Q(SC0), .en(Write));  // open: Qn, preset, reset
  D_Flip_Flop d_ff_10 (.clk(clk), .D(next_address_input[9]), .Q(SC1), .en(Write));  // open: Qn, preset, reset
  D_Flip_Flop d_ff_11 (.clk(clk), .D(signals_input[0]), .Q(ALU0), .en(Write));  // open: Qn, preset, reset
  D_Flip_Flop d_ff_12 (.clk(clk), .D(signals_input[1]), .Q(ALU1), .en(Write));  // open: Qn, preset, reset
  D_Flip_Flop d_ff_13 (.clk(clk), .D(signals_input[2]), .Q(ALU2), .en(Write));  // open: Qn, preset, reset
  D_Flip_Flop d_ff_14 (.clk(clk), .D(signals_input[3]), .Q(ALU3), .en(Write));  // open: Qn, preset, reset
  D_Flip_Flop d_ff_15 (.clk(clk), .D(signals_input[4]), .Q(Mux0), .en(Write));  // open: Qn, preset, reset
  D_Flip_Flop d_ff_16 (.clk(clk), .D(signals_input[5]), .Q(Mux1), .en(Write));  // open: Qn, preset, reset
  D_Flip_Flop d_ff_17 (.clk(clk), .D(signals_input[6]), .Q(Mux2), .en(Write));  // open: Qn, preset, reset
  D_Flip_Flop d_ff_18 (.clk(clk), .D(signals_input[7]), .Q(MU0), .en(Write));  // open: Qn, preset, reset
  D_Flip_Flop d_ff_19 (.clk(clk), .D(signals_input[8]), .Q(MU1), .en(Write));  // open: Qn, preset, reset
  D_Flip_Flop d_ff_20 (.clk(clk), .D(signals_input[9]), .Q(V0), .en(Write));  // open: Qn, preset, reset
  D_Flip_Flop d_ff_21 (.clk(clk), .D(signals_input[10]), .Q(V1), .en(Write));  // open: Qn, preset, reset
  D_Flip_Flop d_ff_22 (.clk(clk), .D(signals_input[11]), .Q(V2), .en(Write));  // open: Qn, preset, reset
  D_Flip_Flop d_ff_23 (.clk(clk), .D(signals_input[12]), .Q(CF0), .en(Write));  // open: Qn, preset, reset
  D_Flip_Flop d_ff_24 (.clk(clk), .D(signals_input[13]), .Q(CF1), .en(Write));  // open: Qn, preset, reset
  D_Flip_Flop d_ff_25 (.clk(clk), .D(signals_input[14]), .Q(CF2), .en(Write));  // open: Qn, preset, reset
  D_Flip_Flop d_ff_26 (.clk(clk), .D(signals_input[15]), .Q(F0), .en(Write));  // open: Qn, preset, reset
  D_Flip_Flop d_ff_27 (.clk(clk), .D(signals_input[16]), .Q(F1), .en(Write));  // open: Qn, preset, reset
  D_Flip_Flop d_ff_28 (.clk(clk), .D(signals_input[17]), .Q(F2), .en(Write));  // open: Qn, preset, reset
  D_Flip_Flop d_ff_29 (.clk(clk), .D(signals_input[18]), .Q(Accw), .en(Write));  // open: Qn, preset, reset
  D_Flip_Flop d_ff_30 (.clk(clk), .D(signals_input[19]), .Q(Xw), .en(Write));  // open: Qn, preset, reset
  D_Flip_Flop d_ff_31 (.clk(clk), .D(signals_input[20]), .Q(Yw), .en(Write));  // open: Qn, preset, reset
  D_Flip_Flop d_ff_32 (.clk(clk), .D(signals_input[21]), .Q(TMPw), .en(Write));  // open: Qn, preset, reset
  D_Flip_Flop d_ff_33 (.clk(clk), .D(signals_input[22]), .Q(SPw), .en(Write));  // open: Qn, preset, reset
  D_Flip_Flop d_ff_34 (.clk(clk), .D(signals_input[23]), .Q(PClw), .en(Write));  // open: Qn, preset, reset
  D_Flip_Flop d_ff_35 (.clk(clk), .D(signals_input[24]), .Q(PChw), .en(Write));  // open: Qn, preset, reset
  D_Flip_Flop d_ff_36 (.clk(clk), .D(signals_input[25]), .Q(IRw), .en(Write));  // open: Qn, preset, reset
  D_Flip_Flop d_ff_37 (.clk(clk), .D(signals_input[26]), .Q(ABw), .en(Write));  // open: Qn, preset, reset
  D_Flip_Flop d_ff_38 (.clk(clk), .D(signals_input[27]), .Q(OUTw), .en(Write));  // open: Qn, preset, reset
  D_Flip_Flop d_ff_39 (.clk(clk), .D(signals_input[28]), .Q(PC_plus_plus), .en(Write));  // open: Qn, preset, reset
  D_Flip_Flop d_ff_40 (.clk(clk), .D(signals_input[29]), .Q(R_W_), .en(Write));  // open: Qn, preset, reset
  D_Flip_Flop d_ff_41 (.clk(clk), .D(signals_input[30]), .Q(SYNC), .en(Write));  // open: Qn, preset, reset
  D_Flip_Flop d_ff_42 (.clk(clk), .D(signals_input[31]), .Q(d_ff_42_q), .en(Write));  // open: Qn, preset, reset
endmodule

// BC
module BC__Branch_Controller (
  input  negative,
  input  overflow,
  input  carry,
  input  zero,
  input  [7:0] OpCode,
  input  branch,
  output branch_2
);

  wire and_1_out, and_2_out, and_3_out, and_4_out, and_5_out, and_6_out, and_7_out, and_8_out, and_9_out,
       and_10_out, nand_1_out, or_1_out;

  nand nand_1 (nand_1_out, OpCode[1], OpCode[0]);
  and and_1 (and_1_out, OpCode[4], ~OpCode[3], ~OpCode[2]);  // AND_Gate
  and and_2 (and_2_out, ~OpCode[7], ~OpCode[6], ~OpCode[5], ~negative);  // AND_Gate
  and and_3 (and_3_out, negative, ~OpCode[7], ~OpCode[6], OpCode[5]);  // AND_Gate
  and and_4 (and_4_out, ~OpCode[7], OpCode[6], ~OpCode[5], ~overflow);  // AND_Gate
  and and_5 (and_5_out, overflow, ~OpCode[7], OpCode[6], OpCode[5]);  // AND_Gate
  and and_6 (and_6_out, OpCode[7], ~OpCode[6], ~OpCode[5], ~carry);  // AND_Gate
  and and_7 (and_7_out, carry, OpCode[7], ~OpCode[6], OpCode[5]);  // AND_Gate
  and and_8 (and_8_out, OpCode[7], OpCode[6], ~OpCode[5], ~zero);  // AND_Gate
  and and_9 (and_9_out, zero, OpCode[7], OpCode[6], OpCode[5]);
  and and_10 (and_10_out, and_1_out, nand_1_out);
  or or_1 (or_1_out, and_2_out, and_3_out, and_4_out, and_5_out, and_6_out, and_7_out, and_8_out, and_9_out);
  and and_11 (branch_2, or_1_out, and_10_out, branch);

  // Notes on the sheet:
  //   AAA
  //   Notes :
  //   BBB
  //   CC
  //   - Brunch instructions follow this format : ---.100.00
  //   BPL : AAA=000 and N=0
  //   BMI : AAA=001 and N=1
  //   BVC : AAA=010 and V=0
  //   BVS : AAA=011 and V=1
  //   BCC : AAA=100 and Z=0
  //   BCS : AAA=101 and Z=1
  //   BNE : AAA=110 and N=0
  //   BEQ : AAA=111 and N=1
  //   Bruch instructions : BBB=100 and CC=00
  //   - OpCode binary format (8 bits) is represented AAA.BBB.CC (- means 0 or 1)
endmodule

// Mapper
module Operation_Mapper (
  input  [7:0] OpCode,
  output [7:0] operation_address
);

  wire and_1_out, and_2_out, and_3_out, and_4_out, and_5_out, and_6_out, and_7_out, and_8_out, and_9_out,
       and_10_out, and_11_out, and_12_out, and_13_out, and_14_out, and_15_out, demux_1_2_1_bit_1_output_0,
       demux_1_2_1_bit_1_output_1, demux_1_2_1_bit_2_output_0, demux_1_2_1_bit_2_output_1,
       demux_1_2_1_bit_3_output_0, demux_1_2_1_bit_3_output_1, demux_1_2_1_bit_4_output_0,
       demux_1_2_1_bit_4_output_1, or_1_out;
  wire [3:0] encoder_16_4_1_bits_1_output_0;
  wire [7:0] rom_1_data, rom_2_data;

  and and_1 (and_1_out, ~OpCode[7], ~OpCode[6], ~OpCode[5], OpCode[0]);  // AND_Gate
  and and_2 (and_2_out, ~OpCode[7], ~OpCode[6], OpCode[5], OpCode[0]);  // AND_Gate
  and and_3 (and_3_out, ~OpCode[7], OpCode[6], ~OpCode[5], OpCode[0]);  // AND_Gate
  and and_4 (and_4_out, ~OpCode[7], OpCode[6], OpCode[5], OpCode[0]);  // AND_Gate
  and and_5 (and_5_out, OpCode[7], ~OpCode[6], ~OpCode[5], OpCode[0]);  // AND_Gate
  and and_6 (and_6_out, OpCode[7], ~OpCode[6], OpCode[5], OpCode[0]);  // AND_Gate
  and and_7 (and_7_out, OpCode[7], OpCode[6], ~OpCode[5], OpCode[0]);  // AND_Gate
  and and_8 (and_8_out, OpCode[7], OpCode[6], OpCode[5], OpCode[0]);
  and and_9 (and_9_out, ~OpCode[4], OpCode[3], ~OpCode[2]);  // AND_Gate
  and and_10 (and_10_out, ~OpCode[7], ~OpCode[6], ~OpCode[5], OpCode[1], ~OpCode[0]);  // AND_Gate
  and and_11 (and_11_out, ~OpCode[7], ~OpCode[6], OpCode[5], OpCode[1], ~OpCode[0]);  // AND_Gate
  and and_12 (and_12_out, ~OpCode[7], OpCode[6], ~OpCode[5], OpCode[1], ~OpCode[0]);  // AND_Gate
  and and_13 (and_13_out, ~OpCode[7], OpCode[6], OpCode[5], OpCode[1], ~OpCode[0]);  // AND_Gate
  Demux_1_2__1_bit demux_1_2_1_bit_1 (
    .Input(and_10_out), .Output_0(demux_1_2_1_bit_1_output_0), .Output_1(demux_1_2_1_bit_1_output_1),
    .Select(and_9_out));
  Demux_1_2__1_bit demux_1_2_1_bit_2 (
    .Input(and_11_out), .Output_0(demux_1_2_1_bit_2_output_0), .Output_1(demux_1_2_1_bit_2_output_1),
    .Select(and_9_out));
  Demux_1_2__1_bit demux_1_2_1_bit_3 (
    .Input(and_12_out), .Output_0(demux_1_2_1_bit_3_output_0), .Output_1(demux_1_2_1_bit_3_output_1),
    .Select(and_9_out));
  Demux_1_2__1_bit demux_1_2_1_bit_4 (
    .Input(and_13_out), .Output_0(demux_1_2_1_bit_4_output_0), .Output_1(demux_1_2_1_bit_4_output_1),
    .Select(and_9_out));
  Encoder_16_4__1_bits encoder_16_4_1_bits_1 (
    .input_0(and_1_out), .input_1(and_2_out), .input_2(and_3_out), .input_3(and_4_out), .input_4(and_5_out),
    .input_5(and_6_out), .input_6(and_7_out), .input_7(and_8_out), .input_8(demux_1_2_1_bit_1_output_0),
    .input_9(demux_1_2_1_bit_1_output_1), .input_10(demux_1_2_1_bit_2_output_0),
    .input_11(demux_1_2_1_bit_2_output_1), .input_12(demux_1_2_1_bit_3_output_0),
    .input_13(demux_1_2_1_bit_3_output_1), .input_14(demux_1_2_1_bit_4_output_0),
    .input_15(demux_1_2_1_bit_4_output_1), .output_3(encoder_16_4_1_bits_1_output_0[3]),
    .output_2(encoder_16_4_1_bits_1_output_0[2]), .output_1(encoder_16_4_1_bits_1_output_0[1]),
    .output_0(encoder_16_4_1_bits_1_output_0[0]));  // open: active
  and and_14 (and_14_out, OpCode[0], ~OpCode[1]);  // AND_Gate
  or or_1 (or_1_out, and_14_out, and_15_out);
  and and_15 (and_15_out, ~OpCode[0], OpCode[1], ~OpCode[7]);  // AND_Gate
  ROM #(.addrWidth(7)) rom_1 (.addr(OpCode[7:1]), .data(rom_1_data));  // open: sel
  ROM #(.addrWidth(4)) rom_2 (.addr(encoder_16_4_1_bits_1_output_0), .data(rom_2_data));  // open: sel
  Mux_2_1__8_bits mux_2_1_8_bits_1 (
    .Input_0(rom_1_data), .Input_1(rom_2_data), .Output(operation_address), .Select(or_1_out));

  // Notes on the sheet:
  //   BBB
  //   AAA
  //   BBB
  //   AAA
  //   CC
  //   CC
  //   ORA
  //   AND
  //   EOR
  //   ADC
  //   STA
  //   LDA
  //   CMP
  //   SBC
  //   (B=2) => Acc
  //   ASL
  //   ROL
  //   LSR
  //   ROR
  //   Mem
  //   Acc
  //   Mem
  //   Acc
  //   Mem
  //   Acc
  //   Mem
  //   Acc
  //   AAA
  //   BBB
  //   CC
  //   Notes :
  //   opc = ---.---.-0
  //   Instructions Operation
  //   Address Table (grp0)
  //   Instructions Operation
  //   Address Table (grp1)
  //   ---.---.01 or 0--.---.10
  //   contents of rom_1 (hex, n*v repeats v):
  //   e 0 0 0 9d 7*0 96 0 0 0 a1 0 9f 0 98 0 9f 5*0 97 0 0 0 b1 0 0 0 9b 0 8f 5*0 94 0 0 0 aa 0 0 0 89 0
  //   8c 5*0 95 5*0 85 69 87 6b 85 69 0 0 85 69 88 6c 0 0 82 6d 82 6d 83 6e 82 6d 0 0 82 6d 84 6f 82 6d 7c
  //   0 7c 70 80 72 7c 70 0 0 0 70 81 0 0 70 76 0 76 73 7a 75 76 73 0 0 0 73 7b 0 0 73
  //   contents of rom_2 (hex, n*v repeats v):
  //   50 51 52 53 54 56 57 58 59 5b 5d 5f 61 63 65 67
  //   - Separating instructions in 2 groups helps optimization.
  //   instructions with 8 addressing modes :
  //   - OpCode binary format (8 bits) is represented AAA.BBB.CC (- means 0 or 1)
  //   - The instructions ORA, AND, EOR, ADC, STA, LDA CMP, SBC, ASL, ROL,
  //    LSR, ROR are special, they use 8 different addressing modes.
  //   - Instructions with 8 different addressing modes are like : AAA.---.CC
  //   Choose between instructions with 8
  //    addressing modes and others with less
  //   Notes :
  //   - JMP indirect (100.011.00) is included within absolute mode
  //   - OpCode binary format (8 bits) is represented AAA.BBB.CC (- means 0 or 1)
  //   - Accumulator addressing mode (0--.010.10) is included within implied mode
  //   - special instructions (BRK,JSR,RTI,RTS) are traited after as implied instructions
endmodule

// Mapper
module Address_Mode_Mapper (
  input  [7:0] OpCode,
  output [7:0] Control_Address
);

  wire and_1_out, and_2_out, and_3_out, and_4_out, and_5_out, and_6_out, and_7_out, and_8_out, and_9_out,
       and_10_out, and_11_out, and_12_out, and_13_out, and_14_out, and_15_out, and_16_out, and_17_out,
       and_18_out, or_1_out, or_2_out, or_3_out;
  wire [3:0] encoder_16_4_1_bits_1_output_0;

  and and_1 (and_1_out, OpCode[3], ~OpCode[2], ~OpCode[0]);  // AND_Gate
  and and_2 (and_2_out, OpCode[7], ~OpCode[4], ~OpCode[3], ~OpCode[2], ~OpCode[0]);  // AND_Gate
  and and_3 (and_3_out, ~OpCode[4], OpCode[3], ~OpCode[2], OpCode[0]);  // AND_Gate
  and and_4 (and_4_out, ~OpCode[4], ~OpCode[3], OpCode[2]);  // AND_Gate
  and and_5 (and_5_out, OpCode[4], ~OpCode[3], OpCode[2]);  // AND_Gate
  and and_6 (and_6_out, OpCode[7], ~OpCode[6], OpCode[4], ~OpCode[3], OpCode[2], OpCode[1]);  // AND_Gate
  and and_7 (and_7_out, ~OpCode[4], ~OpCode[3], ~OpCode[2], OpCode[0]);  // AND_Gate
  and and_8 (and_8_out, OpCode[4], ~OpCode[3], ~OpCode[2], OpCode[0]);  // AND_Gate
  and and_9 (and_9_out, OpCode[4], ~OpCode[3], ~OpCode[2], ~OpCode[0]);  // AND_Gate
  and and_10 (and_10_out, ~OpCode[4], OpCode[3], OpCode[2]);  // AND_Gate
  and and_11 (and_11_out, OpCode[4], OpCode[3], OpCode[2]);
  and and_12 (and_12_out, OpCode[7], ~OpCode[6], OpCode[4], OpCode[3], OpCode[2], OpCode[1]);  // AND_Gate
  and and_13 (and_13_out, OpCode[4], OpCode[3], ~OpCode[2], OpCode[0]);  // AND_Gate
  and and_14 (and_14_out, ~OpCode[7], ~OpCode[4], ~OpCode[3], ~OpCode[2], ~OpCode[0]);  // AND_Gate
  and and_15 (and_15_out, ~OpCode[7], OpCode[6], ~OpCode[5], ~OpCode[4], OpCode[3], OpCode[2], ~OpCode[1], ~OpCode[0]);  // AND_Gate
  or or_1 (or_1_out, and_2_out, and_3_out);
  and and_16 (and_16_out, and_5_out, ~and_6_out);  // AND_Gate
  and and_17 (and_17_out, and_10_out, ~and_15_out);  // AND_Gate
  and and_18 (and_18_out, and_11_out, ~and_12_out);  // AND_Gate
  or or_2 (or_2_out, and_12_out, and_13_out);
  or or_3 (or_3_out, and_14_out, and_15_out);
  Encoder_16_4__1_bits encoder_16_4_1_bits_1 (
    .input_0(and_1_out), .input_1(or_1_out), .input_2(and_4_out), .input_3(and_16_out), .input_4(and_6_out),
    .input_5(and_7_out), .input_6(and_8_out), .input_7(and_9_out), .input_8(and_17_out),
    .input_9(and_18_out), .input_10(or_2_out), .input_11(or_3_out), .input_12(1'b0), .input_13(1'b0),
    .input_14(1'b0), .input_15(1'b0), .output_3(encoder_16_4_1_bits_1_output_0[3]),
    .output_2(encoder_16_4_1_bits_1_output_0[2]), .output_1(encoder_16_4_1_bits_1_output_0[1]),
    .output_0(encoder_16_4_1_bits_1_output_0[0]));  // open: active
  ROM #(.addrWidth(4)) rom_1 (.addr(encoder_16_4_1_bits_1_output_0), .data(Control_Address));  // open: sel

  // Notes on the sheet:
  //   BBB
  //   AAA
  //   BBB
  //   AAA
  //   CC
  //   CC
  //   Notes :
  //   zero page,X : ---.101.-- 
  //   implied : ---.-10.-0
  //   zero page : ---.001.--
  //   X,indirect : ---.000.-1
  //   indirect,Y : ---.100.-1
  //   relative : ---.100.-0
  //   absolute : ---.011.--
  //   absolute,X : ---.111.--
  //   LDX abs,Y : 10-.111.1-
  //   absolute,Y : ---.110.-1
  //   JMP abs : 010.011.00
  //   - JMP indirect (100.011.00) is included within absolute mode
  //   immediate : 1--.000.-0 or ---.010.-1
  //   - JMP abs is distinct from others, thus it is treated like special instruction
  //   zero page,Y : 10-.101.1- (STX zpg,Y and LDX zpg,Y)
  //   special instructions : 0--.000.-0 (BRK,JSR,RTI,RTS)
  //   - OpCode binary format (8 bits) is represented AAA.BBB.CC (- means 0 or 1)
  //   - Accumulator addressing mode (0--.010.10) is included within implied mode
  //   - special instructions (BRK,JSR,RTI,RTS) are traited later as implied instructions
  //   excluding STX zpg,Y and LDX zpg,Y
  //   excluding JMP abs
  //   excluding LDX abs,Y
  //   Addressing Mode
  //   Address Table
  //   contents of rom_1 (hex, n*v repeats v):
  //   14 15 16 19 1d 38 40 21 25 2a 31 14
endmodule

// Adder
module Adder__8_bits (
  input  Cin,
  input  [7:0] A,
  input  [7:0] B,
  output [7:0] S,
  output overflow,
  output Cout
);

  wire full_adder_1_cout, full_adder_2_cout, full_adder_3_cout, full_adder_4_cout, full_adder_5_cout,
       full_adder_6_cout, full_adder_7_cout;

  Full_Adder full_adder_1 (.A(A[0]), .B(B[0]), .S(S[0]), .Cin(Cin), .Cout(full_adder_1_cout));
  Full_Adder full_adder_2 (.A(A[1]), .B(B[1]), .S(S[1]), .Cin(full_adder_1_cout), .Cout(full_adder_2_cout));
  Full_Adder full_adder_3 (.A(A[2]), .B(B[2]), .S(S[2]), .Cin(full_adder_2_cout), .Cout(full_adder_3_cout));
  Full_Adder full_adder_4 (.A(A[3]), .B(B[3]), .S(S[3]), .Cin(full_adder_3_cout), .Cout(full_adder_4_cout));
  Full_Adder full_adder_5 (.A(A[4]), .B(B[4]), .S(S[4]), .Cin(full_adder_4_cout), .Cout(full_adder_5_cout));
  Full_Adder full_adder_6 (.A(A[5]), .B(B[5]), .S(S[5]), .Cin(full_adder_5_cout), .Cout(full_adder_6_cout));
  Full_Adder full_adder_7 (.A(A[6]), .B(B[6]), .S(S[6]), .Cin(full_adder_6_cout), .Cout(full_adder_7_cout));
  Full_Adder full_adder_8 (.A(A[7]), .B(B[7]), .S(S[7]), .Cin(full_adder_7_cout), .Cout(Cout));
  xor xor_1 (overflow, full_adder_7_cout, Cout);
endmodule

module Full_Adder (
  input  Cin,
  input  A,
  input  B,
  output S,
  output Cout
);

  wire and_1_out, and_2_out, and_3_out;

  xor xor_1 (S, A, B, Cin);
  and and_1 (and_1_out, A, B);
  and and_2 (and_2_out, A, Cin);
  and and_3 (and_3_out, B, Cin);
  or or_1 (Cout, and_1_out, and_2_out, and_3_out);
endmodule

// >>
module Shift_1_bit_right__8_bits (
  input  [7:0] Input,
  input  Cin,
  output Cout,
  output [7:0] Output
);


  assign Cout = Input[0];
  assign Output = {Cin, Input[7:1]};
endmodule

// Shifter
module Serial_to_Parallel_Shifter__8_bits (
  input  clk,
  input  reset,
  input  Input,
  output Output_0,
  output Output_1,
  output Output_2,
  output Output_3,
  output Output_4,
  output Output_5,
  output Output_6,
  output Output_7
);

  D_Flip_Flop d_ff_1 (.clk(clk), .D(Input), .Q(Output_0), .reset(reset));  // open: Qn, preset, en
  D_Flip_Flop d_ff_2 (.clk(clk), .D(Output_0), .Q(Output_1), .reset(reset));  // open: Qn, preset, en
  D_Flip_Flop d_ff_3 (.clk(clk), .D(Output_1), .Q(Output_2), .reset(reset));  // open: Qn, preset, en
  D_Flip_Flop d_ff_4 (.clk(clk), .D(Output_2), .Q(Output_3), .reset(reset));  // open: Qn, preset, en
  D_Flip_Flop d_ff_5 (.clk(clk), .D(Output_3), .Q(Output_4), .reset(reset));  // open: Qn, preset, en
  D_Flip_Flop d_ff_6 (.clk(clk), .D(Output_4), .Q(Output_5), .reset(reset));  // open: Qn, preset, en
  D_Flip_Flop d_ff_7 (.clk(clk), .D(Output_5), .Q(Output_6), .reset(reset));  // open: Qn, preset, en
  D_Flip_Flop d_ff_8 (.clk(clk), .D(Output_6), .Q(Output_7), .reset(reset));  // open: Qn, preset, en
endmodule

// Mux 2-1
module Mux_2_1__1_bit (
  input  Select,
  input  Input_0,
  input  Input_1,
  output Output
);

  wire and_1_out, and_2_out, not_1_out;

  not not_1 (not_1_out, Select);
  and and_1 (and_1_out, not_1_out, Input_0);
  and and_2 (and_2_out, Select, Input_1);
  or or_1 (Output, and_1_out, and_2_out);
endmodule

// Mux 2-1
module Mux_2_1__8_bits (
  input  Select,
  input  [7:0] Input_0,
  input  [7:0] Input_1,
  output [7:0] Output
);

  wire [7:0] and_1_out, and_2_out;
  wire [7:7] not_1_out;

  not not_1 (not_1_out[7], Select);
  assign and_1_out = {8{not_1_out[7]}} & Input_0;  // AND_Gate and_1, 8 bits wide
  assign and_2_out = {8{Select}} & Input_1;  // AND_Gate and_2, 8 bits wide
  assign Output = and_1_out | and_2_out;  // OR_Gate or_1, 8 bits wide
endmodule

// Mux 4-1
module Mux_4_1__1_bit (
  input  Select_0,
  input  Select_1,
  input  Input_0,
  input  Input_1,
  input  Input_2,
  input  Input_3,
  output Output
);

  wire mux_2_1_1_bit_1_output, mux_2_1_1_bit_2_output;

  Mux_2_1__1_bit mux_2_1_1_bit_1 (
    .Input_0(Input_0), .Input_1(Input_1), .Output(mux_2_1_1_bit_1_output), .Select(Select_0));
  Mux_2_1__1_bit mux_2_1_1_bit_2 (
    .Input_0(Input_2), .Input_1(Input_3), .Output(mux_2_1_1_bit_2_output), .Select(Select_0));
  Mux_2_1__1_bit mux_2_1_1_bit_3 (
    .Input_0(mux_2_1_1_bit_1_output), .Input_1(mux_2_1_1_bit_2_output), .Output(Output), .Select(Select_1));
endmodule

// Mux 4-1
module Mux_4_1__8_bits (
  input  Select_0,
  input  Select_1,
  input  [7:0] Input_0,
  input  [7:0] Input_1,
  input  [7:0] Input_2,
  input  [7:0] Input_3,
  output [7:0] Output
);

  wire [7:0] mux_2_1_8_bits_1_output, mux_2_1_8_bits_2_output;

  Mux_2_1__8_bits mux_2_1_8_bits_1 (
    .Input_0(Input_0), .Input_1(Input_1), .Output(mux_2_1_8_bits_1_output), .Select(Select_0));
  Mux_2_1__8_bits mux_2_1_8_bits_2 (
    .Input_0(Input_2), .Input_1(Input_3), .Output(mux_2_1_8_bits_2_output), .Select(Select_0));
  Mux_2_1__8_bits mux_2_1_8_bits_3 (
    .Input_0(mux_2_1_8_bits_1_output), .Input_1(mux_2_1_8_bits_2_output), .Output(Output), .Select(Select_1));
endmodule

// Mux 8-1
module Mux_8_1__1_bit (
  input  Select_0,
  input  Select_1,
  input  Select_2,
  input  Input_0,
  input  Input_1,
  input  Input_2,
  input  Input_3,
  input  Input_4,
  input  Input_5,
  input  Input_6,
  input  Input_7,
  output Output
);

  wire mux_2_1_1_bit_1_output, mux_2_1_1_bit_2_output, mux_2_1_1_bit_3_output, mux_2_1_1_bit_4_output,
       mux_2_1_1_bit_5_output, mux_2_1_1_bit_6_output;

  Mux_2_1__1_bit mux_2_1_1_bit_1 (
    .Input_0(Input_0), .Input_1(Input_1), .Output(mux_2_1_1_bit_1_output), .Select(Select_0));
  Mux_2_1__1_bit mux_2_1_1_bit_2 (
    .Input_0(Input_2), .Input_1(Input_3), .Output(mux_2_1_1_bit_2_output), .Select(Select_0));
  Mux_2_1__1_bit mux_2_1_1_bit_3 (
    .Input_0(Input_4), .Input_1(Input_5), .Output(mux_2_1_1_bit_3_output), .Select(Select_0));
  Mux_2_1__1_bit mux_2_1_1_bit_4 (
    .Input_0(Input_6), .Input_1(Input_7), .Output(mux_2_1_1_bit_4_output), .Select(Select_0));
  Mux_2_1__1_bit mux_2_1_1_bit_5 (
    .Input_0(mux_2_1_1_bit_1_output), .Input_1(mux_2_1_1_bit_2_output), .Output(mux_2_1_1_bit_5_output),
    .Select(Select_1));
  Mux_2_1__1_bit mux_2_1_1_bit_6 (
    .Input_0(mux_2_1_1_bit_3_output), .Input_1(mux_2_1_1_bit_4_output), .Output(mux_2_1_1_bit_6_output),
    .Select(Select_1));
  Mux_2_1__1_bit mux_2_1_1_bit_7 (
    .Input_0(mux_2_1_1_bit_5_output), .Input_1(mux_2_1_1_bit_6_output), .Output(Output), .Select(Select_2));
endmodule
// Mux 8-1
module Mux_8_1__8_bits (
  input  Select_0,
  input  Select_1,
  input  Select_2,
  input  [7:0] Input_0,
  input  [7:0] Input_1,
  input  [7:0] Input_2,
  input  [7:0] Input_3,
  input  [7:0] Input_4,
  input  [7:0] Input_5,
  input  [7:0] Input_6,
  input  [7:0] Input_7,
  output [7:0] Output
);

  wire [7:0] mux_2_1_8_bits_1_output, mux_2_1_8_bits_2_output, mux_2_1_8_bits_3_output,
       mux_2_1_8_bits_4_output, mux_2_1_8_bits_5_output, mux_2_1_8_bits_6_output;

  Mux_2_1__8_bits mux_2_1_8_bits_1 (
    .Input_0(Input_0), .Input_1(Input_1), .Output(mux_2_1_8_bits_1_output), .Select(Select_0));
  Mux_2_1__8_bits mux_2_1_8_bits_2 (
    .Input_0(Input_2), .Input_1(Input_3), .Output(mux_2_1_8_bits_2_output), .Select(Select_0));
  Mux_2_1__8_bits mux_2_1_8_bits_3 (
    .Input_0(Input_4), .Input_1(Input_5), .Output(mux_2_1_8_bits_3_output), .Select(Select_0));
  Mux_2_1__8_bits mux_2_1_8_bits_4 (
    .Input_0(Input_6), .Input_1(Input_7), .Output(mux_2_1_8_bits_4_output), .Select(Select_0));
  Mux_2_1__8_bits mux_2_1_8_bits_5 (
    .Input_0(mux_2_1_8_bits_1_output), .Input_1(mux_2_1_8_bits_2_output), .Output(mux_2_1_8_bits_5_output),
    .Select(Select_1));
  Mux_2_1__8_bits mux_2_1_8_bits_6 (
    .Input_0(mux_2_1_8_bits_3_output), .Input_1(mux_2_1_8_bits_4_output), .Output(mux_2_1_8_bits_6_output),
    .Select(Select_1));
  Mux_2_1__8_bits mux_2_1_8_bits_7 (
    .Input_0(mux_2_1_8_bits_5_output), .Input_1(mux_2_1_8_bits_6_output), .Output(Output), .Select(Select_2));
endmodule

// Demux
module Demux_1_2__1_bit (
  input  Select,
  input  Input,
  output Output_0,
  output Output_1
);

  wire not_1_out;

  not not_1 (not_1_out, Select);
  and and_1 (Output_0, not_1_out, Input);
  and and_2 (Output_1, Select, Input);
endmodule

// Decoder 3-8
module Decoder_3_8__1_bit (
  input  Input_2,
  input  Input_1,
  input  Input_0,
  output output_0,
  output output_1,
  output output_2,
  output output_3,
  output output_4,
  output output_5,
  output output_6,
  output output_7
);

  wire not_1_out, not_2_out, not_3_out;

  not not_1 (not_1_out, Input_2);
  not not_2 (not_2_out, Input_1);
  not not_3 (not_3_out, Input_0);
  and and_1 (output_0, not_3_out, not_2_out, not_1_out);
  and and_2 (output_1, Input_0, not_2_out, not_1_out);
  and and_3 (output_2, not_3_out, Input_1, not_1_out);
  and and_4 (output_3, Input_0, Input_1, not_1_out);
  and and_5 (output_4, not_3_out, not_2_out, Input_2);
  and and_6 (output_5, Input_0, not_2_out, Input_2);
  and and_7 (output_6, not_3_out, Input_1, Input_2);
  and and_8 (output_7, Input_0, Input_1, Input_2);
endmodule

// Encoder 4-2
module Encoder_4_2__1_bit (
  input  input_0,
  input  input_1,
  input  input_2,
  input  input_3,
  output output_1,
  output output_0,
  output active
);

  wire or_2_out, or_3_out;

  or or_1 (active, input_0, input_1, input_2, input_3);
  or or_2 (or_2_out, input_2, input_3);
  or or_3 (or_3_out, input_1, input_3);
  assign output_1 = active ? or_2_out : 1'bz;  // Controlled_Buffer controlled_buffer_1
  assign output_0 = active ? or_3_out : 1'bz;  // Controlled_Buffer controlled_buffer_2
endmodule

// Encoder 16-4
module Encoder_16_4__1_bits (
  input  input_0,
  input  input_1,
  input  input_2,
  input  input_3,
  input  input_4,
  input  input_5,
  input  input_6,
  input  input_7,
  input  input_8,
  input  input_9,
  input  input_10,
  input  input_11,
  input  input_12,
  input  input_13,
  input  input_14,
  input  input_15,
  output output_3,
  output output_2,
  output output_1,
  output output_0,
  output active
);

  wire encoder_4_2_1_bit_1_active, encoder_4_2_1_bit_1_output_0, encoder_4_2_1_bit_1_output_1,
       encoder_4_2_1_bit_2_active, encoder_4_2_1_bit_3_active, encoder_4_2_1_bit_4_active,
       encoder_4_2_1_bit_5_output_0, encoder_4_2_1_bit_5_output_1;

  Encoder_4_2__1_bit encoder_4_2_1_bit_1 (
    .input_0(input_4), .input_1(input_5), .input_2(input_6), .input_3(input_7),
    .output_1(encoder_4_2_1_bit_1_output_1), .output_0(encoder_4_2_1_bit_1_output_0),
    .active(encoder_4_2_1_bit_1_active));
  Encoder_4_2__1_bit encoder_4_2_1_bit_2 (
    .input_0(input_8), .input_1(input_9), .input_2(input_10), .input_3(input_11),
    .output_1(encoder_4_2_1_bit_1_output_1), .output_0(encoder_4_2_1_bit_1_output_0),
    .active(encoder_4_2_1_bit_2_active));
  Encoder_4_2__1_bit encoder_4_2_1_bit_3 (
    .input_0(input_12), .input_1(input_13), .input_2(input_14), .input_3(input_15),
    .output_1(encoder_4_2_1_bit_1_output_1), .output_0(encoder_4_2_1_bit_1_output_0),
    .active(encoder_4_2_1_bit_3_active));
  or or_1 (active, encoder_4_2_1_bit_3_active, encoder_4_2_1_bit_2_active, encoder_4_2_1_bit_1_active, encoder_4_2_1_bit_4_active);
  Encoder_4_2__1_bit encoder_4_2_1_bit_4 (
    .input_0(input_0), .input_1(input_1), .input_2(input_2), .input_3(input_3),
    .output_1(encoder_4_2_1_bit_1_output_1), .output_0(encoder_4_2_1_bit_1_output_0),
    .active(encoder_4_2_1_bit_4_active));
  Encoder_4_2__1_bit encoder_4_2_1_bit_5 (
    .input_0(encoder_4_2_1_bit_4_active), .input_1(encoder_4_2_1_bit_1_active),
    .input_2(encoder_4_2_1_bit_2_active), .input_3(encoder_4_2_1_bit_3_active),
    .output_1(encoder_4_2_1_bit_5_output_1), .output_0(encoder_4_2_1_bit_5_output_0));  // open: active
  assign output_3 = active ? encoder_4_2_1_bit_5_output_1 : 1'bz;  // Controlled_Buffer controlled_buffer_1
  assign output_2 = active ? encoder_4_2_1_bit_5_output_0 : 1'bz;  // Controlled_Buffer controlled_buffer_2
  assign output_1 = active ? encoder_4_2_1_bit_1_output_1 : 1'bz;  // Controlled_Buffer controlled_buffer_3
  assign output_0 = active ? encoder_4_2_1_bit_1_output_0 : 1'bz;  // Controlled_Buffer controlled_buffer_4
endmodule

module Rising_Eadge_Detector (
  input  clk,
  input  \input ,
  output \output 
);

  wire and_1_out, d_ff_1_q;

  and and_1 (and_1_out, \input , ~d_ff_1_q);  // AND_Gate
  D_Flip_Flop d_ff_1 (.clk(clk), .D(\input ), .Q(d_ff_1_q));  // open: Qn, preset, en, reset
  D_Flip_Flop d_ff_2 (.clk(clk), .D(and_1_out), .Q(\output ));  // open: Qn, preset, en, reset
endmodule
